// Logisim project 6502_Emulation.circ as structural Verilog: 17 circuits, main circuit main
module main (
  input  Power,
  input  TriggerManualInterupt,
  input  TriggerReturnFromInterupt,
  output InteruptState
);

  wire and_1_out, and_2_out, and_10_out, and_11_out, AWrite, Break, Carry, Clear, ClearBreak, ClearCarry,
       ClearDecimal, ClearInterupt, ClearOverflow, Clock, clock_1_out, clock_2_c1, clock_2_c2, clock_2_c3,
       controlled_buffer_8_out, controlled_buffer_11_out, CRead, d_ff_3_q, d_ff_4_q, d_ff_5_q, d_ff_9_q,
       Decode, DecodeFlag, DecodeHigh, Execute, execute_1_stackoverwrite, ExecuteDone, ExecuteFlag,
       ExecuteOff, Fetch, FetchFlag, FetchTrigger, HighFlag, InitialExecuteFlag, InstDone, Itterate,
       KeepPCOFF, MRead, MWrite, Negative, not_1_out, not_3_out, not_4_out, not_5_out, not_6_out, not_7_out,
       not_8_out, not_9_out, not_10_out, or_2_out, or_3_out, or_4_out, or_5_out, or_7_out, or_8_out, ORead,
       Overflow, PCOFF, PCWrite, PWrite, retreive_1_pcoffflag, SetCarry, SetDecimal, SetInterupt, Stack,
       StackOverwrite, Start, SWrite, TempOverwrtie, XWrite, YWrite, Zero, ZNRead;
  wire [6:0] POut;
  wire [7:0] controlled_buffer_1_out, controlled_buffer_2_out, controlled_buffer_4_out,
       controlled_buffer_5_out, controlled_buffer_6_out, controlled_buffer_17_out, InstOut, LowByte,
       ram_1_data, register_1_q, register_3_q, register_8_q, Sout;
  wire [11:0] AddMode;
  wire [15:0] controlled_buffer_9_out, controlled_buffer_12_out, controlled_buffer_14_out, PCALTOUT,
       PCInstOut, PCOUT, TempPCOveride;
  wire [16:0] InstructionSet2, InstructionSet3;
  wire [19:0] InstructionSet1;
  wire [23:0] RegOut;

  Clock_part clock_1 (.out(clock_1_out));
  and and_1 (and_1_out, clock_1_out, and_2_out);
  Clock clock_2 (
    .ClockIn(and_1_out), .Clock(Clock), .C3(clock_2_c3), .C2(clock_2_c2), .C1(clock_2_c1), .C0(TempOverwrtie));
  and and_2 (and_2_out, Power, not_1_out);
  not not_1 (not_1_out, InteruptState);
  D_Flip_Flop d_ff_1 (.D(Power), .clk(Power), .Q(Start), .reset(clock_2_c1));  // open: Qn, preset
  and and_3 (InteruptState, POut[2], ExecuteDone);
  or or_1 (FetchFlag, FetchTrigger, Start);
  not not_2 (Clear, Power);
  and and_4 (Execute, ExecuteFlag, clock_2_c3);
  and and_5 (DecodeHigh, HighFlag, clock_2_c2);
  and and_6 (Decode, clock_2_c1, DecodeFlag);
  and and_7 (Fetch, TempOverwrtie, FetchFlag);
  Decoder decoder_1 (
    .Input(register_1_q), .ORA(InstructionSet1[19]), .AND(InstructionSet1[18]), .EOR(InstructionSet1[17]),
    .ADC(InstructionSet1[16]), .STA(InstructionSet1[15]), .LDY(InstructionSet1[14]),
    .CPY(InstructionSet1[13]), .CPX(InstructionSet1[12]), .ASL(InstructionSet1[11]),
    .ROL(InstructionSet1[10]), .LSR(InstructionSet1[9]), .ROR(InstructionSet1[8]), .STY(InstructionSet1[7]),
    .LDA(InstructionSet1[6]), .CMP(InstructionSet1[5]), .SBC(InstructionSet1[4]), .STX(InstructionSet1[3]),
    .LDX(InstructionSet1[2]), .DEC(InstructionSet1[1]), .INC(InstructionSet1[0]), .rel(AddMode[11]),
    .hash(AddMode[10]), .Xind(AddMode[9]), .indY(AddMode[8]), .zpg(AddMode[7]), .zpgX(AddMode[6]),
    .zpgY(AddMode[5]), .absY(AddMode[4]), .A(AddMode[3]), .ind(AddMode[2]), .abs(AddMode[1]),
    .absX(AddMode[0]), .BRK(InstructionSet2[0]), .PHP(InstructionSet2[1]), .CLC(InstructionSet2[2]),
    .BPL(InstructionSet2[3]), .JSR(InstructionSet2[4]), .PLP(InstructionSet2[5]), .SEC(InstructionSet2[6]),
    .BMI(InstructionSet2[7]), .RTI(InstructionSet2[8]), .PHA(InstructionSet2[9]), .CLI(InstructionSet2[10]),
    .JMP(InstructionSet2[11]), .BVC(InstructionSet2[12]), .RTS(InstructionSet2[13]),
    .PLA(InstructionSet2[14]), .SEI(InstructionSet2[15]), .BVS(InstructionSet2[16]),
    .DEY(InstructionSet3[0]), .TXA(InstructionSet3[1]), .TYA(InstructionSet3[2]), .TXS(InstructionSet3[3]),
    .BCC(InstructionSet3[4]), .TAY(InstructionSet3[5]), .TAX(InstructionSet3[6]), .CLV(InstructionSet3[7]),
    .TSX(InstructionSet3[8]), .BCS(InstructionSet3[9]), .INY(InstructionSet3[10]), .DEX(InstructionSet3[11]),
    .CLD(InstructionSet3[12]), .BNE(InstructionSet3[13]), .INX(InstructionSet3[14]),
    .SED(InstructionSet3[15]), .BEQ(InstructionSet3[16]));
  not not_3 (not_3_out, ExecuteOff);
  D_Flip_Flop d_ff_2 (.D(Clock), .clk(Clock), .Q(ExecuteDone), .reset(or_3_out));  // open: Qn, preset
  not not_4 (not_4_out, ClearBreak);
  and and_8 (Itterate, not_4_out, or_2_out);
  or or_2 (or_2_out, DecodeHigh, Decode, Fetch);
  and and_9 (ExecuteFlag, InitialExecuteFlag, not_3_out);
  or or_3 (or_3_out, Execute, Clear);
  D_Flip_Flop d_ff_3 (
    .D(TriggerManualInterupt), .clk(TriggerManualInterupt), .Q(d_ff_3_q), .reset(InteruptState));  // open: Qn, preset
  ProcessorStatusRegister processorstatusregister_1 (
    .Pin(InstOut[7:1]), .RegsiterInput(PWrite), .Execute(Execute), .Clear(Clear), .Carry_2(POut[6]),
    .Zero_2(POut[5]), .Interupt(POut[4]), .Decimal(POut[3]), .Break(POut[2]), .Overflow_2(POut[1]),
    .Negative_2(POut[0]), .Carry(Carry), .CarryOn(SetCarry), .CarryRead(CRead), .CarryOff(ClearCarry),
    .Zero(Zero), .ZeroRead(ZNRead), .InteruptOn(SetInterupt), .InteruptOff(ClearInterupt),
    .DecimalOn(SetDecimal), .DecimalOff(ClearDecimal), .BreakOn(Break), .BreakOff(ClearBreak),
    .Overflow(Overflow), .OverflowRead(ORead), .ClearOverflow(ClearOverflow), .Negative(Negative),
    .NegativeRead(ZNRead));
  D_Flip_Flop d_ff_4 (.D(ExecuteDone), .clk(Clock), .Q(d_ff_4_q), .reset(or_3_out));  // open: Qn, preset
  or or_4 (or_4_out, d_ff_5_q, Clear);
  not not_5 (not_5_out, d_ff_3_q);
  assign controlled_buffer_1_out = Fetch ? controlled_buffer_6_out : 8'bz;  // Controlled_Buffer controlled_buffer_1
  assign controlled_buffer_2_out = not_5_out ? controlled_buffer_1_out : 8'bz;  // Controlled_Buffer controlled_buffer_2
  Register #(.trigger("falling")) register_1 (
    .D(controlled_buffer_2_out), .en(Fetch), .clk(Clock), .Q(register_1_q), .clr(Clear));
  D_Flip_Flop d_ff_5 (.D(d_ff_4_q), .clk(Clock), .Q(d_ff_5_q), .reset(or_3_out));  // open: Qn, preset
  D_Flip_Flop #(.trigger("falling")) d_ff_6 (
    .D(InstDone), .clk(Execute), .Q(ExecuteOff), .reset(or_4_out));  // open: Qn, preset
  assign controlled_buffer_2_out = d_ff_3_q ? {8{1'b0}} : 8'bz;  // Controlled_Buffer controlled_buffer_3
  Register #(.trigger("falling")) register_2 (
    .D(controlled_buffer_4_out), .en(Decode), .clk(Clock), .Q(LowByte), .clr(Clear));
  assign controlled_buffer_4_out = Decode ? controlled_buffer_6_out : 8'bz;  // Controlled_Buffer controlled_buffer_4
  D_Flip_Flop #(.trigger("falling")) d_ff_7 (
    .D(InstDone), .clk(Execute), .Q(FetchTrigger), .reset(or_4_out));  // open: Qn, preset
  D_Flip_Flop d_ff_8 (.D(and_10_out), .clk(and_10_out), .Q(ClearBreak), .reset(and_11_out));  // open: Qn, preset
  and and_10 (and_10_out, TriggerReturnFromInterupt, InteruptState);
  Register #(.trigger("falling")) register_3 (
    .D(controlled_buffer_5_out), .en(DecodeHigh), .clk(Clock), .Q(register_3_q), .clr(Clear));
  assign controlled_buffer_5_out = DecodeHigh ? controlled_buffer_6_out : 8'bz;  // Controlled_Buffer controlled_buffer_5
  Retreive retreive_1 (
    .Reset(Fetch), .Clock(Decode), .LowByte(LowByte), .DecodeHigh(DecodeHigh), .X(RegOut[15:8]),
    .Y(RegOut[23:16]), .HighByte(register_3_q), .ExecuteFlag(InitialExecuteFlag), .DecodeFlag(DecodeFlag),
    .HighByteFlag(HighFlag), .PCOFFflag(retreive_1_pcoffflag), .AddressInput(AddMode),
    .NextAddress(TempPCOveride));
  and and_11 (and_11_out, ClearBreak, ExecuteFlag);
  D_Flip_Flop #(.trigger("falling")) d_ff_9 (
    .D(KeepPCOFF), .clk(PCOFF), .Q(d_ff_9_q), .reset(or_5_out));  // open: Qn, preset
  Register #(.trigger("falling")) register_4 (.D(InstOut), .en(SWrite), .clk(Clock), .Q(Sout), .clr(Clear));
  Execute execute_1 (
    .InstIn(InstOut), .InstructionSet1(InstructionSet1), .InstructionSet2(InstructionSet2),
    .InstructionSet3(InstructionSet3), .LowByte(LowByte), .RegisterIn(RegOut), .PCin(PCOUT),
    .PCin_2(PCALTOUT), .StackIn(Sout), .StatusIn(POut), .Execute(Execute), .Fetch(Fetch), .AMode(AddMode[3]),
    .SWrite(SWrite), .YWrite(YWrite), .XWrite(XWrite), .AWrite(AWrite), .MWrite(MWrite), .PWrite(PWrite),
    .Stack(Stack), .MRead(MRead), .StackOverwrite(execute_1_stackoverwrite), .KeepPCOFF(KeepPCOFF),
    .PCWrite(PCWrite), .ClearCarry(ClearCarry), .ClearDecimal(ClearDecimal), .ClearInterupt(ClearInterupt),
    .ClearOverflow(ClearOverflow), .SetCarry(SetCarry), .SetDecimal(SetDecimal), .SetInterupt(SetInterupt),
    .PCInstructionOut(PCInstOut), .InstructionDone(InstDone), .InstructionOut(InstOut), .ZNRead(ZNRead),
    .CRead(CRead), .ORead(ORead), .ZWrite(Zero), .NWrite(Negative), .CWrite(Carry), .OWrite(Overflow),
    .Break(Break));
  not not_6 (not_6_out, ClearBreak);
  assign controlled_buffer_6_out = not_6_out ? controlled_buffer_17_out : 8'bz;  // Controlled_Buffer controlled_buffer_6
  or or_5 (or_5_out, ExecuteOff, Clear);
  assign controlled_buffer_6_out = ClearBreak ? 8'h40 : 8'bz;  // Controlled_Buffer controlled_buffer_7
  or or_6 (PCOFF, d_ff_9_q, retreive_1_pcoffflag);
  not not_7 (not_7_out, ExecuteOff);
  Register #(.trigger("falling")) register_5 (.D(InstOut), .en(AWrite), .clk(Clock), .Q(RegOut[7:0]), .clr(Clear));
  Register #(.trigger("falling")) register_6 (.D(InstOut), .en(XWrite), .clk(Clock), .Q(RegOut[15:8]), .clr(Clear));
  Register #(.trigger("falling")) register_7 (.D(InstOut), .en(YWrite), .clk(Clock), .Q(RegOut[23:16]), .clr(Clear));
  and and_12 (StackOverwrite, not_7_out, execute_1_stackoverwrite);
  not not_8 (not_8_out, PCOFF);
  assign controlled_buffer_8_out = not_8_out ? Itterate : 1'bz;  // Controlled_Buffer controlled_buffer_8
  or or_7 (or_7_out, Itterate, MRead);
  or or_8 (or_8_out, or_7_out, MWrite);
  assign controlled_buffer_9_out = PCWrite ? PCInstOut : 16'bz;  // Controlled_Buffer controlled_buffer_9
  assign controlled_buffer_9_out = not_9_out ? PCOUT : 16'bz;  // Controlled_Buffer controlled_buffer_10
  not not_9 (not_9_out, PCWrite);
  assign controlled_buffer_11_out = PCOFF ? DecodeHigh : 1'bz;  // Controlled_Buffer controlled_buffer_11
  Program_Counter program_counter_1 (
    .Input(TempPCOveride), .ClockIn(Clock), .OverwriteIn(TempOverwrtie),
    .ItterateIn(controlled_buffer_11_out), .Reset(Clear), .Output(PCALTOUT));
  RAM #(.addrWidth(16)) ram_1 (
    .addr(controlled_buffer_14_out), .we(MWrite), .oe(or_7_out), .clk(or_8_out), .data(ram_1_data));
  Program_Counter program_counter_2 (
    .Input(controlled_buffer_9_out), .ClockIn(Clock), .OverwriteIn(PCWrite),
    .ItterateIn(controlled_buffer_8_out), .Reset(Clear), .Output(PCOUT));
  assign controlled_buffer_12_out = not_8_out ? PCOUT : 16'bz;  // Controlled_Buffer controlled_buffer_12
  assign controlled_buffer_12_out = PCOFF ? PCALTOUT : 16'bz;  // Controlled_Buffer controlled_buffer_13
  Register register_8 (.D(InstOut), .en(Clock), .clk(Stack), .Q(register_8_q));  // open: clr
  not not_10 (not_10_out, StackOverwrite);
  assign controlled_buffer_14_out = not_10_out ? controlled_buffer_12_out : 16'bz;  // Controlled_Buffer controlled_buffer_14
  assign controlled_buffer_14_out = StackOverwrite ? {8'h1, register_8_q} : 16'bz;  // Controlled_Buffer controlled_buffer_15
  assign InstOut = MRead ? ram_1_data : 8'bz;  // Controlled_Buffer controlled_buffer_16
  assign controlled_buffer_17_out = Itterate ? ram_1_data : 8'bz;  // Controlled_Buffer controlled_buffer_17
  assign ram_1_data = MWrite ? InstOut : 8'bz;  // Controlled_Buffer controlled_buffer_18

  // Other names for the same wires on the sheet: InteruptOveride = ClearBreak; Off = InteruptState

  // Notes on the sheet:
  //   Low Byte
  //   High Byte
  //   A
  //   X
  //   Y
  //   Program Counter
endmodule

module Clock (
  input  ClockIn,
  output C3,
  output C2,
  output C1,
  output C0,
  output Clock
);

  wire d_ff_1_q, d_ff_2_q, d_ff_3_q, d_ff_4_q, not_1_out, or_1_out;

  or or_1 (or_1_out, d_ff_1_q, d_ff_2_q, d_ff_3_q, d_ff_4_q);
  not not_1 (not_1_out, or_1_out);
  D_Flip_Flop #(.trigger("falling")) d_ff_1 (.D(d_ff_2_q), .clk(ClockIn), .Q(d_ff_1_q));  // open: Qn, preset, reset
  D_Flip_Flop #(.trigger("falling")) d_ff_2 (.D(d_ff_3_q), .clk(ClockIn), .Q(d_ff_2_q));  // open: Qn, preset, reset
  D_Flip_Flop #(.trigger("falling")) d_ff_3 (.D(d_ff_4_q), .clk(ClockIn), .Q(d_ff_3_q));  // open: Qn, preset, reset
  D_Flip_Flop #(.trigger("falling")) d_ff_4 (.D(not_1_out), .clk(ClockIn), .Q(d_ff_4_q));  // open: Qn, preset, reset
  and and_1 (C3, ClockIn, d_ff_1_q);
  and and_2 (C2, ClockIn, d_ff_2_q);
  and and_3 (C1, ClockIn, d_ff_3_q);
  and and_4 (C0, ClockIn, d_ff_4_q);

  assign Clock = ClockIn;
endmodule

module Program_Counter (
  input  [15:0] Input,
  input  ClockIn,
  input  OverwriteIn,
  input  Reset,
  input  ItterateIn,
  output [15:0] Output
);

  wire or_1_out;
  wire [15:0] adder_1_out, controlled_buffer_1_out;

  Adder #(.width(16)) adder_1 (.a(Output), .b(16'h1), .out(adder_1_out));  // open: cin, cout
  assign controlled_buffer_1_out = ItterateIn ? adder_1_out : 16'bz;  // Controlled_Buffer controlled_buffer_1
  assign controlled_buffer_1_out = OverwriteIn ? Input : 16'bz;  // Controlled_Buffer controlled_buffer_2
  Register #(.width(16), .trigger("falling")) register_1 (
    .D(controlled_buffer_1_out), .en(or_1_out), .clk(ClockIn), .Q(Output), .clr(Reset));
  or or_1 (or_1_out, OverwriteIn, ItterateIn);
endmodule

module Decoder (
  input  [7:0] Input,
  output BRK,
  output PHP,
  output ORA,
  output ASL,
  output CLC,
  output BPL,
  output JSR,
  output PLP,
  output AND,
  output ROL,
  output SEC,
  output BMI,
  output RTI,
  output PHA,
  output EOR,
  output LSR,
  output CLI,
  output JMP,
  output BVC,
  output RTS,
  output PLA,
  output ind,
  output ADC,
  output ROR,
  output SEI,
  output BVS,
  output DEY,
  output TXA,
  output STA,
  output STY,
  output STX,
  output TYA,
  output TXS,
  output BCC,
  output TAY,
  output TAX,
  output LDY,
  output LDA,
  output LDX,
  output CLV,
  output TSX,
  output BCS,
  output zpgY,
  output INY,
  output DEX,
  output CPY,
  output CMP,
  output DEC,
  output CLD,
  output BNE,
  output INX,
  output CPX,
  output SBC,
  output INC,
  output SED,
  output BEQ,
  output rel,
  output Xind,
  output absY,
  output A,
  output zpg,
  output indY,
  output zpgX,
  output abs,
  output absX,
  output hash
);

  wire and_10_out, and_12_out, and_14_out, and_16_out, and_17_out, and_18_out, and_19_out, and_20_out,
       and_21_out, and_22_out, and_23_out, and_24_out, and_25_out, and_26_out, and_27_out, and_28_out,
       and_29_out, and_30_out, and_31_out, and_32_out, and_33_out, and_34_out, and_35_out, and_36_out,
       and_37_out, and_38_out, and_39_out, and_40_out, and_41_out, and_42_out, and_43_out, and_44_out,
       and_45_out, and_46_out, and_47_out, and_48_out, and_49_out, and_50_out, and_51_out, and_52_out,
       and_53_out, and_54_out, and_55_out, and_56_out, and_57_out, and_58_out, and_59_out, and_60_out,
       and_61_out, and_62_out, and_63_out, and_64_out, and_65_out, and_66_out, and_67_out, and_68_out,
       and_69_out, and_70_out, and_87_out, and_88_out, and_89_out, and_90_out, and_91_out, and_92_out,
       and_93_out, and_94_out, and_95_out, and_96_out, and_97_out, and_98_out, and_99_out, and_100_out,
       and_101_out, and_102_out, and_103_out, and_104_out, and_105_out, and_111_out, and_113_out,
       and_114_out, and_116_out, and_117_out, and_118_out, and_119_out, and_120_out, and_121_out,
       and_122_out, and_123_out, and_124_out, and_125_out, and_126_out, and_127_out, and_128_out,
       and_129_out, and_130_out, and_131_out, and_132_out, and_133_out, and_134_out, and_135_out,
       and_136_out, and_137_out, and_138_out, and_139_out, and_140_out, and_141_out, and_142_out,
       and_143_out, and_145_out, and_146_out, and_147_out, and_148_out, decoder_1_out0, decoder_1_out1,
       decoder_1_out2, decoder_1_out3, decoder_1_out4, decoder_1_out5, decoder_1_out6, decoder_1_out7,
       decoder_1_out8, decoder_1_out9, decoder_1_out10, decoder_1_out11, decoder_1_out12, decoder_1_out13,
       decoder_1_out14, decoder_1_out15, decoder_2_out0, decoder_2_out1, decoder_2_out2, decoder_2_out4,
       decoder_2_out5, decoder_2_out6, decoder_2_out8, decoder_2_out9, decoder_2_out10, decoder_2_out12,
       decoder_2_out13, decoder_2_out14, LDXABSY, LDYABSX, or_1_out, or_2_out, or_3_out, or_4_out, or_5_out,
       or_6_out, or_7_out, or_8_out, or_10_out, or_12_out, or_13_out, or_14_out, or_15_out, or_16_out,
       or_17_out, or_19_out, or_20_out, or_21_out, or_22_out, or_23_out, or_24_out, or_25_out, or_26_out,
       or_27_out, or_28_out, or_29_out, or_30_out, or_31_out, or_32_out, or_34_out, or_35_out, or_36_out,
       or_38_out, or_39_out, or_40_out, or_41_out, or_42_out, or_44_out, or_45_out, or_46_out, or_47_out,
       or_48_out, or_49_out, or_50_out, or_51_out, or_52_out, or_53_out, or_54_out, or_55_out, or_56_out,
       or_57_out, or_58_out, or_59_out, or_60_out, or_61_out, or_62_out, or_63_out, or_64_out, or_65_out,
       or_66_out, or_67_out, or_68_out, or_69_out, or_70_out, or_71_out, or_72_out, or_73_out, or_74_out,
       or_75_out, or_76_out, or_77_out, or_78_out, or_79_out, or_80_out, or_81_out, or_82_out, or_83_out,
       or_84_out, or_85_out, or_86_out, or_87_out, or_88_out, or_89_out, or_90_out, or_91_out, or_92_out,
       or_93_out, or_94_out, or_96_out, or_97_out, or_98_out, or_99_out, or_100_out, or_101_out, or_102_out,
       or_103_out, or_104_out, or_105_out, or_106_out, or_107_out, or_108_out, or_109_out, or_110_out,
       or_111_out, or_112_out, or_113_out, or_114_out, or_115_out, or_116_out, or_117_out, or_118_out,
       or_119_out, or_121_out, or_122_out, or_123_out, or_124_out, or_125_out, or_126_out, or_127_out,
       or_128_out, or_129_out, or_131_out, or_132_out, or_133_out, or_134_out, or_135_out, or_136_out,
       or_137_out, or_138_out, or_139_out, or_142_out, or_147_out, or_148_out, or_149_out, or_150_out,
       or_151_out, or_152_out, or_153_out, or_154_out, or_155_out, or_156_out, or_157_out, or_158_out,
       or_159_out, or_160_out, or_161_out, or_163_out, or_164_out, or_165_out, or_166_out, or_167_out,
       or_168_out, or_169_out, or_170_out, or_178_out, or_180_out, or_181_out, or_182_out, or_183_out,
       or_184_out, or_185_out, or_186_out, or_187_out, or_188_out, or_189_out, or_190_out, or_191_out,
       or_193_out, or_194_out, or_195_out, or_196_out, or_199_out, or_200_out, or_201_out;

  Decoder_part #(.select(4)) decoder_1 (
    .out0(decoder_1_out0), .out1(decoder_1_out1), .out2(decoder_1_out2), .out3(decoder_1_out3),
    .out4(decoder_1_out4), .out5(decoder_1_out5), .out6(decoder_1_out6), .out7(decoder_1_out7),
    .out8(decoder_1_out8), .out9(decoder_1_out9), .out10(decoder_1_out10), .out11(decoder_1_out11),
    .out12(decoder_1_out12), .out13(decoder_1_out13), .out14(decoder_1_out14), .out15(decoder_1_out15),
    .sel(Input[7:4]));  // open: en
  and and_1 (BRK, decoder_2_out0, decoder_1_out0);
  and and_2 (BPL, decoder_2_out0, decoder_1_out1);
  and and_3 (JSR, decoder_2_out0, decoder_1_out2);
  and and_4 (BMI, decoder_2_out0, decoder_1_out3);
  and and_5 (RTI, decoder_2_out0, decoder_1_out4);
  and and_6 (BVC, decoder_2_out0, decoder_1_out5);
  and and_7 (RTS, decoder_2_out0, decoder_1_out6);
  and and_8 (BVS, decoder_2_out0, decoder_1_out7);
  and and_9 (BCC, decoder_2_out0, decoder_1_out9);
  and and_10 (and_10_out, decoder_2_out0, decoder_1_out10);
  and and_11 (BCS, decoder_2_out0, decoder_1_out11);
  and and_12 (and_12_out, decoder_2_out0, decoder_1_out12);
  and and_13 (BNE, decoder_2_out0, decoder_1_out13);
  and and_14 (and_14_out, decoder_2_out0, decoder_1_out14);
  and and_15 (BEQ, decoder_2_out0, decoder_1_out15);
  or or_1 (or_1_out, BMI, BPL);
  or or_2 (or_2_out, BVC, or_1_out);
  or or_3 (or_3_out, BVS, or_2_out);
  or or_4 (or_4_out, BCC, or_3_out);
  or or_5 (or_5_out, BCS, or_4_out);
  or or_6 (or_6_out, and_12_out, and_10_out);
  or or_7 (or_7_out, BNE, or_5_out);
  or or_8 (or_8_out, and_14_out, or_6_out);
  or or_9 (rel, BEQ, or_7_out);
  or or_10 (or_10_out, or_8_out, and_32_out);
  or or_11 (hash, or_10_out, or_104_out);
  and and_16 (and_16_out, decoder_2_out1, decoder_1_out0);
  and and_17 (and_17_out, decoder_2_out1, decoder_1_out1);
  and and_18 (and_18_out, decoder_2_out1, decoder_1_out2);
  or or_12 (or_12_out, and_18_out, and_16_out);
  and and_19 (and_19_out, decoder_2_out1, decoder_1_out3);
  and and_20 (and_20_out, decoder_2_out1, decoder_1_out4);
  or or_13 (or_13_out, and_20_out, or_12_out);
  and and_21 (and_21_out, decoder_2_out1, decoder_1_out5);
  and and_22 (and_22_out, decoder_2_out1, decoder_1_out6);
  or or_14 (or_14_out, and_22_out, or_13_out);
  and and_23 (and_23_out, decoder_2_out1, decoder_1_out7);
  and and_24 (and_24_out, decoder_2_out1, decoder_1_out8);
  or or_15 (or_15_out, and_24_out, or_14_out);
  and and_25 (and_25_out, decoder_2_out1, decoder_1_out9);
  and and_26 (and_26_out, decoder_2_out1, decoder_1_out10);
  or or_16 (or_16_out, and_26_out, or_15_out);
  and and_27 (and_27_out, decoder_2_out1, decoder_1_out11);
  and and_28 (and_28_out, decoder_2_out1, decoder_1_out12);
  or or_17 (or_17_out, and_28_out, or_16_out);
  and and_29 (and_29_out, decoder_2_out1, decoder_1_out13);
  and and_30 (and_30_out, decoder_2_out1, decoder_1_out14);
  or or_18 (Xind, and_30_out, or_17_out);
  and and_31 (and_31_out, decoder_2_out1, decoder_1_out15);
  or or_19 (or_19_out, and_16_out, and_17_out);
  or or_20 (or_20_out, and_19_out, and_18_out);
  or or_21 (or_21_out, and_19_out, and_17_out);
  or or_22 (or_22_out, and_21_out, and_20_out);
  or or_23 (or_23_out, and_21_out, or_21_out);
  or or_24 (or_24_out, and_23_out, and_22_out);
  or or_25 (or_25_out, and_23_out, or_23_out);
  or or_26 (or_26_out, and_25_out, and_24_out);
  or or_27 (or_27_out, and_25_out, or_25_out);
  or or_28 (or_28_out, and_27_out, and_26_out);
  or or_29 (or_29_out, and_27_out, or_27_out);
  or or_30 (or_30_out, and_29_out, and_28_out);
  or or_31 (or_31_out, and_29_out, or_29_out);
  or or_32 (or_32_out, and_31_out, and_30_out);
  or or_33 (indY, and_31_out, or_31_out);
  and and_32 (and_32_out, decoder_2_out2, decoder_1_out10);
  and and_33 (and_33_out, decoder_2_out4, decoder_1_out8);
  and and_34 (and_34_out, decoder_2_out4, decoder_1_out9);
  and and_35 (and_35_out, decoder_2_out4, decoder_1_out10);
  or or_34 (or_34_out, and_35_out, and_33_out);
  and and_36 (and_36_out, decoder_2_out4, decoder_1_out11);
  and and_37 (and_37_out, decoder_2_out4, decoder_1_out12);
  or or_35 (or_35_out, and_37_out, or_34_out);
  and and_38 (and_38_out, decoder_2_out4, decoder_1_out14);
  or or_36 (or_36_out, and_38_out, or_35_out);
  or or_37 (zpg, or_36_out, or_45_out);
  or or_38 (or_38_out, and_33_out, and_34_out);
  or or_39 (or_39_out, and_36_out, and_35_out);
  or or_40 (or_40_out, and_36_out, and_34_out);
  or or_41 (or_41_out, and_37_out, and_12_out);
  or or_42 (or_42_out, and_38_out, and_14_out);
  or or_43 (zpgX, or_40_out, or_53_out);
  or or_44 (or_44_out, and_10_out, or_39_out);
  or or_45 (or_45_out, or_87_out, or_52_out);
  and and_39 (and_39_out, decoder_2_out5, decoder_1_out0);
  and and_40 (and_40_out, decoder_2_out5, decoder_1_out1);
  and and_41 (and_41_out, decoder_2_out5, decoder_1_out2);
  or or_46 (or_46_out, and_41_out, and_39_out);
  and and_42 (and_42_out, decoder_2_out5, decoder_1_out3);
  and and_43 (and_43_out, decoder_2_out5, decoder_1_out4);
  or or_47 (or_47_out, and_43_out, or_46_out);
  and and_44 (and_44_out, decoder_2_out5, decoder_1_out5);
  and and_45 (and_45_out, decoder_2_out5, decoder_1_out6);
  or or_48 (or_48_out, and_45_out, or_47_out);
  and and_46 (and_46_out, decoder_2_out5, decoder_1_out7);
  and and_47 (and_47_out, decoder_2_out5, decoder_1_out8);
  or or_49 (or_49_out, and_47_out, or_48_out);
  and and_48 (and_48_out, decoder_2_out5, decoder_1_out9);
  and and_49 (and_49_out, decoder_2_out5, decoder_1_out10);
  or or_50 (or_50_out, and_49_out, or_49_out);
  and and_50 (and_50_out, decoder_2_out5, decoder_1_out11);
  and and_51 (and_51_out, decoder_2_out5, decoder_1_out12);
  or or_51 (or_51_out, and_51_out, or_50_out);
  and and_52 (and_52_out, decoder_2_out5, decoder_1_out13);
  and and_53 (and_53_out, decoder_2_out5, decoder_1_out14);
  or or_52 (or_52_out, and_53_out, or_51_out);
  and and_54 (and_54_out, decoder_2_out5, decoder_1_out15);
  or or_53 (or_53_out, or_88_out, or_68_out);
  or or_54 (or_54_out, and_39_out, and_40_out);
  or or_55 (or_55_out, and_42_out, and_41_out);
  or or_56 (or_56_out, and_42_out, and_40_out);
  or or_57 (or_57_out, and_44_out, and_43_out);
  or or_58 (or_58_out, and_44_out, or_56_out);
  or or_59 (or_59_out, and_46_out, and_45_out);
  or or_60 (or_60_out, and_46_out, or_58_out);
  or or_61 (or_61_out, and_48_out, and_47_out);
  or or_62 (or_62_out, and_48_out, or_60_out);
  or or_63 (or_63_out, and_50_out, and_49_out);
  or or_64 (or_64_out, and_50_out, or_62_out);
  or or_65 (or_65_out, and_52_out, and_51_out);
  or or_66 (or_66_out, and_52_out, or_64_out);
  or or_67 (or_67_out, and_54_out, and_53_out);
  or or_68 (or_68_out, and_54_out, or_66_out);
  or or_69 (or_69_out, or_19_out, or_54_out);
  or or_70 (or_70_out, or_20_out, or_55_out);
  or or_71 (or_71_out, or_22_out, or_57_out);
  or or_72 (or_72_out, or_24_out, or_59_out);
  or or_73 (or_73_out, or_26_out, or_61_out);
  or or_74 (or_74_out, or_28_out, or_63_out);
  or or_75 (or_75_out, or_30_out, or_65_out);
  or or_76 (or_76_out, or_32_out, or_67_out);
  and and_55 (and_55_out, decoder_2_out6, decoder_1_out0);
  and and_56 (and_56_out, decoder_2_out6, decoder_1_out1);
  and and_57 (and_57_out, decoder_2_out6, decoder_1_out2);
  or or_77 (or_77_out, and_57_out, and_55_out);
  and and_58 (and_58_out, decoder_2_out6, decoder_1_out3);
  or or_78 (or_78_out, and_58_out, and_56_out);
  and and_59 (and_59_out, decoder_2_out6, decoder_1_out4);
  or or_79 (or_79_out, and_59_out, or_77_out);
  and and_60 (and_60_out, decoder_2_out6, decoder_1_out5);
  or or_80 (or_80_out, and_60_out, or_78_out);
  and and_61 (and_61_out, decoder_2_out6, decoder_1_out6);
  or or_81 (or_81_out, and_61_out, or_79_out);
  and and_62 (and_62_out, decoder_2_out6, decoder_1_out7);
  or or_82 (or_82_out, and_62_out, or_80_out);
  and and_63 (and_63_out, decoder_2_out6, decoder_1_out8);
  or or_83 (or_83_out, and_63_out, or_81_out);
  and and_64 (and_64_out, decoder_2_out6, decoder_1_out9);
  and and_65 (and_65_out, decoder_2_out6, decoder_1_out10);
  or or_84 (or_84_out, and_65_out, or_83_out);
  and and_66 (and_66_out, decoder_2_out6, decoder_1_out11);
  and and_67 (and_67_out, decoder_2_out6, decoder_1_out12);
  or or_85 (or_85_out, and_67_out, or_84_out);
  and and_68 (and_68_out, decoder_2_out6, decoder_1_out13);
  or or_86 (or_86_out, and_68_out, or_82_out);
  and and_69 (and_69_out, decoder_2_out6, decoder_1_out14);
  or or_87 (or_87_out, and_69_out, or_85_out);
  and and_70 (and_70_out, decoder_2_out6, decoder_1_out15);
  or or_88 (or_88_out, and_70_out, or_86_out);
  Decoder_part #(.select(4)) decoder_2 (
    .out0(decoder_2_out0), .out1(decoder_2_out1), .out2(decoder_2_out2), .out4(decoder_2_out4),
    .out5(decoder_2_out5), .out6(decoder_2_out6), .out8(decoder_2_out8), .out9(decoder_2_out9),
    .out10(decoder_2_out10), .out12(decoder_2_out12), .out13(decoder_2_out13), .out14(decoder_2_out14),
    .sel(Input[3:0]));  // open: out3, out7, out11, out15, en
  or or_89 (or_89_out, and_55_out, and_56_out);
  or or_90 (or_90_out, and_58_out, and_57_out);
  or or_91 (or_91_out, and_60_out, and_59_out);
  or or_92 (or_92_out, and_62_out, and_61_out);
  or or_93 (or_93_out, and_64_out, and_63_out);
  or or_94 (or_94_out, and_66_out, and_65_out);
  or or_95 (zpgY, and_66_out, and_64_out);
  or or_96 (or_96_out, and_68_out, and_67_out);
  or or_97 (or_97_out, and_70_out, and_69_out);
  or or_98 (or_98_out, and_32_out, or_94_out);
  and and_71 (PHP, decoder_2_out8, decoder_1_out0);
  and and_72 (CLC, decoder_2_out8, decoder_1_out1);
  and and_73 (PLP, decoder_2_out8, decoder_1_out2);
  and and_74 (SEC, decoder_2_out8, decoder_1_out3);
  and and_75 (PHA, decoder_2_out8, decoder_1_out4);
  and and_76 (CLI, decoder_2_out8, decoder_1_out5);
  and and_77 (PLA, decoder_2_out8, decoder_1_out6);
  and and_78 (SEI, decoder_2_out8, decoder_1_out7);
  and and_79 (DEY, decoder_2_out8, decoder_1_out8);
  and and_80 (TYA, decoder_2_out8, decoder_1_out9);
  and and_81 (TAY, decoder_2_out8, decoder_1_out10);
  and and_82 (CLV, decoder_2_out8, decoder_1_out11);
  and and_83 (INY, decoder_2_out8, decoder_1_out12);
  and and_84 (CLD, decoder_2_out8, decoder_1_out13);
  and and_85 (INX, decoder_2_out8, decoder_1_out14);
  and and_86 (SED, decoder_2_out8, decoder_1_out15);
  and and_87 (and_87_out, decoder_2_out9, decoder_1_out0);
  and and_88 (and_88_out, decoder_2_out9, decoder_1_out1);
  and and_89 (and_89_out, decoder_2_out9, decoder_1_out2);
  or or_99 (or_99_out, and_89_out, and_87_out);
  and and_90 (and_90_out, decoder_2_out9, decoder_1_out3);
  and and_91 (and_91_out, decoder_2_out9, decoder_1_out4);
  or or_100 (or_100_out, and_91_out, or_99_out);
  and and_92 (and_92_out, decoder_2_out9, decoder_1_out5);
  and and_93 (and_93_out, decoder_2_out9, decoder_1_out6);
  or or_101 (or_101_out, and_93_out, or_100_out);
  and and_94 (and_94_out, decoder_2_out9, decoder_1_out7);
  and and_95 (and_95_out, decoder_2_out9, decoder_1_out9);
  and and_96 (and_96_out, decoder_2_out9, decoder_1_out10);
  or or_102 (or_102_out, and_96_out, or_101_out);
  and and_97 (and_97_out, decoder_2_out9, decoder_1_out11);
  and and_98 (and_98_out, decoder_2_out9, decoder_1_out12);
  or or_103 (or_103_out, and_98_out, or_102_out);
  and and_99 (and_99_out, decoder_2_out9, decoder_1_out13);
  and and_100 (and_100_out, decoder_2_out9, decoder_1_out14);
  or or_104 (or_104_out, and_100_out, or_103_out);
  and and_101 (and_101_out, decoder_2_out9, decoder_1_out15);
  or or_105 (or_105_out, and_87_out, and_88_out);
  or or_106 (or_106_out, and_90_out, and_89_out);
  or or_107 (or_107_out, and_90_out, and_88_out);
  or or_108 (or_108_out, and_92_out, and_91_out);
  or or_109 (or_109_out, and_92_out, or_107_out);
  or or_110 (or_110_out, and_94_out, and_93_out);
  or or_111 (or_111_out, and_94_out, or_109_out);
  or or_112 (or_112_out, and_95_out, or_73_out);
  or or_113 (or_113_out, and_95_out, or_111_out);
  or or_114 (or_114_out, and_97_out, and_96_out);
  or or_115 (or_115_out, and_97_out, or_113_out);
  or or_116 (or_116_out, and_99_out, and_98_out);
  or or_117 (or_117_out, and_99_out, or_115_out);
  or or_118 (or_118_out, and_101_out, and_100_out);
  or or_119 (or_119_out, and_101_out, or_117_out);
  or or_120 (absY, or_119_out, LDXABSY);
  or or_121 (or_121_out, or_69_out, or_105_out);
  or or_122 (or_122_out, or_70_out, or_106_out);
  or or_123 (or_123_out, or_71_out, or_108_out);
  or or_124 (or_124_out, or_72_out, or_110_out);
  or or_125 (or_125_out, or_74_out, or_114_out);
  or or_126 (or_126_out, or_75_out, or_116_out);
  or or_127 (or_127_out, or_76_out, or_118_out);
  and and_102 (and_102_out, decoder_2_out10, decoder_1_out0);
  and and_103 (and_103_out, decoder_2_out10, decoder_1_out2);
  or or_128 (or_128_out, and_103_out, and_102_out);
  and and_104 (and_104_out, decoder_2_out10, decoder_1_out4);
  or or_129 (or_129_out, and_104_out, or_128_out);
  and and_105 (and_105_out, decoder_2_out10, decoder_1_out6);
  or or_130 (A, and_105_out, or_129_out);
  and and_106 (TXA, decoder_2_out10, decoder_1_out8);
  and and_107 (TXS, decoder_2_out10, decoder_1_out9);
  and and_108 (TAX, decoder_2_out10, decoder_1_out10);
  and and_109 (TSX, decoder_2_out10, decoder_1_out11);
  and and_110 (DEX, decoder_2_out10, decoder_1_out12);
  or or_131 (or_131_out, or_89_out, and_102_out);
  or or_132 (or_132_out, or_90_out, and_103_out);
  or or_133 (or_133_out, or_91_out, and_104_out);
  or or_134 (or_134_out, or_92_out, and_105_out);
  and and_111 (and_111_out, decoder_2_out12, decoder_1_out4);
  and and_112 (ind, decoder_2_out12, decoder_1_out6);
  and and_113 (and_113_out, decoder_2_out12, decoder_1_out8);
  or or_135 (or_135_out, and_113_out, and_111_out);
  and and_114 (and_114_out, decoder_2_out12, decoder_1_out10);
  or or_136 (or_136_out, and_114_out, or_135_out);
  and and_115 (LDYABSX, decoder_2_out12, decoder_1_out11);
  and and_116 (and_116_out, decoder_2_out12, decoder_1_out12);
  or or_137 (or_137_out, and_116_out, or_136_out);
  and and_117 (and_117_out, decoder_2_out12, decoder_1_out14);
  or or_138 (or_138_out, and_117_out, or_137_out);
  or or_139 (or_139_out, or_138_out, JSR);
  or or_140 (JMP, and_111_out, ind);
  or or_141 (STY, or_38_out, and_113_out);
  or or_142 (or_142_out, LDYABSX, and_114_out);
  or or_143 (CPY, or_41_out, and_116_out);
  or or_144 (CPX, or_42_out, and_117_out);
  or or_145 (abs, or_139_out, or_147_out);
  and and_118 (and_118_out, decoder_2_out13, decoder_1_out0);
  and and_119 (and_119_out, decoder_2_out13, decoder_1_out1);
  and and_120 (and_120_out, decoder_2_out13, decoder_1_out2);
  and and_121 (and_121_out, decoder_2_out13, decoder_1_out3);
  and and_122 (and_122_out, decoder_2_out13, decoder_1_out4);
  and and_123 (and_123_out, decoder_2_out13, decoder_1_out5);
  and and_124 (and_124_out, decoder_2_out13, decoder_1_out6);
  and and_125 (and_125_out, decoder_2_out13, decoder_1_out7);
  and and_126 (and_126_out, decoder_2_out13, decoder_1_out8);
  and and_127 (and_127_out, decoder_2_out13, decoder_1_out9);
  and and_128 (and_128_out, decoder_2_out13, decoder_1_out10);
  or or_146 (LDY, or_44_out, or_142_out);
  and and_129 (and_129_out, decoder_2_out13, decoder_1_out11);
  and and_130 (and_130_out, decoder_2_out13, decoder_1_out12);
  and and_131 (and_131_out, decoder_2_out13, decoder_1_out13);
  and and_132 (and_132_out, decoder_2_out13, decoder_1_out14);
  and and_133 (and_133_out, decoder_2_out13, decoder_1_out15);
  or or_147 (or_147_out, or_160_out, or_190_out);
  or or_148 (or_148_out, and_120_out, and_118_out);
  or or_149 (or_149_out, and_121_out, and_119_out);
  or or_150 (or_150_out, and_122_out, or_148_out);
  or or_151 (or_151_out, and_123_out, or_149_out);
  or or_152 (or_152_out, and_124_out, or_150_out);
  or or_153 (or_153_out, and_125_out, or_151_out);
  or or_154 (or_154_out, and_126_out, or_152_out);
  or or_155 (or_155_out, and_127_out, or_153_out);
  or or_156 (or_156_out, and_128_out, or_154_out);
  or or_157 (or_157_out, and_129_out, or_155_out);
  or or_158 (or_158_out, and_130_out, or_156_out);
  or or_159 (or_159_out, and_131_out, or_157_out);
  or or_160 (or_160_out, and_132_out, or_158_out);
  or or_161 (or_161_out, and_133_out, or_159_out);
  or or_162 (ORA, or_121_out, or_163_out);
  or or_163 (or_163_out, and_118_out, and_119_out);
  or or_164 (or_164_out, and_121_out, and_120_out);
  or or_165 (or_165_out, and_123_out, and_122_out);
  or or_166 (or_166_out, and_125_out, and_124_out);
  or or_167 (or_167_out, and_127_out, and_126_out);
  or or_168 (or_168_out, and_129_out, and_128_out);
  or or_169 (or_169_out, and_131_out, and_130_out);
  or or_170 (or_170_out, and_133_out, and_132_out);
  or or_171 (AND, or_122_out, or_164_out);
  or or_172 (EOR, or_123_out, or_165_out);
  or or_173 (ADC, or_124_out, or_166_out);
  or or_174 (STA, or_112_out, or_167_out);
  or or_175 (LDA, or_125_out, or_168_out);
  or or_176 (CMP, or_126_out, or_169_out);
  or or_177 (SBC, or_127_out, or_170_out);
  or or_178 (or_178_out, or_161_out, or_191_out);
  or or_179 (absX, or_178_out, LDYABSX);
  and and_134 (and_134_out, decoder_2_out14, decoder_1_out0);
  and and_135 (and_135_out, decoder_2_out14, decoder_1_out1);
  and and_136 (and_136_out, decoder_2_out14, decoder_1_out2);
  or or_180 (or_180_out, and_136_out, and_134_out);
  and and_137 (and_137_out, decoder_2_out14, decoder_1_out3);
  or or_181 (or_181_out, and_137_out, and_135_out);
  and and_138 (and_138_out, decoder_2_out14, decoder_1_out4);
  or or_182 (or_182_out, and_138_out, or_180_out);
  and and_139 (and_139_out, decoder_2_out14, decoder_1_out5);
  or or_183 (or_183_out, and_139_out, or_181_out);
  and and_140 (and_140_out, decoder_2_out14, decoder_1_out6);
  or or_184 (or_184_out, and_140_out, or_182_out);
  and and_141 (and_141_out, decoder_2_out14, decoder_1_out7);
  or or_185 (or_185_out, and_141_out, or_183_out);
  and and_142 (and_142_out, decoder_2_out14, decoder_1_out8);
  or or_186 (or_186_out, and_142_out, or_184_out);
  and and_143 (and_143_out, decoder_2_out14, decoder_1_out10);
  or or_187 (or_187_out, and_143_out, or_186_out);
  and and_144 (LDXABSY, decoder_2_out14, decoder_1_out11);
  and and_145 (and_145_out, decoder_2_out14, decoder_1_out12);
  or or_188 (or_188_out, and_145_out, or_187_out);
  and and_146 (and_146_out, decoder_2_out14, decoder_1_out13);
  or or_189 (or_189_out, and_146_out, or_185_out);
  and and_147 (and_147_out, decoder_2_out14, decoder_1_out14);
  or or_190 (or_190_out, and_147_out, or_188_out);
  and and_148 (and_148_out, decoder_2_out14, decoder_1_out15);
  or or_191 (or_191_out, and_148_out, or_189_out);
  or or_192 (ASL, or_131_out, or_193_out);
  or or_193 (or_193_out, and_134_out, and_135_out);
  or or_194 (or_194_out, and_137_out, and_136_out);
  or or_195 (or_195_out, and_139_out, and_138_out);
  or or_196 (or_196_out, and_141_out, and_140_out);
  or or_197 (STX, or_93_out, and_142_out);
  or or_198 (LDX, or_98_out, or_199_out);
  or or_199 (or_199_out, LDXABSY, and_143_out);
  or or_200 (or_200_out, and_146_out, and_145_out);
  or or_201 (or_201_out, and_148_out, and_147_out);
  or or_202 (ROL, or_132_out, or_194_out);
  or or_203 (LSR, or_133_out, or_195_out);
  or or_204 (ROR, or_134_out, or_196_out);
  or or_205 (DEC, or_96_out, or_200_out);
  or or_206 (INC, or_97_out, or_201_out);

  // Other names for the same wires on the sheet: JSRABS = JSR

  // Notes on the sheet:
  //   _0
  //   _1
  //   _2
  //   _4
endmodule

module Retreive (
  input  Reset,
  input  Clock,
  input  [7:0] LowByte,
  input  DecodeHigh,
  input  [7:0] X,
  input  [7:0] Y,
  input  [7:0] HighByte,
  input  [11:0] AddressInput,
  output ExecuteFlag,
  output DecodeFlag,
  output HighByteFlag,
  output PCOFFflag,
  output [15:0] NextAddress
);

  wire and_1_out, and_2_out, and_4_out, and_5_out, d_ff_1_q, d_ff_3_q, d_ff_4_q, Itter1, not_1_out,
       not_3_out, not_4_out, not_5_out, not_6_out, not_7_out, not_8_out, not_9_out, or_1_out, or_3_out,
       or_4_out, or_5_out, or_6_out, or_7_out, or_8_out, or_9_out, or_10_out, or_11_out, or_12_out,
       or_13_out, or_14_out, or_15_out, or_16_out, or_17_out, or_18_out, or_19_out, or_20_out, or_21_out,
       or_22_out;
  wire [7:0] adder_1_out, adder_2_out, adder_3_out, adder_4_out, adder_5_out, adder_6_out,
       controlled_buffer_14_out, controlled_buffer_16_out, controlled_buffer_21_out, controlled_buffer_23_out;

  not not_1 (not_1_out, or_1_out);
  or or_1 (or_1_out, AddressInput[11], AddressInput[10], AddressInput[9], AddressInput[8], AddressInput[7], AddressInput[6], AddressInput[5], AddressInput[4], AddressInput[2], AddressInput[1], AddressInput[0]);
  not not_2 (DecodeFlag, ExecuteFlag);
  or or_2 (ExecuteFlag, not_1_out, d_ff_1_q);
  or or_3 (or_3_out, AddressInput[11], AddressInput[10]);
  or or_4 (or_4_out, or_3_out, Itter1);
  assign NextAddress[7:0] = AddressInput[7] ? LowByte : 8'bz;  // Controlled_Buffer controlled_buffer_1
  Adder adder_1 (.a(LowByte), .b(X), .out(adder_1_out));  // open: cin, cout
  assign NextAddress[15:8] = AddressInput[7] ? {8{1'b0}} : 8'bz;  // Controlled_Buffer controlled_buffer_2
  D_Flip_Flop #(.trigger("falling")) d_ff_1 (
    .D(or_4_out), .clk(Clock), .Q(d_ff_1_q), .reset(Reset));  // open: Qn, preset
  assign NextAddress[7:0] = AddressInput[6] ? adder_1_out : 8'bz;  // Controlled_Buffer controlled_buffer_3
  assign NextAddress[15:8] = AddressInput[6] ? {8{1'b0}} : 8'bz;  // Controlled_Buffer controlled_buffer_4
  or or_5 (or_5_out, AddressInput[7], AddressInput[6]);
  assign NextAddress[7:0] = AddressInput[5] ? adder_2_out : 8'bz;  // Controlled_Buffer controlled_buffer_5
  Adder adder_2 (.a(LowByte), .b(Y), .out(adder_2_out));  // open: cin, cout
  assign NextAddress[15:8] = AddressInput[5] ? {8{1'b0}} : 8'bz;  // Controlled_Buffer controlled_buffer_6
  or or_6 (or_6_out, or_5_out, AddressInput[5]);
  assign NextAddress[7:0] = AddressInput[1] ? LowByte : 8'bz;  // Controlled_Buffer controlled_buffer_7
  assign NextAddress[15:8] = AddressInput[1] ? HighByte : 8'bz;  // Controlled_Buffer controlled_buffer_8
  assign NextAddress[7:0] = AddressInput[0] ? adder_3_out : 8'bz;  // Controlled_Buffer controlled_buffer_9
  Adder adder_3 (.a(LowByte), .b(X), .out(adder_3_out));  // open: cin, cout
  assign NextAddress[15:8] = AddressInput[0] ? HighByte : 8'bz;  // Controlled_Buffer controlled_buffer_10
  or or_7 (or_7_out, or_6_out, AddressInput[1]);
  assign NextAddress[7:0] = AddressInput[4] ? adder_4_out : 8'bz;  // Controlled_Buffer controlled_buffer_11
  Adder adder_4 (.a(LowByte), .b(Y), .out(adder_4_out));  // open: cin, cout
  assign NextAddress[15:8] = AddressInput[4] ? HighByte : 8'bz;  // Controlled_Buffer controlled_buffer_12
  or or_8 (or_8_out, AddressInput[1], AddressInput[0]);
  or or_9 (or_9_out, AddressInput[1], AddressInput[0]);
  or or_10 (or_10_out, or_7_out, AddressInput[0]);
  or or_11 (or_11_out, or_8_out, AddressInput[4]);
  or or_12 (or_12_out, or_9_out, AddressInput[4]);
  or or_13 (or_13_out, or_10_out, AddressInput[4]);
  D_Flip_Flop #(.trigger("falling")) d_ff_2 (
    .D(or_14_out), .clk(Clock), .Q(Itter1), .reset(Reset));  // open: Qn, preset
  or or_14 (or_14_out, or_13_out, d_ff_3_q);
  assign NextAddress[7:0] = AddressInput[2] ? LowByte : 8'bz;  // Controlled_Buffer controlled_buffer_13
  not not_3 (not_3_out, Itter1);
  not not_4 (not_4_out, not_3_out);
  not not_5 (not_5_out, Itter1);
  assign controlled_buffer_14_out = not_5_out ? {8{1'b0}} : 8'bz;  // Controlled_Buffer controlled_buffer_14
  assign NextAddress[15:8] = AddressInput[2] ? HighByte : 8'bz;  // Controlled_Buffer controlled_buffer_15
  or or_15 (or_15_out, or_11_out, AddressInput[2]);
  or or_16 (or_16_out, or_12_out, AddressInput[2]);
  assign controlled_buffer_16_out = not_3_out ? X : 8'bz;  // Controlled_Buffer controlled_buffer_16
  assign controlled_buffer_16_out = not_4_out ? {8{1'b0}} : 8'bz;  // Controlled_Buffer controlled_buffer_17
  and and_1 (and_1_out, AddressInput[9], Itter1);
  assign controlled_buffer_14_out = Itter1 ? HighByte : 8'bz;  // Controlled_Buffer controlled_buffer_18
  Adder adder_5 (.a(LowByte), .b(controlled_buffer_16_out), .out(adder_5_out));  // open: cin, cout
  or or_17 (or_17_out, and_1_out, or_16_out);
  assign NextAddress[7:0] = AddressInput[9] ? adder_5_out : 8'bz;  // Controlled_Buffer controlled_buffer_19
  assign NextAddress[15:8] = AddressInput[9] ? controlled_buffer_14_out : 8'bz;  // Controlled_Buffer controlled_buffer_20
  or or_18 (or_18_out, AddressInput[2], AddressInput[9]);
  assign controlled_buffer_21_out = Itter1 ? Y : 8'bz;  // Controlled_Buffer controlled_buffer_21
  not not_6 (not_6_out, Itter1);
  assign controlled_buffer_21_out = not_6_out ? {8{1'b0}} : 8'bz;  // Controlled_Buffer controlled_buffer_22
  assign controlled_buffer_23_out = Itter1 ? HighByte : 8'bz;  // Controlled_Buffer controlled_buffer_23
  not not_7 (not_7_out, Itter1);
  assign controlled_buffer_23_out = not_7_out ? {8{1'b0}} : 8'bz;  // Controlled_Buffer controlled_buffer_24
  Adder adder_6 (.a(LowByte), .b(controlled_buffer_21_out), .out(adder_6_out));  // open: cin, cout
  and and_2 (and_2_out, AddressInput[8], Itter1);
  or or_19 (or_19_out, and_2_out, or_17_out);
  and and_3 (HighByteFlag, DecodeFlag, or_19_out);
  assign NextAddress[7:0] = AddressInput[8] ? adder_6_out : 8'bz;  // Controlled_Buffer controlled_buffer_25
  assign NextAddress[15:8] = AddressInput[8] ? controlled_buffer_23_out : 8'bz;  // Controlled_Buffer controlled_buffer_26
  or or_20 (or_20_out, or_18_out, AddressInput[8]);
  D_Flip_Flop #(.trigger("falling")) d_ff_3 (
    .D(or_20_out), .clk(Clock), .Q(d_ff_3_q), .reset(Reset));  // open: Qn, preset
  or or_21 (or_21_out, Itter1, d_ff_3_q);
  not not_8 (not_8_out, ExecuteFlag);
  and and_4 (and_4_out, or_21_out, not_9_out);
  and and_5 (and_5_out, d_ff_4_q, or_15_out);
  not not_9 (not_9_out, or_15_out);
  D_Flip_Flop #(.trigger("falling")) d_ff_4 (
    .D(or_15_out), .clk(DecodeHigh), .Q(d_ff_4_q), .reset(Reset));  // open: Qn, preset
  and and_6 (PCOFFflag, not_8_out, or_22_out);
  or or_22 (or_22_out, and_4_out, and_5_out);

  // Notes on the sheet:
  //   impl
  //   rel
  //   Hash
  //   A
  //   zpg
  //   zpgX
  //   zpgY
  //   abs
  //   absX
  //   absY
  //   ind
  //   indX
  //   indY
endmodule

module TransferInstructions (
  input  [7:0] x,
  input  [7:0] y,
  input  [7:0] a,
  input  [7:0] s,
  input  [7:0] M,
  input  STA,
  input  LDA,
  input  STY,
  input  LDY,
  input  TAX,
  input  TAY,
  input  TXS,
  input  STX,
  input  LDX,
  input  TXA,
  input  TYA,
  input  TSX,
  output [7:0] out_18,
  output MWrite,
  output PCOFF,
  output XWrite,
  output YWrite,
  output AWrite,
  output SWrite,
  output TransferInstructionDone,
  output FlagFlag
);

  wire or_1_out, or_2_out, or_3_out, or_4_out, or_5_out, or_6_out, or_7_out;

  assign out_18 = STA ? a : 8'bz;  // Controlled_Buffer controlled_buffer_1
  assign out_18 = STY ? y : 8'bz;  // Controlled_Buffer controlled_buffer_2
  assign out_18 = STX ? x : 8'bz;  // Controlled_Buffer controlled_buffer_3
  or or_1 (or_1_out, STA, STY, STX);
  assign out_18 = LDA ? M : 8'bz;  // Controlled_Buffer controlled_buffer_4
  assign out_18 = LDY ? M : 8'bz;  // Controlled_Buffer controlled_buffer_5
  assign out_18 = LDX ? M : 8'bz;  // Controlled_Buffer controlled_buffer_6
  assign out_18 = TAX ? a : 8'bz;  // Controlled_Buffer controlled_buffer_7
  or or_2 (or_2_out, LDA, LDY, or_1_out, LDX);
  or or_3 (or_3_out, LDA, LDY, LDX);
  assign out_18 = TAY ? a : 8'bz;  // Controlled_Buffer controlled_buffer_8
  assign out_18 = TXA ? x : 8'bz;  // Controlled_Buffer controlled_buffer_9
  or or_4 (or_4_out, TAX, or_2_out, TXA);
  or or_5 (or_5_out, TAX, or_3_out, TXA);
  assign out_18 = TYA ? y : 8'bz;  // Controlled_Buffer controlled_buffer_10
  or or_6 (or_6_out, TAY, or_4_out, TYA);
  or or_7 (or_7_out, TAY, or_5_out, TYA);
  assign out_18 = TXS ? x : 8'bz;  // Controlled_Buffer controlled_buffer_11
  assign out_18 = TSX ? s : 8'bz;  // Controlled_Buffer controlled_buffer_12
  or or_8 (XWrite, LDX, TAX, TSX);
  or or_9 (FlagFlag, TXS, or_7_out, TSX);
  or or_10 (TransferInstructionDone, TXS, or_6_out, TSX);
  or or_11 (YWrite, LDY, TAY);
  or or_12 (AWrite, LDA, TXA, TYA);
  or or_13 (MWrite, STA, STY, STX);

  assign PCOFF = MWrite;
  assign SWrite = TXS;
endmodule

module Execute (
  input  [7:0] InstIn,
  input  [19:0] InstructionSet1,
  input  [16:0] InstructionSet2,
  input  [16:0] InstructionSet3,
  input  [7:0] LowByte,
  input  [23:0] RegisterIn,
  input  [15:0] PCin,
  input  [15:0] PCin_2,
  input  [7:0] StackIn,
  input  [6:0] StatusIn,
  input  Execute,
  input  Fetch,
  input  AMode,
  output [15:0] PCInstructionOut,
  output SWrite,
  output YWrite,
  output XWrite,
  output AWrite,
  output MWrite,
  output PWrite,
  output Stack,
  output MRead,
  output StackOverwrite,
  output KeepPCOFF,
  output PCWrite,
  output InstructionDone,
  output [7:0] InstructionOut,
  output ZNRead,
  output CRead,
  output ORead,
  output ZWrite,
  output NWrite,
  output CWrite,
  output OWrite,
  output Break,
  output ClearCarry,
  output ClearDecimal,
  output ClearInterupt,
  output ClearOverflow,
  output SetCarry,
  output SetDecimal,
  output SetInterupt
);

  wire and_10_out, and_11_out, and_12_out, and_14_out, ArithAWrite, ArithInstDone, ArithIntCarry,
       ArithIntFlag, ArithIntZero, BranchInstDone, BranchPCWrite, Break_t, FlagInstDone, IncrementInstDone,
       IncrMWrite, IncrPCOFF, IncrXWrite, IncrYWrite, InteruptInstDone, InteruptMRead, InteruptMWrite,
       InteruptOveride, InteruptPCWrite, InteruptPWrite, InteruptStack, InteruptSWrite, JumpInstDone,
       JumpMRead, JumpMWrite, JumpOveride, JumpPCWrite, JumpStack, JumpSWrite, LogAWrite, LogInstDone,
       not_1_out, not_2_out, not_3_out, not_4_out, not_5_out, not_6_out, not_7_out, not_8_out, not_9_out,
       not_10_out, or_1_out, or_2_out, or_3_out, or_4_out, or_5_out, or_6_out, or_7_out, or_8_out, or_9_out,
       or_10_out, or_11_out, or_12_out, or_13_out, or_14_out, or_15_out, or_16_out, or_17_out, or_18_out,
       or_19_out, or_21_out, or_23_out, or_24_out, or_27_out, or_28_out, or_29_out, or_30_out, or_33_out,
       or_34_out, or_35_out, or_36_out, or_37_out, or_38_out, or_39_out, or_40_out, RotAWrite, RotInstDone,
       RotIntCarry, RotMWrite, RotPCOFF, StackAWrite, StackInstDone, StackIntFlag, StackMRead, StackMWrite,
       StackOveride, StackPWrite, StackStack, StackSWrite, TransAWrite, TransferInstDone, TransferInstFlag,
       TransMWrite, TransPCOFF, TransSWrite, TransXWrite, TransYWrite;

  not not_1 (not_1_out, InstructionOut[0]);
  not not_2 (not_2_out, InstructionOut[1]);
  not not_3 (not_3_out, InstructionOut[2]);
  not not_4 (not_4_out, InstructionOut[3]);
  not not_5 (not_5_out, InstructionOut[4]);
  not not_6 (not_6_out, InstructionOut[5]);
  not not_7 (not_7_out, InstructionOut[6]);
  not not_8 (not_8_out, InstructionOut[7]);
  and and_1 (ZWrite, not_1_out, not_2_out, not_3_out, not_4_out, not_5_out, not_6_out, not_7_out, not_8_out);
  and and_2 (SWrite, or_1_out, Execute);
  or or_1 (or_1_out, TransSWrite, or_2_out);
  or or_2 (or_2_out, StackSWrite, or_3_out);
  or or_3 (or_3_out, JumpSWrite, InteruptSWrite);
  ArithmeticInstructions arithmeticinstructions_1 (
    .Y(RegisterIn[23:16]), .X(RegisterIn[15:8]), .A(RegisterIn[7:0]), .LowByte(LowByte),
    .CarryFlag(StatusIn[6]), .DecimalFlag(StatusIn[3]), .AWrite(ArithAWrite), .ADC(InstructionSet1[16]),
    .CMP(InstructionSet1[5]), .CPX(InstructionSet1[12]), .CPY(InstructionSet1[13]), .SBC(InstructionSet1[4]),
    .InstructionDone(ArithInstDone), .InstructionOutput(InstructionOut), .CarryFlag_2(ArithIntZero),
    .OverflowFlag(OWrite), .FlagFlag(ArithIntFlag));
  FlagInstructions flaginstructions_1 (
    .ClearCarry(ClearCarry), .ClearDecimal(ClearDecimal), .ClearInterupt(ClearInterupt),
    .ClearOverflow(ClearOverflow), .SetCarry(SetCarry), .SetDecimal(SetDecimal), .SetInterupt(SetInterupt),
    .CLC(InstructionSet2[2]), .CLD(InstructionSet3[12]), .CLI(InstructionSet2[10]), .CLV(InstructionSet3[7]),
    .SEC(InstructionSet2[6]), .SED(InstructionSet3[15]), .SEI(InstructionSet2[15]), .InstDone(FlagInstDone));
  // LogicalInstructions logicalinstructions_1: pin names not known; wires that end beside it: RegisterIn[7:0], LowByte, InstructionSet1[18], LogAWrite, InstructionSet1[19], InstructionSet1[17], LogInstDone, InstructionOut
  or or_4 (or_4_out, TransYWrite, IncrYWrite);
  TransferInstructions transferinstructions_1 (
    .x(RegisterIn[15:8]), .y(RegisterIn[23:16]), .a(RegisterIn[7:0]), .s(StackIn), .M(LowByte),
    .XWrite(TransXWrite), .YWrite(TransYWrite), .AWrite(TransAWrite), .SWrite(TransSWrite),
    .MWrite(TransMWrite), .PCOFF(TransPCOFF), .STA(InstructionSet1[15]), .STY(InstructionSet1[7]),
    .STX(InstructionSet1[3]), .LDA(InstructionSet1[6]), .LDY(InstructionSet1[14]), .LDX(InstructionSet1[2]),
    .TAX(InstructionSet3[6]), .TXA(InstructionSet3[1]), .TAY(InstructionSet3[5]), .TYA(InstructionSet3[2]),
    .TXS(InstructionSet3[3]), .TSX(InstructionSet3[8]), .out_18(InstructionOut),
    .TransferInstructionDone(TransferInstDone), .FlagFlag(TransferInstFlag));
  and and_3 (YWrite, or_4_out, Execute);
  and and_4 (XWrite, or_5_out, Execute);
  or or_5 (or_5_out, TransXWrite, IncrXWrite);
  and and_5 (AWrite, or_6_out, Execute);
  or or_6 (or_6_out, TransAWrite, or_7_out);
  or or_7 (or_7_out, StackAWrite, or_8_out);
  or or_8 (or_8_out, ArithAWrite, or_9_out);
  or or_9 (or_9_out, LogAWrite, RotAWrite);
  BranchInstructions branchinstructions_1 (
    .P({StatusIn, 1'b0}), .PC(PCin), .LowByte(LowByte), .PCWrite(BranchPCWrite), .BCC(InstructionSet3[4]),
    .BCS(InstructionSet3[9]), .BNE(InstructionSet3[13]), .BEQ(InstructionSet3[16]), .BPL(InstructionSet2[3]),
    .BMI(InstructionSet2[7]), .BVC(InstructionSet2[12]), .BVS(InstructionSet2[16]),
    .INSTPCOut(PCInstructionOut), .InstDone(BranchInstDone));
  IncrementInstructions incrementinstructions_1 (
    .X(RegisterIn[15:8]), .Y(RegisterIn[23:16]), .LowByte(LowByte), .XWrite(IncrXWrite), .YWrite(IncrYWrite),
    .MWrite(IncrMWrite), .PCOFF(IncrPCOFF), .DEX(InstructionSet3[11]), .DEY(InstructionSet3[0]),
    .DEC(InstructionSet1[1]), .INX(InstructionSet3[14]), .INY(InstructionSet3[10]), .INC(InstructionSet1[0]),
    .InstOut(InstructionOut), .InstDone(IncrementInstDone));
  StackInstructions stackinstructions_1 (
    .Execute(Execute), .Fetch(Fetch), .StackPointer(StackIn), .StatusRegister({StatusIn, 1'b0}),
    .Accumulator(RegisterIn[7:0]), .StackStack(StackStack), .Swrite(StackSWrite),
    .StackOveride(StackOveride), .MWrite(StackMWrite), .MRead(StackMRead), .AWrite(StackAWrite),
    .StatusWrite(StackPWrite), .PHA(InstructionSet2[9]), .PHP(InstructionSet2[1]), .PLA(InstructionSet2[14]),
    .PLP(InstructionSet2[5]), .InstDone(StackInstDone), .InstructionOut(InstructionOut),
    .FlagFlag(StackIntFlag));
  and and_6 (MWrite, or_10_out, Execute);
  or or_10 (or_10_out, TransMWrite, or_11_out);
  or or_11 (or_11_out, StackMWrite, or_12_out);
  or or_12 (or_12_out, IncrMWrite, or_13_out);
  or or_13 (or_13_out, RotMWrite, or_14_out);
  or or_14 (or_14_out, JumpMWrite, InteruptMWrite);
  and and_7 (PWrite, or_15_out, Execute);
  or or_15 (or_15_out, StackPWrite, InteruptPWrite);
  RotationInstruction rotationinstruction_1 (
    .AccumulatorTrigger(AMode), .A(RegisterIn[7:0]), .LowByte(LowByte), .Carry(StatusIn[0]),
    .AWrite(RotAWrite), .MWrite(RotMWrite), .PCOFF(RotPCOFF), .ASL(InstructionSet1[11]),
    .ROL(InstructionSet1[10]), .LSR(InstructionSet1[9]), .ROR(InstructionSet1[8]), .InstDone(RotInstDone),
    .InstructionOut(InstructionOut), .CarryFlag(RotIntCarry));
  and and_8 (Stack, or_16_out, Execute);
  or or_16 (or_16_out, StackStack, or_17_out);
  or or_17 (or_17_out, JumpStack, InteruptStack);
  JumpInstructions jumpinstructions_1 (
    .Execute(Execute), .Fetch(Fetch), .PCALT(PCin_2), .PC(PCin), .StackPointer(StackIn), .InstIn(InstIn),
    .StackStack(JumpStack), .SWrite(JumpSWrite), .MWrite(JumpMWrite), .StackOveride(JumpOveride),
    .MRead(JumpMRead), .PCWrite(JumpPCWrite), .JMP(InstructionSet2[11]), .JSR(InstructionSet2[4]),
    .RTS(InstructionSet2[13]), .InstDone(JumpInstDone), .PCinstOut(PCInstructionOut),
    .PCinstOut_2(InstructionOut));
  and and_9 (MRead, or_18_out, Execute);
  or or_18 (or_18_out, StackMRead, or_19_out);
  or or_19 (or_19_out, JumpMRead, InteruptMRead);
  InteruptInstructions interuptinstructions_1 (
    .Execute(Execute), .Fetch(Fetch), .PC(PCin), .P({StatusIn, 1'b0}), .StackPointer(StackIn),
    .InstIn(InstIn), .StackStack(InteruptStack), .SWrite(InteruptSWrite), .MWrite(InteruptMWrite),
    .StackOveride(InteruptOveride), .MRead(InteruptMRead), .PWrite(InteruptPWrite),
    .PCWrite(InteruptPCWrite), .Break(Break_t), .BRK(InstructionSet2[0]), .RTI(InstructionSet2[8]),
    .InstDone(InteruptInstDone), .InstOut(InstructionOut), .PCinstOut(PCInstructionOut));
  or or_20 (StackOverwrite, StackOveride, or_21_out);
  or or_21 (or_21_out, JumpOveride, InteruptOveride);
  or or_22 (KeepPCOFF, TransPCOFF, or_23_out);
  or or_23 (or_23_out, IncrPCOFF, or_24_out);
  buf or_24 (or_24_out, RotPCOFF);  // OR_Gate
  and and_10 (and_10_out, ArithInstDone, not_9_out);
  not not_9 (not_9_out, StatusIn[3]);
  and and_11 (and_11_out, TransferInstDone, TransferInstFlag);
  and and_12 (and_12_out, StackInstDone, StackIntFlag);
  or or_25 (CRead, and_10_out, RotInstDone);
  and and_13 (ORead, and_10_out, ArithIntFlag);
  or or_26 (CWrite, RotIntCarry, and_14_out);
  and and_14 (and_14_out, ArithInstDone, ArithIntCarry);
  not not_10 (not_10_out, StatusIn[3]);
  and and_15 (PCWrite, or_27_out, Execute);
  or or_27 (or_27_out, BranchPCWrite, or_28_out);
  or or_28 (or_28_out, JumpPCWrite, InteruptPCWrite);
  or or_29 (or_29_out, and_11_out, LogInstDone, and_12_out);
  or or_30 (or_30_out, IncrementInstDone, RotInstDone, and_10_out);
  and and_16 (Break, Break_t, not_10_out);
  or or_31 (ZNRead, or_29_out, or_30_out);
  or or_32 (InstructionDone, TransferInstDone, or_33_out);
  or or_33 (or_33_out, StackInstDone, or_34_out);
  or or_34 (or_34_out, IncrementInstDone, or_35_out);
  or or_35 (or_35_out, ArithInstDone, or_36_out);
  or or_36 (or_36_out, LogInstDone, or_37_out);
  or or_37 (or_37_out, RotInstDone, or_38_out);
  or or_38 (or_38_out, BranchInstDone, or_39_out);
  or or_39 (or_39_out, JumpInstDone, or_40_out);
  or or_40 (or_40_out, InteruptInstDone, FlagInstDone);

  assign NWrite = InstructionOut[7];

  // Other names for the same wires on the sheet: ArithIntOverflow = OWrite; BranchInstOut[15:0] = PCInstructionOut;
  //   InterupPCtInstOut[15:0] = PCInstructionOut; JumpPCInstOut[15:0] = PCInstructionOut; PAltCout[15:0] = PCin_2;
  //   PCout[15:0] = PCin; Pout[7:1] = StatusIn; RegOut[23:0] = RegisterIn; Sout[7:0] = StackIn;
  //   ArithInstOut[7:0] = InstructionOut; IncrementInstOut[7:0] = InstructionOut;
  //   InteruptInstOut[7:0] = InstructionOut; JumpInstOut[7:0] = InstructionOut; LogInstOut[7:0] = InstructionOut;
  //   RotInstOut[7:0] = InstructionOut; StackInstOut[7:0] = InstructionOut; TransferInstOut[7:0] = InstructionOut;
  //   Negative = InstructionOut[7]; Zero = ZWrite
endmodule

module ProcessorStatusRegister (
  input  [6:0] Pin,
  input  RegsiterInput,
  input  Execute,
  input  Clear,
  input  BreakOff,
  input  ClearOverflow,
  input  Overflow,
  input  Negative,
  input  OverflowRead,
  input  NegativeRead,
  input  Zero,
  input  InteruptOn,
  input  InteruptOff,
  input  DecimalOn,
  input  DecimalOff,
  input  CarryOff,
  input  BreakOn,
  input  Carry,
  input  CarryOn,
  input  ZeroRead,
  input  CarryRead,
  output Carry_2,
  output Zero_2,
  output Interupt,
  output Decimal,
  output Break,
  output Overflow_2,
  output Negative_2
);

  wire and_1_out, and_2_out, and_3_out, and_4_out, and_5_out, and_6_out, and_7_out, and_8_out, and_9_out,
       and_10_out, and_11_out, and_12_out, and_13_out, and_14_out, and_15_out, and_16_out, and_17_out,
       and_18_out, and_19_out, and_20_out, and_21_out, and_22_out, and_23_out, and_24_out, and_25_out,
       and_26_out, and_27_out, and_28_out, and_29_out, and_30_out, and_31_out, and_32_out, and_33_out,
       and_34_out, and_35_out, and_36_out, and_37_out, and_38_out, and_39_out, and_40_out, and_41_out,
       and_42_out, and_43_out, not_1_out, not_2_out, not_3_out, not_4_out, not_5_out, not_6_out, not_7_out,
       not_8_out, not_9_out, not_10_out, not_11_out, not_12_out, not_13_out, not_14_out, not_15_out,
       not_16_out, not_17_out, not_18_out, or_1_out, or_2_out, or_3_out, or_4_out, or_5_out, or_6_out,
       or_7_out, or_8_out, or_9_out, or_10_out, or_11_out, or_12_out, or_13_out, or_14_out, or_15_out,
       or_16_out, or_17_out, or_18_out, or_19_out, or_20_out;

  not not_1 (not_1_out, RegsiterInput);
  or or_1 (or_1_out, CarryOn, Carry);
  not not_2 (not_2_out, RegsiterInput);
  or or_2 (or_2_out, CarryOn, CarryRead);
  and and_1 (and_1_out, RegsiterInput, Pin[6]);
  or or_3 (or_3_out, and_1_out, and_2_out);
  and and_2 (and_2_out, not_1_out, or_1_out);
  and and_3 (and_3_out, RegsiterInput, Pin[6]);
  and and_4 (and_4_out, not_2_out, or_2_out);
  D_Flip_Flop #(.trigger("falling")) d_ff_1 (
    .D(or_3_out), .clk(and_5_out), .Q(Carry_2), .reset(or_4_out));  // open: Qn, preset
  and and_5 (and_5_out, or_5_out, Execute);
  or or_4 (or_4_out, and_6_out, Clear);
  and and_6 (and_6_out, Execute, and_7_out);
  or or_5 (or_5_out, and_3_out, and_4_out);
  and and_7 (and_7_out, not_3_out, CarryOff);
  not not_3 (not_3_out, RegsiterInput);
  not not_4 (not_4_out, RegsiterInput);
  not not_5 (not_5_out, RegsiterInput);
  and and_8 (and_8_out, RegsiterInput, Pin[5]);
  and and_9 (and_9_out, not_4_out, Zero);
  and and_10 (and_10_out, RegsiterInput, Pin[5]);
  and and_11 (and_11_out, not_5_out, ZeroRead);
  or or_6 (or_6_out, and_8_out, and_9_out);
  D_Flip_Flop #(.trigger("falling")) d_ff_2 (
    .D(or_6_out), .clk(and_12_out), .Q(Zero_2), .reset(Clear));  // open: Qn, preset
  and and_12 (and_12_out, or_7_out, Execute);
  or or_7 (or_7_out, and_10_out, and_11_out);
  not not_6 (not_6_out, RegsiterInput);
  not not_7 (not_7_out, RegsiterInput);
  and and_13 (and_13_out, RegsiterInput, Pin[4]);
  and and_14 (and_14_out, not_6_out, InteruptOn);
  and and_15 (and_15_out, RegsiterInput, Pin[4]);
  and and_16 (and_16_out, not_7_out, InteruptOn);
  or or_8 (or_8_out, and_13_out, and_14_out);
  D_Flip_Flop #(.trigger("falling")) d_ff_3 (
    .D(or_8_out), .clk(and_17_out), .Q(Interupt), .reset(or_9_out));  // open: Qn, preset
  and and_17 (and_17_out, or_10_out, Execute);
  or or_9 (or_9_out, and_18_out, Clear);
  and and_18 (and_18_out, Execute, and_19_out);
  or or_10 (or_10_out, and_15_out, and_16_out);
  and and_19 (and_19_out, not_8_out, InteruptOff);
  not not_8 (not_8_out, RegsiterInput);
  not not_9 (not_9_out, RegsiterInput);
  not not_10 (not_10_out, RegsiterInput);
  and and_20 (and_20_out, RegsiterInput, Pin[3]);
  and and_21 (and_21_out, not_9_out, DecimalOn);
  and and_22 (and_22_out, RegsiterInput, Pin[3]);
  and and_23 (and_23_out, not_10_out, DecimalOn);
  or or_11 (or_11_out, and_20_out, and_21_out);
  D_Flip_Flop #(.trigger("falling")) d_ff_4 (
    .D(or_11_out), .clk(and_24_out), .Q(Decimal), .reset(or_12_out));  // open: Qn, preset
  and and_24 (and_24_out, or_13_out, Execute);
  or or_12 (or_12_out, and_25_out, Clear);
  and and_25 (and_25_out, Execute, and_26_out);
  or or_13 (or_13_out, and_22_out, and_23_out);
  and and_26 (and_26_out, not_11_out, DecimalOff);
  not not_11 (not_11_out, RegsiterInput);
  not not_12 (not_12_out, RegsiterInput);
  not not_13 (not_13_out, RegsiterInput);
  and and_27 (and_27_out, RegsiterInput, Pin[2]);
  or or_14 (or_14_out, and_27_out, and_28_out);
  and and_28 (and_28_out, not_12_out, BreakOn);
  and and_29 (and_29_out, RegsiterInput, Pin[2]);
  or or_15 (or_15_out, and_29_out, and_30_out);
  and and_30 (and_30_out, not_13_out, BreakOn);
  D_Flip_Flop #(.trigger("falling")) d_ff_5 (
    .D(or_14_out), .clk(and_31_out), .Q(Break), .reset(BreakOff));  // open: Qn, preset
  and and_31 (and_31_out, or_15_out, Execute);
  not not_14 (not_14_out, RegsiterInput);
  not not_15 (not_15_out, RegsiterInput);
  and and_32 (and_32_out, RegsiterInput, Pin[1]);
  or or_16 (or_16_out, and_32_out, and_33_out);
  and and_33 (and_33_out, not_14_out, Overflow);
  and and_34 (and_34_out, or_17_out, Execute);
  and and_35 (and_35_out, RegsiterInput, Pin[1]);
  or or_17 (or_17_out, and_35_out, and_36_out);
  and and_36 (and_36_out, not_15_out, OverflowRead);
  D_Flip_Flop #(.trigger("falling")) d_ff_6 (
    .D(or_16_out), .clk(and_34_out), .Q(Overflow_2), .reset(or_18_out));  // open: Qn, preset
  or or_18 (or_18_out, and_37_out, Clear);
  and and_37 (and_37_out, Execute, and_38_out);
  and and_38 (and_38_out, not_16_out, ClearOverflow);
  not not_16 (not_16_out, RegsiterInput);
  not not_17 (not_17_out, RegsiterInput);
  not not_18 (not_18_out, RegsiterInput);
  and and_39 (and_39_out, RegsiterInput, Pin[0]);
  or or_19 (or_19_out, and_39_out, and_40_out);
  and and_40 (and_40_out, not_17_out, Negative);
  and and_41 (and_41_out, or_20_out, Execute);
  and and_42 (and_42_out, RegsiterInput, Pin[0]);
  or or_20 (or_20_out, and_42_out, and_43_out);
  and and_43 (and_43_out, not_18_out, NegativeRead);
  D_Flip_Flop #(.trigger("falling")) d_ff_7 (
    .D(or_19_out), .clk(and_41_out), .Q(Negative_2), .reset(Clear));  // open: Qn, preset
endmodule

module StackInstructions (
  input  Execute,
  input  Fetch,
  input  [7:0] StackPointer,
  input  [7:0] StatusRegister,
  input  [7:0] Accumulator,
  input  PHA,
  input  PHP,
  input  PLA,
  input  PLP,
  output StackStack,
  output Swrite,
  output StackOveride,
  output MWrite,
  output MRead,
  output AWrite,
  output StatusWrite,
  output InstDone,
  output [7:0] InstructionOut,
  output FlagFlag
);

  wire and_1_out, and_2_out, and_3_out, and_4_out, and_5_out, and_6_out, and_7_out, and_8_out, and_9_out,
       and_10_out, and_11_out, and_12_out, and_13_out, and_14_out, and_16_out, and_17_out, d_ff_1_q,
       not_1_out, not_2_out, not_3_out, not_4_out, or_3_out, or_4_out, or_5_out, or_6_out, or_7_out;
  wire [7:0] adder_1_out, subtractor_1_out;

  and and_1 (and_1_out, and_2_out, not_1_out);
  and and_2 (and_2_out, or_3_out, or_4_out);
  D_Flip_Flop #(.trigger("falling")) d_ff_1 (
    .D(or_4_out), .clk(Execute), .Q(d_ff_1_q), .reset(Fetch));  // open: Qn, preset
  or or_1 (StackStack, and_1_out, and_11_out);
  and and_3 (and_3_out, and_4_out, not_1_out);
  and and_4 (and_4_out, or_6_out, or_4_out);
  not not_1 (not_1_out, d_ff_1_q);
  not not_2 (not_2_out, d_ff_1_q);
  Subtractor subtractor_1 (.a(StackPointer), .b(8'h1), .out(subtractor_1_out));  // open: bin, bout
  and and_5 (and_5_out, or_3_out, and_7_out);
  assign InstructionOut = and_5_out ? StackPointer : 8'bz;  // Controlled_Buffer controlled_buffer_1
  and and_6 (and_6_out, or_3_out, d_ff_1_q);
  and and_7 (and_7_out, not_2_out, not_4_out);
  and and_8 (and_8_out, and_7_out, or_6_out);
  assign InstructionOut = and_8_out ? subtractor_1_out : 8'bz;  // Controlled_Buffer controlled_buffer_2
  or or_2 (Swrite, and_9_out, and_3_out);
  and and_9 (and_9_out, and_6_out, not_3_out);
  and and_10 (and_10_out, or_6_out, d_ff_1_q);
  and and_11 (and_11_out, and_10_out, not_3_out);
  Adder adder_1 (.a(StackPointer), .b(8'h1), .out(adder_1_out));  // open: cin, cout
  not not_3 (not_3_out, InstDone);
  D_Flip_Flop #(.trigger("falling")) d_ff_2 (
    .D(d_ff_1_q), .clk(Execute), .Q(InstDone), .reset(Fetch));  // open: Qn, preset
  not not_4 (not_4_out, InstDone);
  and and_12 (and_12_out, d_ff_1_q, not_4_out);
  and and_13 (and_13_out, or_3_out, and_12_out);
  assign InstructionOut = and_13_out ? adder_1_out : 8'bz;  // Controlled_Buffer controlled_buffer_3
  and and_14 (and_14_out, and_12_out, or_6_out);
  assign InstructionOut = and_14_out ? StackPointer : 8'bz;  // Controlled_Buffer controlled_buffer_4
  and and_15 (MWrite, InstDone, or_3_out);
  or or_3 (or_3_out, PHP, PHA);
  or or_4 (or_4_out, or_5_out, PHA);
  assign InstructionOut = and_16_out ? Accumulator : 8'bz;  // Controlled_Buffer controlled_buffer_5
  and and_16 (and_16_out, PHA, InstDone);
  or or_5 (or_5_out, or_7_out, PHP);
  assign InstructionOut = and_17_out ? StatusRegister : 8'bz;  // Controlled_Buffer controlled_buffer_6
  and and_17 (and_17_out, PHP, InstDone);
  and and_18 (MRead, or_6_out, InstDone);
  or or_6 (or_6_out, PLP, PLA);
  or or_7 (or_7_out, PLP, PLA);
  and and_19 (AWrite, PLA, InstDone);
  and and_20 (StatusWrite, PLP, InstDone);

  assign FlagFlag = PLA;
  assign StackOveride = InstDone;
endmodule

module IncrementInstructions (
  input  [7:0] X,
  input  [7:0] Y,
  input  [7:0] LowByte,
  input  INX,
  input  INY,
  input  INC,
  input  DEX,
  input  DEY,
  input  DEC,
  output XWrite,
  output YWrite,
  output MWrite,
  output PCOFF,
  output [7:0] InstOut,
  output InstDone
);

  wire or_3_out, or_4_out, or_6_out, or_7_out, or_8_out, or_9_out, or_10_out, or_12_out;
  wire [7:0] adder_1_out, controlled_buffer_1_out, controlled_buffer_5_out, subtractor_1_out;

  or or_1 (XWrite, DEX, INX);
  assign controlled_buffer_1_out = DEX ? X : 8'bz;  // Controlled_Buffer controlled_buffer_1
  assign controlled_buffer_1_out = DEY ? Y : 8'bz;  // Controlled_Buffer controlled_buffer_2
  or or_2 (YWrite, DEY, INY);
  assign controlled_buffer_1_out = DEC ? LowByte : 8'bz;  // Controlled_Buffer controlled_buffer_3
  or or_3 (or_3_out, DEX, DEY);
  or or_4 (or_4_out, DEX, DEY);
  or or_5 (MWrite, DEC, INC);
  or or_6 (or_6_out, or_3_out, DEC);
  or or_7 (or_7_out, or_4_out, DEC);
  Subtractor subtractor_1 (.a(controlled_buffer_1_out), .b(8'h1), .out(subtractor_1_out));  // open: bin, bout
  assign InstOut = or_7_out ? subtractor_1_out : 8'bz;  // Controlled_Buffer controlled_buffer_4
  assign controlled_buffer_5_out = INX ? X : 8'bz;  // Controlled_Buffer controlled_buffer_5
  or or_8 (or_8_out, or_6_out, INX);
  assign controlled_buffer_5_out = INY ? Y : 8'bz;  // Controlled_Buffer controlled_buffer_6
  assign controlled_buffer_5_out = INC ? LowByte : 8'bz;  // Controlled_Buffer controlled_buffer_7
  or or_9 (or_9_out, or_8_out, INY);
  or or_10 (or_10_out, INX, INY);
  or or_11 (InstDone, or_9_out, INC);
  or or_12 (or_12_out, or_10_out, INC);
  Adder adder_1 (.a(controlled_buffer_5_out), .b(8'h1), .out(adder_1_out));  // open: cin, cout
  assign InstOut = or_12_out ? adder_1_out : 8'bz;  // Controlled_Buffer controlled_buffer_8

  assign PCOFF = MWrite;
endmodule

module ArithmeticInstructions (
  input  [7:0] Y,
  input  [7:0] X,
  input  [7:0] A,
  input  [7:0] LowByte,
  input  CarryFlag,
  input  DecimalFlag,
  input  ADC,
  input  CMP,
  input  CPX,
  input  CPY,
  input  SBC,
  output AWrite,
  output InstructionDone,
  output [7:0] InstructionOutput,
  output CarryFlag_2,
  output OverflowFlag,
  output FlagFlag
);

  wire adder_1_cout, adder_2_cout, adder_3_cout, and_1_out, and_2_out, and_3_out, and_4_out, not_1_out,
       not_2_out, not_3_out, not_4_out, not_5_out, not_6_out, not_7_out, not_8_out, not_9_out, not_10_out,
       not_11_out, not_12_out, not_13_out, or_1_out, or_2_out, or_3_out, or_4_out, or_5_out, or_6_out,
       or_8_out, subtractor_1_bout, subtractor_2_bout, subtractor_3_bout, subtractor_4_bout,
       subtractor_5_bout, subtractor_6_bout, subtractor_7_bout, subtractor_8_bout, subtractor_9_bout;
  wire [3:0] adder_2_out, adder_3_out, controlled_buffer_1_out, controlled_buffer_2_out,
       controlled_buffer_12_out, controlled_buffer_13_out, controlled_buffer_14_out,
       controlled_buffer_15_out, controlled_buffer_21_out, controlled_buffer_23_out, subtractor_1_out,
       subtractor_2_out, subtractor_4_out, subtractor_5_out, subtractor_6_out, subtractor_7_out,
       subtractor_8_out, subtractor_9_out, subtractor_10_out, subtractor_11_out;
  wire [7:0] adder_1_out, controlled_buffer_3_out, controlled_buffer_8_out, controlled_buffer_20_out,
       subtractor_3_out;

  and and_1 (and_1_out, ADC, CarryFlag);
  Adder adder_1 (.a(A), .b(LowByte), .out(adder_1_out), .cin(and_1_out), .cout(adder_1_cout));
  and and_2 (and_2_out, ADC, CarryFlag);
  Adder #(.width(4)) adder_2 (.a(A[3:0]), .b(LowByte[3:0]), .out(adder_2_out), .cin(and_2_out), .cout(adder_2_cout));
  not not_1 (not_1_out, subtractor_1_bout);
  or or_1 (or_1_out, adder_2_cout, not_1_out);
  Adder #(.width(4)) adder_3 (.a(A[7:4]), .b(LowByte[7:4]), .out(adder_3_out), .cin(or_1_out), .cout(adder_3_cout));
  or or_2 (or_2_out, adder_3_cout, adder_1_cout);
  not not_2 (not_2_out, CarryFlag);
  assign controlled_buffer_1_out = not_3_out ? subtractor_1_out : 4'bz;  // Controlled_Buffer controlled_buffer_1
  Subtractor #(.width(4)) subtractor_1 (
    .a(adder_2_out), .b(4'b1010), .out(subtractor_1_out), .bout(subtractor_1_bout));  // open: bin
  not not_3 (not_3_out, subtractor_1_bout);
  assign controlled_buffer_2_out = not_4_out ? subtractor_2_out : 4'bz;  // Controlled_Buffer controlled_buffer_2
  Subtractor #(.width(4)) subtractor_2 (
    .a(adder_3_out), .b(4'b1010), .out(subtractor_2_out), .bout(subtractor_2_bout));  // open: bin
  not not_4 (not_4_out, subtractor_2_bout);
  not not_5 (not_5_out, DecimalFlag);
  assign controlled_buffer_3_out = not_5_out ? adder_1_out : 8'bz;  // Controlled_Buffer controlled_buffer_3
  assign controlled_buffer_1_out = subtractor_1_bout ? adder_2_out : 4'bz;  // Controlled_Buffer controlled_buffer_4
  assign controlled_buffer_2_out = subtractor_2_bout ? adder_3_out : 4'bz;  // Controlled_Buffer controlled_buffer_5
  assign InstructionOutput = ADC ? controlled_buffer_3_out : 8'bz;  // Controlled_Buffer controlled_buffer_6
  assign controlled_buffer_3_out = DecimalFlag ? {controlled_buffer_2_out, controlled_buffer_1_out} : 8'bz;  // Controlled_Buffer controlled_buffer_7
  assign controlled_buffer_8_out = SBC ? A : 8'bz;  // Controlled_Buffer controlled_buffer_8
  assign controlled_buffer_8_out = CMP ? A : 8'bz;  // Controlled_Buffer controlled_buffer_9
  assign controlled_buffer_8_out = CPX ? X : 8'bz;  // Controlled_Buffer controlled_buffer_10
  or or_3 (or_3_out, CMP, CPX);
  assign controlled_buffer_8_out = CPY ? Y : 8'bz;  // Controlled_Buffer controlled_buffer_11
  or or_4 (or_4_out, or_3_out, CPY);
  and and_3 (and_3_out, SBC, not_2_out);
  Subtractor subtractor_3 (
    .a(controlled_buffer_8_out), .b(LowByte), .out(subtractor_3_out), .bin(and_3_out),
    .bout(subtractor_3_bout));
  or or_5 (or_5_out, subtractor_3_bout, or_2_out);
  and and_4 (and_4_out, SBC, not_2_out);
  Subtractor #(.width(4)) subtractor_4 (
    .a(A[3:0]), .b(LowByte[3:0]), .out(subtractor_4_out), .bin(and_4_out), .bout(subtractor_4_bout));
  or or_6 (or_6_out, subtractor_4_bout, subtractor_3_bout);
  not not_6 (not_6_out, subtractor_6_bout);
  or or_7 (AWrite, ADC, SBC);
  or or_8 (or_8_out, not_6_out, or_6_out);
  Subtractor #(.width(4)) subtractor_5 (
    .a(A[7:4]), .b(LowByte[7:4]), .out(subtractor_5_out), .bin(or_8_out), .bout(subtractor_5_bout));
  or or_9 (CarryFlag_2, subtractor_5_bout, or_5_out);
  or or_10 (InstructionDone, AWrite, or_4_out);
  Subtractor #(.width(4)) subtractor_6 (
    .a(subtractor_4_out), .b(4'b1010), .out(subtractor_6_out), .bout(subtractor_6_bout));  // open: bin
  assign controlled_buffer_12_out = not_7_out ? subtractor_6_out : 4'bz;  // Controlled_Buffer controlled_buffer_12
  not not_7 (not_7_out, subtractor_6_bout);
  assign controlled_buffer_13_out = not_8_out ? subtractor_7_out : 4'bz;  // Controlled_Buffer controlled_buffer_13
  Subtractor #(.width(4)) subtractor_7 (
    .a(subtractor_4_out), .b(4'b0110), .out(subtractor_7_out), .bout(subtractor_7_bout));  // open: bin
  not not_8 (not_8_out, subtractor_7_bout);
  assign controlled_buffer_14_out = not_9_out ? subtractor_8_out : 4'bz;  // Controlled_Buffer controlled_buffer_14
  Subtractor #(.width(4)) subtractor_8 (
    .a(subtractor_5_out), .b(4'b1010), .out(subtractor_8_out), .bout(subtractor_8_bout));  // open: bin
  not not_9 (not_9_out, subtractor_8_bout);
  assign controlled_buffer_15_out = not_10_out ? subtractor_9_out : 4'bz;  // Controlled_Buffer controlled_buffer_15
  Subtractor #(.width(4)) subtractor_9 (
    .a(subtractor_5_out), .b(4'b0110), .out(subtractor_9_out), .bout(subtractor_9_bout));  // open: bin
  not not_10 (not_10_out, subtractor_9_bout);
  assign controlled_buffer_12_out = subtractor_6_bout ? subtractor_4_out : 4'bz;  // Controlled_Buffer controlled_buffer_16
  assign controlled_buffer_13_out = subtractor_7_bout ? subtractor_10_out : 4'bz;  // Controlled_Buffer controlled_buffer_17
  Subtractor #(.width(4)) subtractor_10 (
    .a(subtractor_4_out), .b(4'b1010), .out(subtractor_10_out));  // open: bin, bout
  assign controlled_buffer_14_out = subtractor_8_bout ? subtractor_5_out : 4'bz;  // Controlled_Buffer controlled_buffer_18
  assign controlled_buffer_15_out = subtractor_9_bout ? subtractor_11_out : 4'bz;  // Controlled_Buffer controlled_buffer_19
  Subtractor #(.width(4)) subtractor_11 (
    .a(subtractor_5_out), .b(4'b1010), .out(subtractor_11_out));  // open: bin, bout
  not not_11 (not_11_out, DecimalFlag);
  assign controlled_buffer_20_out = not_11_out ? subtractor_3_out : 8'bz;  // Controlled_Buffer controlled_buffer_20
  assign controlled_buffer_21_out = not_12_out ? controlled_buffer_12_out : 4'bz;  // Controlled_Buffer controlled_buffer_21
  not not_12 (not_12_out, or_6_out);
  assign controlled_buffer_21_out = or_6_out ? controlled_buffer_13_out : 4'bz;  // Controlled_Buffer controlled_buffer_22
  assign controlled_buffer_23_out = not_13_out ? controlled_buffer_14_out : 4'bz;  // Controlled_Buffer controlled_buffer_23
  not not_13 (not_13_out, subtractor_5_bout);
  assign controlled_buffer_23_out = subtractor_5_bout ? controlled_buffer_15_out : 4'bz;  // Controlled_Buffer controlled_buffer_24
  assign InstructionOutput = SBC ? controlled_buffer_20_out : 8'bz;  // Controlled_Buffer controlled_buffer_25
  assign controlled_buffer_20_out = DecimalFlag ? {controlled_buffer_23_out, controlled_buffer_21_out} : 8'bz;  // Controlled_Buffer controlled_buffer_26
  or or_11 (FlagFlag, ADC, SBC);
  assign InstructionOutput = or_4_out ? controlled_buffer_20_out : 8'bz;  // Controlled_Buffer controlled_buffer_27
  xor xor_1 (OverflowFlag, LowByte[0], InstructionOutput[7]);
endmodule

module LogicalInstructions (
  input  [7:0] Lowbyte,
  input  [7:0] A,
  input  AND,
  input  ORA,
  input  EOR,
  output AWrite,
  output InstructionDone,
  output [7:0] InstructionOut
);

  wire or_2_out;
  wire [7:0] and_1_out, or_1_out, xor_1_out;

  assign and_1_out = Lowbyte & A;  // AND_Gate and_1, 8 bits wide
  assign InstructionOut = AND ? and_1_out : 8'bz;  // Controlled_Buffer controlled_buffer_1
  assign or_1_out = Lowbyte | A;  // OR_Gate or_1, 8 bits wide
  assign InstructionOut = ORA ? or_1_out : 8'bz;  // Controlled_Buffer controlled_buffer_2
  assign xor_1_out = Lowbyte ^ A;  // XOR_Gate xor_1, 8 bits wide
  assign InstructionOut = EOR ? xor_1_out : 8'bz;  // Controlled_Buffer controlled_buffer_3
  or or_2 (or_2_out, AND, ORA);
  or or_3 (AWrite, or_2_out, EOR);

  assign InstructionDone = AWrite;
endmodule

module RotationInstruction (
  input  AccumulatorTrigger,
  input  [7:0] A,
  input  [7:0] LowByte,
  input  Carry,
  input  ASL,
  input  ROL,
  input  LSR,
  input  ROR,
  output AWrite,
  output MWrite,
  output PCOFF,
  output InstDone,
  output [7:0] InstructionOut,
  output CarryFlag
);

  wire and_1_out, and_2_out, and_3_out, and_4_out, and_5_out, and_7_out, not_1_out, not_2_out, or_2_out,
       or_3_out, or_5_out, or_7_out;
  wire [0:0] or_1_out;
  wire [7:0] controlled_buffer_1_out;
  wire [7:7] or_4_out;

  assign controlled_buffer_1_out = AccumulatorTrigger ? A : 8'bz;  // Controlled_Buffer controlled_buffer_1
  not not_1 (not_1_out, AccumulatorTrigger);
  assign controlled_buffer_1_out = not_1_out ? LowByte : 8'bz;  // Controlled_Buffer controlled_buffer_2
  and and_1 (and_1_out, 1'b0, ASL);
  and and_2 (and_2_out, Carry, ROL);
  or or_1 (or_1_out[0], and_1_out, and_2_out);
  or or_2 (or_2_out, ROL, ASL);
  assign InstructionOut = or_3_out ? {controlled_buffer_1_out[6:0], or_1_out[0]} : 8'bz;  // Controlled_Buffer controlled_buffer_3
  and and_3 (and_3_out, controlled_buffer_1_out[7], or_3_out);
  or or_3 (or_3_out, ROL, ASL);
  and and_4 (and_4_out, Carry, ROR);
  and and_5 (and_5_out, 1'b0, LSR);
  or or_4 (or_4_out[7], and_5_out, and_4_out);
  or or_5 (or_5_out, or_2_out, LSR);
  or or_6 (InstDone, or_5_out, ROR);
  or or_7 (or_7_out, ROR, LSR);
  and and_6 (AWrite, AccumulatorTrigger, InstDone);
  assign InstructionOut = or_7_out ? {or_4_out[7], controlled_buffer_1_out[7:1]} : 8'bz;  // Controlled_Buffer controlled_buffer_4
  and and_7 (and_7_out, controlled_buffer_1_out[0], or_7_out);
  or or_8 (CarryFlag, and_3_out, and_7_out);
  and and_8 (MWrite, not_2_out, InstDone);
  not not_2 (not_2_out, AccumulatorTrigger);

  assign PCOFF = MWrite;
endmodule

module FlagInstructions (
  input  CLC,
  input  CLD,
  input  CLI,
  input  CLV,
  input  SEC,
  input  SED,
  input  SEI,
  output ClearCarry,
  output ClearDecimal,
  output ClearInterupt,
  output ClearOverflow,
  output SetCarry,
  output SetDecimal,
  output SetInterupt,
  output InstDone
);

  wire or_1_out, or_2_out, or_3_out, or_4_out, or_5_out;

  or or_1 (or_1_out, CLC, CLD);
  or or_2 (or_2_out, or_1_out, CLI);
  or or_3 (or_3_out, or_2_out, CLV);
  or or_4 (or_4_out, or_3_out, SEC);
  or or_5 (or_5_out, or_4_out, SED);
  or or_6 (InstDone, or_5_out, SEI);

  assign ClearCarry = CLC;
  assign ClearDecimal = CLD;
  assign ClearInterupt = CLI;
  assign ClearOverflow = CLV;
  assign SetCarry = SEC;
  assign SetDecimal = SED;
  assign SetInterupt = SEI;
endmodule

module BranchInstructions (
  input  [7:0] P,
  input  [15:0] PC,
  input  [7:0] LowByte,
  input  BCC,
  input  BCS,
  input  BNE,
  input  BEQ,
  input  BPL,
  input  BMI,
  input  BVC,
  input  BVS,
  output PCWrite,
  output [15:0] INSTPCOut,
  output InstDone
);

  wire and_1_out, and_2_out, and_3_out, and_4_out, and_5_out, and_6_out, and_7_out, and_8_out, not_1_out,
       not_2_out, not_3_out, not_4_out, or_1_out, or_2_out, or_3_out, or_4_out, or_5_out, or_6_out, or_7_out,
       or_8_out, or_9_out, or_10_out, or_11_out, or_12_out;
  wire [15:0] controlled_buffer_1_out, controlled_buffer_9_out;

  not not_1 (not_1_out, P[7]);
  and and_1 (and_1_out, not_1_out, BCC);
  assign controlled_buffer_1_out = and_1_out ? PC : 16'bz;  // Controlled_Buffer controlled_buffer_1
  and and_2 (and_2_out, P[7], BCS);
  assign controlled_buffer_1_out = and_2_out ? PC : 16'bz;  // Controlled_Buffer controlled_buffer_2
  or or_1 (or_1_out, BCC, BCS);
  not not_2 (not_2_out, P[6]);
  and and_3 (and_3_out, not_2_out, BNE);
  or or_2 (or_2_out, and_2_out, and_1_out);
  assign controlled_buffer_1_out = and_3_out ? PC : 16'bz;  // Controlled_Buffer controlled_buffer_3
  or or_3 (or_3_out, or_1_out, BNE);
  and and_4 (and_4_out, P[6], BEQ);
  or or_4 (or_4_out, or_2_out, and_3_out);
  assign controlled_buffer_1_out = and_4_out ? PC : 16'bz;  // Controlled_Buffer controlled_buffer_4
  or or_5 (or_5_out, or_3_out, BEQ);
  not not_3 (not_3_out, P[1]);
  and and_5 (and_5_out, not_3_out, BPL);
  or or_6 (or_6_out, or_4_out, and_4_out);
  assign controlled_buffer_1_out = and_5_out ? PC : 16'bz;  // Controlled_Buffer controlled_buffer_5
  or or_7 (or_7_out, or_5_out, BPL);
  and and_6 (and_6_out, P[1], BMI);
  or or_8 (or_8_out, or_6_out, and_5_out);
  assign controlled_buffer_1_out = and_6_out ? PC : 16'bz;  // Controlled_Buffer controlled_buffer_6
  or or_9 (or_9_out, or_7_out, BMI);
  not not_4 (not_4_out, P[2]);
  and and_7 (and_7_out, not_4_out, BVC);
  or or_10 (or_10_out, or_8_out, and_6_out);
  assign controlled_buffer_1_out = and_7_out ? PC : 16'bz;  // Controlled_Buffer controlled_buffer_7
  or or_11 (or_11_out, or_9_out, BVC);
  and and_8 (and_8_out, P[2], BVS);
  or or_12 (or_12_out, or_10_out, and_7_out);
  assign controlled_buffer_1_out = and_8_out ? PC : 16'bz;  // Controlled_Buffer controlled_buffer_8
  or or_13 (InstDone, or_11_out, BVS);
  or or_14 (PCWrite, or_12_out, and_8_out);
  assign controlled_buffer_9_out = PCWrite ? {{8{1'b0}}, LowByte} : 16'bz;  // Controlled_Buffer controlled_buffer_9
  Adder #(.width(16)) adder_1 (
    .a(controlled_buffer_1_out), .b(controlled_buffer_9_out), .out(INSTPCOut));  // open: cin, cout
endmodule

module JumpInstructions (
  input  Execute,
  input  Fetch,
  input  [15:0] PCALT,
  input  [15:0] PC,
  input  [7:0] StackPointer,
  input  [7:0] InstIn,
  input  JMP,
  input  JSR,
  input  RTS,
  output StackStack,
  output SWrite,
  output MWrite,
  output StackOveride,
  output MRead,
  output PCWrite,
  output InstDone,
  output [15:0] PCinstOut,
  output [7:0] PCinstOut_2
);

  wire and_1_out, and_2_out, and_3_out, and_4_out, and_5_out, and_6_out, and_7_out, and_8_out, and_9_out,
       and_10_out, and_11_out, and_12_out, d_ff_1_q, d_ff_2_q, d_ff_3_q, d_ff_4_q, d_ff_5_q, d_ff_6_q,
       d_ff_7_q, d_ff_8_q, d_ff_9_q, d_ff_10_q, d_ff_11_q, d_ff_12_q, not_1_out, not_2_out, not_3_out,
       not_4_out, not_5_out, not_6_out, not_7_out, not_8_out, not_9_out, not_10_out, not_11_out, not_12_out,
       or_1_out, or_2_out;
  wire [7:0] adder_1_out, register_2_q, register_3_q, subtractor_1_out;
  wire [15:0] register_1_q;

  Register #(.width(16)) register_1 (.D(PCALT), .en(and_1_out), .clk(Execute), .Q(register_1_q), .clr(Fetch));
  assign PCinstOut = JMP ? PCALT : 16'bz;  // Controlled_Buffer controlled_buffer_1
  Adder adder_1 (.a(8'h1), .b(StackPointer), .out(adder_1_out));  // open: cin, cout
  Subtractor subtractor_1 (.a(StackPointer), .b(8'h1), .out(subtractor_1_out));  // open: bin, bout
  or or_1 (or_1_out, and_10_out, and_4_out);
  or or_2 (or_2_out, and_8_out, and_2_out);
  and and_1 (and_1_out, not_1_out, JSR);
  and and_2 (and_2_out, not_2_out, RTS);
  assign PCinstOut_2 = and_2_out ? subtractor_1_out : 8'bz;  // Controlled_Buffer controlled_buffer_2
  or or_3 (StackStack, and_1_out, or_1_out, and_7_out);
  not not_1 (not_1_out, d_ff_1_q);
  D_Flip_Flop #(.trigger("falling")) d_ff_1 (.D(JSR), .clk(Execute), .Q(d_ff_1_q), .reset(Fetch));  // open: Qn, preset
  not not_2 (not_2_out, d_ff_2_q);
  D_Flip_Flop #(.trigger("falling")) d_ff_2 (.D(RTS), .clk(Execute), .Q(d_ff_2_q), .reset(Fetch));  // open: Qn, preset
  assign PCinstOut_2 = and_1_out ? StackPointer : 8'bz;  // Controlled_Buffer controlled_buffer_3
  or or_4 (SWrite, and_3_out, or_2_out, and_9_out);
  and and_3 (and_3_out, not_3_out, d_ff_1_q);
  and and_4 (and_4_out, not_4_out, d_ff_2_q);
  assign PCinstOut_2 = and_4_out ? StackPointer : 8'bz;  // Controlled_Buffer controlled_buffer_4
  not not_3 (not_3_out, d_ff_3_q);
  D_Flip_Flop #(.trigger("falling")) d_ff_3 (
    .D(d_ff_1_q), .clk(Execute), .Q(d_ff_3_q), .reset(Fetch));  // open: Qn, preset
  not not_4 (not_4_out, d_ff_4_q);
  D_Flip_Flop #(.trigger("falling")) d_ff_4 (
    .D(d_ff_2_q), .clk(Execute), .Q(d_ff_4_q), .reset(Fetch));  // open: Qn, preset
  assign PCinstOut_2 = and_3_out ? adder_1_out : 8'bz;  // Controlled_Buffer controlled_buffer_5
  or or_5 (MWrite, and_5_out, and_11_out);
  and and_5 (and_5_out, not_5_out, d_ff_3_q);
  and and_6 (and_6_out, not_6_out, d_ff_4_q);
  D_Flip_Flop #(.trigger("falling")) d_ff_5 (
    .D(d_ff_4_q), .clk(Execute), .Q(d_ff_5_q), .reset(Fetch));  // open: Qn, preset
  Register #(.trigger("falling")) register_2 (.D(InstIn), .en(and_6_out), .clk(Execute), .Q(register_2_q), .clr(Fetch));
  or or_6 (StackOveride, MWrite, MRead);
  not not_5 (not_5_out, d_ff_6_q);
  D_Flip_Flop #(.trigger("falling")) d_ff_6 (
    .D(d_ff_3_q), .clk(Execute), .Q(d_ff_6_q), .reset(Fetch));  // open: Qn, preset
  not not_6 (not_6_out, d_ff_5_q);
  assign PCinstOut_2 = and_5_out ? PC[7:0] : 8'bz;  // Controlled_Buffer controlled_buffer_6
  and and_7 (and_7_out, not_8_out, d_ff_6_q);
  D_Flip_Flop #(.trigger("falling")) d_ff_7 (
    .D(d_ff_6_q), .clk(Execute), .Q(d_ff_7_q), .reset(Fetch));  // open: Qn, preset
  not not_7 (not_7_out, d_ff_8_q);
  and and_8 (and_8_out, not_7_out, d_ff_5_q);
  D_Flip_Flop #(.trigger("falling")) d_ff_8 (
    .D(d_ff_5_q), .clk(Execute), .Q(d_ff_8_q), .reset(Fetch));  // open: Qn, preset
  assign PCinstOut_2 = and_8_out ? subtractor_1_out : 8'bz;  // Controlled_Buffer controlled_buffer_7
  not not_8 (not_8_out, d_ff_7_q);
  assign PCinstOut_2 = and_7_out ? StackPointer : 8'bz;  // Controlled_Buffer controlled_buffer_8
  and and_9 (and_9_out, not_10_out, d_ff_7_q);
  D_Flip_Flop #(.trigger("falling")) d_ff_9 (
    .D(d_ff_7_q), .clk(Execute), .Q(d_ff_9_q), .reset(Fetch));  // open: Qn, preset
  not not_9 (not_9_out, d_ff_10_q);
  and and_10 (and_10_out, not_9_out, d_ff_8_q);
  D_Flip_Flop #(.trigger("falling")) d_ff_10 (
    .D(d_ff_8_q), .clk(Execute), .Q(d_ff_10_q), .reset(Fetch));  // open: Qn, preset
  assign PCinstOut_2 = and_10_out ? StackPointer : 8'bz;  // Controlled_Buffer controlled_buffer_9
  not not_10 (not_10_out, d_ff_9_q);
  assign PCinstOut_2 = and_9_out ? adder_1_out : 8'bz;  // Controlled_Buffer controlled_buffer_10
  not not_11 (not_11_out, d_ff_11_q);
  and and_11 (and_11_out, not_11_out, d_ff_9_q);
  D_Flip_Flop #(.trigger("falling")) d_ff_11 (
    .D(d_ff_9_q), .clk(Execute), .Q(d_ff_11_q), .reset(Fetch));  // open: Qn, preset
  not not_12 (not_12_out, d_ff_12_q);
  and and_12 (and_12_out, not_12_out, d_ff_10_q);
  D_Flip_Flop #(.trigger("falling")) d_ff_12 (
    .D(d_ff_10_q), .clk(Execute), .Q(d_ff_12_q), .reset(Fetch));  // open: Qn, preset
  Register #(.trigger("falling")) register_3 (
    .D(InstIn), .en(and_12_out), .clk(Execute), .Q(register_3_q), .clr(Fetch));
  assign PCinstOut_2 = and_11_out ? PC[15:8] : 8'bz;  // Controlled_Buffer controlled_buffer_11
  assign PCinstOut = d_ff_12_q ? {register_2_q, register_3_q} : 16'bz;  // Controlled_Buffer controlled_buffer_12
  or or_7 (InstDone, JMP, d_ff_12_q, d_ff_11_q);
  or or_8 (MRead, and_12_out, and_6_out);
  assign PCinstOut = d_ff_11_q ? register_1_q : 16'bz;  // Controlled_Buffer controlled_buffer_13

  assign PCWrite = InstDone;
endmodule

module InteruptInstructions (
  input  Execute,
  input  Fetch,
  input  [15:0] PC,
  input  [7:0] P,
  input  [7:0] StackPointer,
  input  [7:0] InstIn,
  input  BRK,
  input  RTI,
  output MWrite,
  output StackOveride,
  output MRead,
  output PWrite,
  output PCWrite,
  output Break,
  output StackStack,
  output SWrite,
  output InstDone,
  output [7:0] InstOut,
  output [15:0] PCinstOut
);

  wire and_1_out, and_2_out, and_3_out, and_4_out, and_5_out, and_6_out, and_8_out, and_9_out, and_10_out,
       and_11_out, and_12_out, and_13_out, and_14_out, and_15_out, and_16_out, and_17_out, and_18_out,
       and_19_out, and_20_out, and_21_out, and_22_out, and_23_out, and_24_out, and_25_out, and_26_out,
       and_27_out, d_ff_1_q, d_ff_2_q, d_ff_3_q, d_ff_4_q, d_ff_5_q, d_ff_6_q, d_ff_7_q, d_ff_8_q, d_ff_9_q,
       d_ff_10_q, d_ff_11_q, d_ff_12_q, d_ff_13_q, d_ff_14_q, d_ff_15_q, d_ff_16_q, d_ff_17_q, d_ff_18_q,
       d_ff_19_q, d_ff_20_q, d_ff_21_q, d_ff_22_q, d_ff_23_q, d_ff_26_q, d_ff_27_q, not_1_out, not_2_out,
       not_3_out, not_4_out, not_5_out, not_6_out, not_7_out, not_8_out, not_9_out, not_10_out, not_11_out,
       not_12_out, not_13_out, not_14_out, not_15_out, not_16_out, not_17_out, not_18_out, not_19_out,
       not_20_out, not_21_out, not_22_out, not_23_out, not_24_out, not_25_out, not_26_out, not_27_out,
       or_5_out, or_6_out, undriven, undriven_2, undriven_3;
  wire [7:0] adder_1_out, register_1_q, register_2_q, subtractor_1_out;

  or or_1 (StackStack, and_1_out, and_9_out, and_18_out, or_6_out);
  not not_1 (not_1_out, d_ff_1_q);
  and and_1 (and_1_out, not_1_out, BRK);
  D_Flip_Flop #(.trigger("falling")) d_ff_1 (.D(BRK), .clk(Execute), .Q(d_ff_1_q), .reset(Fetch));  // open: Qn, preset
  assign InstOut = and_1_out ? StackPointer : 8'bz;  // Controlled_Buffer controlled_buffer_1
  Adder adder_1 (.a(StackPointer), .b(8'h1), .out(adder_1_out));  // open: cin, cout
  Subtractor subtractor_1 (.a(StackPointer), .b(8'h1), .out(subtractor_1_out));  // open: bin, bout
  not not_2 (not_2_out, d_ff_2_q);
  and and_2 (and_2_out, not_2_out, RTI);
  D_Flip_Flop #(.trigger("falling")) d_ff_2 (.D(RTI), .clk(Execute), .Q(d_ff_2_q), .reset(Fetch));  // open: Qn, preset
  assign InstOut = and_2_out ? subtractor_1_out : 8'bz;  // Controlled_Buffer controlled_buffer_2
  or or_2 (SWrite, and_3_out, and_12_out, and_21_out, or_5_out);
  not not_3 (not_3_out, d_ff_3_q);
  and and_3 (and_3_out, not_3_out, d_ff_1_q);
  D_Flip_Flop #(.trigger("falling")) d_ff_3 (
    .D(d_ff_1_q), .clk(Execute), .Q(d_ff_3_q), .reset(Fetch));  // open: Qn, preset
  assign InstOut = and_3_out ? adder_1_out : 8'bz;  // Controlled_Buffer controlled_buffer_3
  and and_4 (and_4_out, not_4_out, d_ff_2_q);
  and and_5 (and_5_out, not_5_out, undriven);
  D_Flip_Flop #(.trigger("falling")) d_ff_4 (
    .D(undriven), .clk(undriven_2), .Q(d_ff_4_q), .reset(undriven_3));  // open: Qn, preset
  and and_6 (and_6_out, not_6_out, d_ff_3_q);
  not not_4 (not_4_out, d_ff_5_q);
  D_Flip_Flop #(.trigger("falling")) d_ff_5 (
    .D(d_ff_2_q), .clk(Execute), .Q(d_ff_5_q), .reset(Fetch));  // open: Qn, preset
  assign InstOut = and_4_out ? StackPointer : 8'bz;  // Controlled_Buffer controlled_buffer_4
  not not_5 (not_5_out, d_ff_4_q);
  or or_3 (MWrite, and_6_out, and_15_out, and_24_out);
  not not_6 (not_6_out, d_ff_6_q);
  D_Flip_Flop #(.trigger("falling")) d_ff_6 (
    .D(d_ff_3_q), .clk(Execute), .Q(d_ff_6_q), .reset(Fetch));  // open: Qn, preset
  assign InstOut = and_6_out ? PC[7:0] : 8'bz;  // Controlled_Buffer controlled_buffer_5
  and and_7 (PWrite, not_8_out, d_ff_5_q);
  not not_7 (not_7_out, d_ff_7_q);
  and and_8 (and_8_out, not_7_out, d_ff_4_q);
  D_Flip_Flop #(.trigger("falling")) d_ff_7 (
    .D(d_ff_4_q), .clk(undriven_2), .Q(d_ff_7_q), .reset(undriven_3));  // open: Qn, preset
  or or_4 (StackOveride, MWrite, MRead);
  and and_9 (and_9_out, not_9_out, d_ff_6_q);
  assign InstOut = and_9_out ? StackPointer : 8'bz;  // Controlled_Buffer controlled_buffer_6
  not not_8 (not_8_out, d_ff_8_q);
  D_Flip_Flop #(.trigger("falling")) d_ff_8 (
    .D(d_ff_5_q), .clk(Execute), .Q(d_ff_8_q), .reset(Fetch));  // open: Qn, preset
  and and_10 (and_10_out, not_10_out, d_ff_7_q);
  not not_9 (not_9_out, d_ff_9_q);
  D_Flip_Flop #(.trigger("falling")) d_ff_9 (
    .D(d_ff_6_q), .clk(Execute), .Q(d_ff_9_q), .reset(Fetch));  // open: Qn, preset
  and and_11 (and_11_out, not_12_out, d_ff_8_q);
  D_Flip_Flop #(.trigger("falling")) d_ff_10 (
    .D(d_ff_8_q), .clk(Execute), .Q(d_ff_10_q), .reset(Fetch));  // open: Qn, preset
  assign InstOut = and_11_out ? subtractor_1_out : 8'bz;  // Controlled_Buffer controlled_buffer_7
  not not_10 (not_10_out, d_ff_11_q);
  D_Flip_Flop #(.trigger("falling")) d_ff_11 (
    .D(d_ff_7_q), .clk(undriven_2), .Q(d_ff_11_q), .reset(undriven_3));  // open: Qn, preset
  not not_11 (not_11_out, d_ff_12_q);
  and and_12 (and_12_out, not_11_out, d_ff_9_q);
  D_Flip_Flop #(.trigger("falling")) d_ff_12 (
    .D(d_ff_9_q), .clk(Execute), .Q(d_ff_12_q), .reset(Fetch));  // open: Qn, preset
  assign InstOut = and_12_out ? adder_1_out : 8'bz;  // Controlled_Buffer controlled_buffer_8
  not not_12 (not_12_out, d_ff_10_q);
  and and_13 (and_13_out, not_14_out, d_ff_11_q);
  not not_13 (not_13_out, d_ff_13_q);
  and and_14 (and_14_out, not_13_out, d_ff_10_q);
  D_Flip_Flop #(.trigger("falling")) d_ff_13 (
    .D(d_ff_10_q), .clk(Execute), .Q(d_ff_13_q), .reset(Fetch));  // open: Qn, preset
  assign InstOut = and_14_out ? StackPointer : 8'bz;  // Controlled_Buffer controlled_buffer_9
  not not_14 (not_14_out, d_ff_14_q);
  D_Flip_Flop #(.trigger("falling")) d_ff_14 (
    .D(d_ff_11_q), .clk(undriven_2), .Q(d_ff_14_q), .reset(undriven_3));  // open: Qn, preset
  not not_15 (not_15_out, d_ff_15_q);
  and and_15 (and_15_out, not_15_out, d_ff_12_q);
  D_Flip_Flop #(.trigger("falling")) d_ff_15 (
    .D(d_ff_12_q), .clk(Execute), .Q(d_ff_15_q), .reset(Fetch));  // open: Qn, preset
  assign InstOut = and_15_out ? PC[15:8] : 8'bz;  // Controlled_Buffer controlled_buffer_10
  and and_16 (and_16_out, not_16_out, d_ff_13_q);
  and and_17 (and_17_out, not_17_out, d_ff_14_q);
  D_Flip_Flop #(.trigger("falling")) d_ff_16 (
    .D(d_ff_14_q), .clk(undriven_2), .Q(d_ff_16_q), .reset(undriven_3));  // open: Qn, preset
  and and_18 (and_18_out, not_18_out, d_ff_15_q);
  not not_16 (not_16_out, d_ff_17_q);
  D_Flip_Flop #(.trigger("falling")) d_ff_17 (
    .D(d_ff_13_q), .clk(Execute), .Q(d_ff_17_q), .reset(Fetch));  // open: Qn, preset
  Register #(.trigger("falling")) register_1 (
    .D(InstIn), .en(and_16_out), .clk(Execute), .Q(register_1_q), .clr(Fetch));
  not not_17 (not_17_out, d_ff_16_q);
  not not_18 (not_18_out, d_ff_18_q);
  D_Flip_Flop #(.trigger("falling")) d_ff_18 (
    .D(d_ff_15_q), .clk(Execute), .Q(d_ff_18_q), .reset(Fetch));  // open: Qn, preset
  assign InstOut = and_18_out ? StackPointer : 8'bz;  // Controlled_Buffer controlled_buffer_11
  or or_5 (or_5_out, and_11_out, and_2_out, and_19_out);
  and and_19 (and_19_out, not_20_out, d_ff_17_q);
  assign InstOut = and_19_out ? subtractor_1_out : 8'bz;  // Controlled_Buffer controlled_buffer_12
  not not_19 (not_19_out, d_ff_19_q);
  and and_20 (and_20_out, not_19_out, d_ff_16_q);
  D_Flip_Flop #(.trigger("falling")) d_ff_19 (
    .D(d_ff_16_q), .clk(undriven_2), .Q(d_ff_19_q), .reset(undriven_3));  // open: Qn, preset
  and and_21 (and_21_out, not_21_out, d_ff_18_q);
  assign InstOut = and_21_out ? adder_1_out : 8'bz;  // Controlled_Buffer controlled_buffer_13
  not not_20 (not_20_out, d_ff_20_q);
  D_Flip_Flop #(.trigger("falling")) d_ff_20 (
    .D(d_ff_17_q), .clk(Execute), .Q(d_ff_20_q), .reset(Fetch));  // open: Qn, preset
  and and_22 (and_22_out, not_22_out, d_ff_19_q);
  not not_21 (not_21_out, d_ff_21_q);
  D_Flip_Flop #(.trigger("falling")) d_ff_21 (
    .D(d_ff_18_q), .clk(Execute), .Q(d_ff_21_q), .reset(Fetch));  // open: Qn, preset
  or or_6 (or_6_out, and_14_out, and_4_out, and_23_out);
  and and_23 (and_23_out, not_23_out, d_ff_20_q);
  D_Flip_Flop #(.trigger("falling")) d_ff_22 (
    .D(d_ff_20_q), .clk(Execute), .Q(d_ff_22_q), .reset(Fetch));  // open: Qn, preset
  assign InstOut = and_23_out ? StackPointer : 8'bz;  // Controlled_Buffer controlled_buffer_14
  not not_22 (not_22_out, d_ff_23_q);
  D_Flip_Flop #(.trigger("falling")) d_ff_23 (
    .D(d_ff_19_q), .clk(undriven_2), .Q(d_ff_23_q), .reset(undriven_3));  // open: Qn, preset
  and and_24 (and_24_out, not_24_out, d_ff_21_q);
  D_Flip_Flop #(.trigger("falling")) d_ff_24 (
    .D(d_ff_21_q), .clk(Execute), .Q(Break), .reset(Fetch));  // open: Qn, preset
  assign InstOut = and_24_out ? P : 8'bz;  // Controlled_Buffer controlled_buffer_15
  not not_23 (not_23_out, d_ff_22_q);
  and and_25 (and_25_out, not_26_out, d_ff_23_q);
  not not_24 (not_24_out, Break);
  or or_7 (MRead, and_16_out, PWrite, and_26_out);
  not not_25 (not_25_out, PCWrite);
  and and_26 (and_26_out, not_25_out, d_ff_22_q);
  D_Flip_Flop #(.trigger("falling")) d_ff_25 (
    .D(d_ff_22_q), .clk(Execute), .Q(PCWrite), .reset(Fetch));  // open: Qn, preset
  Register #(.trigger("falling")) register_2 (
    .D(InstIn), .en(and_26_out), .clk(Execute), .Q(register_2_q), .clr(Fetch));
  not not_26 (not_26_out, d_ff_26_q);
  D_Flip_Flop #(.trigger("falling")) d_ff_26 (
    .D(d_ff_23_q), .clk(undriven_2), .Q(d_ff_26_q), .reset(undriven_3));  // open: Qn, preset
  assign PCinstOut = PCWrite ? {register_1_q, register_2_q} : 16'bz;  // Controlled_Buffer controlled_buffer_16
  and and_27 (and_27_out, not_27_out, d_ff_26_q);
  or or_8 (InstDone, Break, PCWrite);
  not not_27 (not_27_out, d_ff_27_q);
  D_Flip_Flop #(.trigger("falling")) d_ff_27 (
    .D(d_ff_26_q), .clk(undriven_2), .Q(d_ff_27_q), .reset(undriven_3));  // open: Qn, preset
endmodule
