// Logisim project arithemetic_instructions.circ as structural Verilog: 1 circuit, main circuit main
module main (
  input  [7:0] Y,
  input  [7:0] X,
  input  [7:0] A,
  input  [7:0] LowByte,
  input  CarryFlag,
  input  DecimalFlag,
  input  ADC,
  input  CMP,
  input  CPX,
  input  CPY,
  input  SBC,
  output AWrite,
  output InstructionDone,
  output [7:0] InstructionOutput,
  output CarryFlag_2,
  output OverflowFlag,
  output FlagFlag
);

  wire adder_1_cout, adder_2_cout, adder_3_cout, and_1_out, and_2_out, and_3_out, and_4_out, not_1_out,
       not_2_out, not_3_out, not_4_out, not_5_out, not_6_out, not_7_out, not_8_out, not_9_out, not_10_out,
       not_11_out, not_12_out, not_13_out, or_1_out, or_2_out, or_3_out, or_4_out, or_5_out, or_6_out,
       or_8_out, subtractor_1_bout, subtractor_2_bout, subtractor_3_bout, subtractor_4_bout,
       subtractor_5_bout, subtractor_6_bout, subtractor_7_bout, subtractor_8_bout, subtractor_9_bout;
  wire [3:0] adder_2_out, adder_3_out, controlled_buffer_1_out, controlled_buffer_2_out,
       controlled_buffer_12_out, controlled_buffer_13_out, controlled_buffer_14_out,
       controlled_buffer_15_out, controlled_buffer_21_out, controlled_buffer_23_out, subtractor_1_out,
       subtractor_2_out, subtractor_4_out, subtractor_5_out, subtractor_6_out, subtractor_7_out,
       subtractor_8_out, subtractor_9_out, subtractor_10_out, subtractor_11_out;
  wire [7:0] adder_1_out, controlled_buffer_3_out, controlled_buffer_8_out, controlled_buffer_20_out,
       subtractor_3_out;

  and and_1 (and_1_out, ADC, CarryFlag);
  Adder adder_1 (.a(A), .b(LowByte), .out(adder_1_out), .cin(and_1_out), .cout(adder_1_cout));
  and and_2 (and_2_out, ADC, CarryFlag);
  Adder #(.width(4)) adder_2 (.a(A[3:0]), .b(LowByte[3:0]), .out(adder_2_out), .cin(and_2_out), .cout(adder_2_cout));
  not not_1 (not_1_out, subtractor_1_bout);
  or or_1 (or_1_out, adder_2_cout, not_1_out);
  Adder #(.width(4)) adder_3 (.a(A[7:4]), .b(LowByte[7:4]), .out(adder_3_out), .cin(or_1_out), .cout(adder_3_cout));
  or or_2 (or_2_out, adder_3_cout, adder_1_cout);
  not not_2 (not_2_out, CarryFlag);
  Subtractor #(.width(4)) subtractor_1 (
    .a(adder_2_out), .b(4'b1010), .out(subtractor_1_out), .bout(subtractor_1_bout));  // open: bin
  assign controlled_buffer_1_out = not_3_out ? subtractor_1_out : 4'bz;  // Controlled_Buffer controlled_buffer_1
  not not_3 (not_3_out, subtractor_1_bout);
  assign controlled_buffer_2_out = not_4_out ? subtractor_2_out : 4'bz;  // Controlled_Buffer controlled_buffer_2
  Subtractor #(.width(4)) subtractor_2 (
    .a(adder_3_out), .b(4'b1010), .out(subtractor_2_out), .bout(subtractor_2_bout));  // open: bin
  not not_4 (not_4_out, subtractor_2_bout);
  not not_5 (not_5_out, DecimalFlag);
  assign controlled_buffer_3_out = not_5_out ? adder_1_out : 8'bz;  // Controlled_Buffer controlled_buffer_3
  assign controlled_buffer_1_out = subtractor_1_bout ? adder_2_out : 4'bz;  // Controlled_Buffer controlled_buffer_4
  assign controlled_buffer_2_out = subtractor_2_bout ? adder_3_out : 4'bz;  // Controlled_Buffer controlled_buffer_5
  assign InstructionOutput = ADC ? controlled_buffer_3_out : 8'bz;  // Controlled_Buffer controlled_buffer_6
  assign controlled_buffer_3_out = DecimalFlag ? {controlled_buffer_2_out, controlled_buffer_1_out} : 8'bz;  // Controlled_Buffer controlled_buffer_7
  assign controlled_buffer_8_out = CMP ? A : 8'bz;  // Controlled_Buffer controlled_buffer_8
  assign controlled_buffer_8_out = SBC ? A : 8'bz;  // Controlled_Buffer controlled_buffer_9
  assign controlled_buffer_8_out = CPX ? X : 8'bz;  // Controlled_Buffer controlled_buffer_10
  or or_3 (or_3_out, CMP, CPX);
  assign controlled_buffer_8_out = CPY ? Y : 8'bz;  // Controlled_Buffer controlled_buffer_11
  or or_4 (or_4_out, or_3_out, CPY);
  and and_3 (and_3_out, SBC, not_2_out);
  Subtractor subtractor_3 (
    .a(controlled_buffer_8_out), .b(LowByte), .out(subtractor_3_out), .bin(and_3_out),
    .bout(subtractor_3_bout));
  or or_5 (or_5_out, subtractor_3_bout, or_2_out);
  and and_4 (and_4_out, SBC, not_2_out);
  Subtractor #(.width(4)) subtractor_4 (
    .a(A[3:0]), .b(LowByte[3:0]), .out(subtractor_4_out), .bin(and_4_out), .bout(subtractor_4_bout));
  or or_6 (or_6_out, subtractor_4_bout, subtractor_3_bout);
  not not_6 (not_6_out, subtractor_6_bout);
  or or_7 (AWrite, ADC, SBC);
  or or_8 (or_8_out, not_6_out, or_6_out);
  Subtractor #(.width(4)) subtractor_5 (
    .a(A[7:4]), .b(LowByte[7:4]), .out(subtractor_5_out), .bin(or_8_out), .bout(subtractor_5_bout));
  or or_9 (CarryFlag_2, subtractor_5_bout, or_5_out);
  or or_10 (InstructionDone, AWrite, or_4_out);
  Subtractor #(.width(4)) subtractor_6 (
    .a(subtractor_4_out), .b(4'b1010), .out(subtractor_6_out), .bout(subtractor_6_bout));  // open: bin
  assign controlled_buffer_12_out = not_7_out ? subtractor_6_out : 4'bz;  // Controlled_Buffer controlled_buffer_12
  not not_7 (not_7_out, subtractor_6_bout);
  assign controlled_buffer_13_out = not_8_out ? subtractor_7_out : 4'bz;  // Controlled_Buffer controlled_buffer_13
  Subtractor #(.width(4)) subtractor_7 (
    .a(subtractor_4_out), .b(4'b0110), .out(subtractor_7_out), .bout(subtractor_7_bout));  // open: bin
  not not_8 (not_8_out, subtractor_7_bout);
  assign controlled_buffer_14_out = not_9_out ? subtractor_8_out : 4'bz;  // Controlled_Buffer controlled_buffer_14
  Subtractor #(.width(4)) subtractor_8 (
    .a(subtractor_5_out), .b(4'b1010), .out(subtractor_8_out), .bout(subtractor_8_bout));  // open: bin
  not not_9 (not_9_out, subtractor_8_bout);
  Subtractor #(.width(4)) subtractor_9 (
    .a(subtractor_5_out), .b(4'b0110), .out(subtractor_9_out), .bout(subtractor_9_bout));  // open: bin
  assign controlled_buffer_15_out = not_10_out ? subtractor_9_out : 4'bz;  // Controlled_Buffer controlled_buffer_15
  not not_10 (not_10_out, subtractor_9_bout);
  assign controlled_buffer_12_out = subtractor_6_bout ? subtractor_4_out : 4'bz;  // Controlled_Buffer controlled_buffer_16
  assign controlled_buffer_13_out = subtractor_7_bout ? subtractor_10_out : 4'bz;  // Controlled_Buffer controlled_buffer_17
  Subtractor #(.width(4)) subtractor_10 (
    .a(subtractor_4_out), .b(4'b1010), .out(subtractor_10_out));  // open: bin, bout
  assign controlled_buffer_14_out = subtractor_8_bout ? subtractor_5_out : 4'bz;  // Controlled_Buffer controlled_buffer_18
  assign controlled_buffer_15_out = subtractor_9_bout ? subtractor_11_out : 4'bz;  // Controlled_Buffer controlled_buffer_19
  Subtractor #(.width(4)) subtractor_11 (
    .a(subtractor_5_out), .b(4'b1010), .out(subtractor_11_out));  // open: bin, bout
  not not_11 (not_11_out, DecimalFlag);
  assign controlled_buffer_20_out = not_11_out ? subtractor_3_out : 8'bz;  // Controlled_Buffer controlled_buffer_20
  assign controlled_buffer_21_out = not_12_out ? controlled_buffer_12_out : 4'bz;  // Controlled_Buffer controlled_buffer_21
  not not_12 (not_12_out, or_6_out);
  assign controlled_buffer_21_out = or_6_out ? controlled_buffer_13_out : 4'bz;  // Controlled_Buffer controlled_buffer_22
  assign controlled_buffer_23_out = not_13_out ? controlled_buffer_14_out : 4'bz;  // Controlled_Buffer controlled_buffer_23
  not not_13 (not_13_out, subtractor_5_bout);
  assign controlled_buffer_23_out = subtractor_5_bout ? controlled_buffer_15_out : 4'bz;  // Controlled_Buffer controlled_buffer_24
  assign InstructionOutput = SBC ? controlled_buffer_20_out : 8'bz;  // Controlled_Buffer controlled_buffer_25
  assign controlled_buffer_20_out = DecimalFlag ? {controlled_buffer_23_out, controlled_buffer_21_out} : 8'bz;  // Controlled_Buffer controlled_buffer_26
  or or_11 (FlagFlag, ADC, SBC);
  assign InstructionOutput = or_4_out ? controlled_buffer_20_out : 8'bz;  // Controlled_Buffer controlled_buffer_27
  xor xor_1 (OverflowFlag, LowByte[0], InstructionOutput[7]);
endmodule
