// Logisim project branch_instructions.circ as structural Verilog: 1 circuit, main circuit main
module main (
  input  [7:0] P,
  input  [15:0] PC,
  input  [7:0] LowByte,
  input  BCC,
  input  BCS,
  input  BNE,
  input  BEQ,
  input  BPL,
  input  BMI,
  input  BVC,
  input  BVS,
  output PCWrite,
  output [15:0] INSTPCOut,
  output InstDone
);

  wire and_1_out, and_2_out, and_3_out, and_4_out, and_5_out, and_6_out, and_7_out, and_8_out, not_1_out,
       not_2_out, not_3_out, not_4_out, or_1_out, or_2_out, or_3_out, or_4_out, or_5_out, or_6_out, or_7_out,
       or_8_out, or_9_out, or_10_out, or_11_out, or_12_out;
  wire [15:0] controlled_buffer_1_out, controlled_buffer_9_out;

  not not_1 (not_1_out, P[7]);
  and and_1 (and_1_out, not_1_out, BCC);
  assign controlled_buffer_1_out = and_1_out ? PC : 16'bz;  // Controlled_Buffer controlled_buffer_1
  and and_2 (and_2_out, P[7], BCS);
  assign controlled_buffer_1_out = and_2_out ? PC : 16'bz;  // Controlled_Buffer controlled_buffer_2
  or or_1 (or_1_out, BCC, BCS);
  not not_2 (not_2_out, P[6]);
  and and_3 (and_3_out, not_2_out, BNE);
  or or_2 (or_2_out, and_2_out, and_1_out);
  assign controlled_buffer_1_out = and_3_out ? PC : 16'bz;  // Controlled_Buffer controlled_buffer_3
  or or_3 (or_3_out, or_1_out, BNE);
  and and_4 (and_4_out, P[6], BEQ);
  or or_4 (or_4_out, or_2_out, and_3_out);
  assign controlled_buffer_1_out = and_4_out ? PC : 16'bz;  // Controlled_Buffer controlled_buffer_4
  or or_5 (or_5_out, or_3_out, BEQ);
  not not_3 (not_3_out, P[1]);
  and and_5 (and_5_out, not_3_out, BPL);
  or or_6 (or_6_out, or_4_out, and_4_out);
  assign controlled_buffer_1_out = and_5_out ? PC : 16'bz;  // Controlled_Buffer controlled_buffer_5
  or or_7 (or_7_out, or_5_out, BPL);
  and and_6 (and_6_out, P[1], BMI);
  or or_8 (or_8_out, or_6_out, and_5_out);
  assign controlled_buffer_1_out = and_6_out ? PC : 16'bz;  // Controlled_Buffer controlled_buffer_6
  or or_9 (or_9_out, or_7_out, BMI);
  not not_4 (not_4_out, P[2]);
  and and_7 (and_7_out, not_4_out, BVC);
  or or_10 (or_10_out, or_8_out, and_6_out);
  assign controlled_buffer_1_out = and_7_out ? PC : 16'bz;  // Controlled_Buffer controlled_buffer_7
  or or_11 (or_11_out, or_9_out, BVC);
  and and_8 (and_8_out, P[2], BVS);
  or or_12 (or_12_out, or_10_out, and_7_out);
  assign controlled_buffer_1_out = and_8_out ? PC : 16'bz;  // Controlled_Buffer controlled_buffer_8
  or or_13 (InstDone, or_11_out, BVS);
  or or_14 (PCWrite, or_12_out, and_8_out);
  assign controlled_buffer_9_out = PCWrite ? {{8{1'b0}}, LowByte} : 16'bz;  // Controlled_Buffer controlled_buffer_9
  Adder #(.width(16)) adder_1 (
    .a(controlled_buffer_1_out), .b(controlled_buffer_9_out), .out(INSTPCOut));  // open: cin, cout
endmodule
