// Logisim project clock.circ as structural Verilog: 1 circuit, main circuit main
module main (
  input  ClockIn,
  output C3,
  output C2,
  output C1,
  output C0,
  output Clock
);

  wire d_ff_1_q, d_ff_2_q, d_ff_3_q, d_ff_4_q, not_1_out, or_1_out;

  or or_1 (or_1_out, d_ff_1_q, d_ff_2_q, d_ff_3_q, d_ff_4_q);
  not not_1 (not_1_out, or_1_out);
  D_Flip_Flop #(.trigger("falling")) d_ff_1 (.D(d_ff_2_q), .clk(ClockIn), .Q(d_ff_1_q));  // open: Qn, preset, reset
  D_Flip_Flop #(.trigger("falling")) d_ff_2 (.D(d_ff_3_q), .clk(ClockIn), .Q(d_ff_2_q));  // open: Qn, preset, reset
  D_Flip_Flop #(.trigger("falling")) d_ff_3 (.D(d_ff_4_q), .clk(ClockIn), .Q(d_ff_3_q));  // open: Qn, preset, reset
  D_Flip_Flop #(.trigger("falling")) d_ff_4 (.D(not_1_out), .clk(ClockIn), .Q(d_ff_4_q));  // open: Qn, preset, reset
  and and_1 (C3, ClockIn, d_ff_1_q);
  and and_2 (C2, ClockIn, d_ff_2_q);
  and and_3 (C1, ClockIn, d_ff_3_q);
  and and_4 (C0, ClockIn, d_ff_4_q);

  assign Clock = ClockIn;
endmodule
