// Logisim project execute.circ as structural Verilog: 11 circuits, main circuit main
module main (
  input  [7:0] InstIn,
  input  [19:0] InstructionSet1,
  input  [16:0] InstructionSet2,
  input  [16:0] InstructionSet3,
  input  [7:0] LowByte,
  input  [23:0] RegisterIn,
  input  [15:0] PCin,
  input  [15:0] PCin_2,
  input  [7:0] StackIn,
  input  [6:0] StatusIn,
  input  Execute,
  input  Fetch,
  input  AMode,
  output [15:0] PCInstructionOut,
  output SWrite,
  output YWrite,
  output XWrite,
  output AWrite,
  output MWrite,
  output PWrite,
  output Stack,
  output MRead,
  output StackOverwrite,
  output KeepPCOFF,
  output PCWrite,
  output InstructionDone,
  output [7:0] InstructionOut,
  output ZNRead,
  output CRead,
  output ORead,
  output ZWrite,
  output NWrite,
  output CWrite,
  output OWrite,
  output Break,
  output ClearCarry,
  output ClearDecimal,
  output ClearInterupt,
  output ClearOverflow,
  output SetCarry,
  output SetDecimal,
  output SetInterupt
);

  wire and_10_out, and_11_out, and_12_out, and_14_out, ArithAWrite, ArithInstDone, ArithIntCarry,
       ArithIntFlag, ArithIntZero, BranchInstDone, BranchPCWrite, Break_t, FlagInstDone, IncrementInstDone,
       IncrMWrite, IncrPCOFF, IncrXWrite, IncrYWrite, InteruptInstDone, InteruptMRead, InteruptMWrite,
       InteruptOveride, InteruptPCWrite, InteruptPWrite, InteruptStack, InteruptSWrite, JumpInstDone,
       JumpMRead, JumpMWrite, JumpOveride, JumpPCWrite, JumpStack, JumpSWrite, LogAWrite, LogInstDone,
       not_1_out, not_2_out, not_3_out, not_4_out, not_5_out, not_6_out, not_7_out, not_8_out, not_9_out,
       not_10_out, or_1_out, or_2_out, or_3_out, or_4_out, or_5_out, or_6_out, or_7_out, or_8_out, or_9_out,
       or_10_out, or_11_out, or_12_out, or_13_out, or_14_out, or_15_out, or_16_out, or_17_out, or_18_out,
       or_19_out, or_21_out, or_23_out, or_24_out, or_27_out, or_28_out, or_29_out, or_30_out, or_33_out,
       or_34_out, or_35_out, or_36_out, or_37_out, or_38_out, or_39_out, or_40_out, RotAWrite, RotInstDone,
       RotIntCarry, RotMWrite, RotPCOFF, StackAWrite, StackInstDone, StackIntFlag, StackMRead, StackMWrite,
       StackOveride, StackPWrite, StackStack, StackSWrite, TransAWrite, TransferInstDone, TransferInstFlag,
       TransMWrite, TransPCOFF, TransSWrite, TransXWrite, TransYWrite;

  not not_1 (not_1_out, InstructionOut[0]);
  not not_2 (not_2_out, InstructionOut[1]);
  not not_3 (not_3_out, InstructionOut[2]);
  not not_4 (not_4_out, InstructionOut[3]);
  not not_5 (not_5_out, InstructionOut[4]);
  not not_6 (not_6_out, InstructionOut[5]);
  not not_7 (not_7_out, InstructionOut[6]);
  not not_8 (not_8_out, InstructionOut[7]);
  and and_1 (ZWrite, not_1_out, not_2_out, not_3_out, not_4_out, not_5_out, not_6_out, not_7_out, not_8_out);
  and and_2 (SWrite, or_1_out, Execute);
  or or_1 (or_1_out, TransSWrite, or_2_out);
  or or_2 (or_2_out, StackSWrite, or_3_out);
  or or_3 (or_3_out, JumpSWrite, InteruptSWrite);
  ArithmeticInstructions arithmeticinstructions_1 (
    .Y(RegisterIn[23:16]), .X(RegisterIn[15:8]), .A(RegisterIn[7:0]), .LowByte(LowByte),
    .CarryFlag(StatusIn[6]), .DecimalFlag(StatusIn[3]), .AWrite(ArithAWrite), .ADC(InstructionSet1[16]),
    .CMP(InstructionSet1[5]), .CPX(InstructionSet1[12]), .CPY(InstructionSet1[13]), .SBC(InstructionSet1[4]),
    .InstructionDone(ArithInstDone), .InstructionOutput(InstructionOut), .CarryFlag_2(ArithIntZero),
    .OverflowFlag(OWrite), .FlagFlag(ArithIntFlag));
  FlagInstructions flaginstructions_1 (
    .ClearCarry(ClearCarry), .ClearDecimal(ClearDecimal), .ClearInterupt(ClearInterupt),
    .ClearOverflow(ClearOverflow), .SetCarry(SetCarry), .SetDecimal(SetDecimal), .SetInterupt(SetInterupt),
    .CLC(InstructionSet2[2]), .CLD(InstructionSet3[12]), .CLI(InstructionSet2[10]), .CLV(InstructionSet3[7]),
    .SEC(InstructionSet2[6]), .SED(InstructionSet3[15]), .SEI(InstructionSet2[15]), .InstDone(FlagInstDone));
  // LogicalInstructions logicalinstructions_1: pin names not known; wires that end beside it: RegisterIn[7:0], LowByte, InstructionSet1[18], LogAWrite, InstructionSet1[19], InstructionSet1[17], LogInstDone, InstructionOut
  or or_4 (or_4_out, TransYWrite, IncrYWrite);
  TransferInstructions transferinstructions_1 (
    .x(RegisterIn[15:8]), .y(RegisterIn[23:16]), .a(RegisterIn[7:0]), .s(StackIn), .M(LowByte),
    .XWrite(TransXWrite), .YWrite(TransYWrite), .AWrite(TransAWrite), .SWrite(TransSWrite),
    .MWrite(TransMWrite), .PCOFF(TransPCOFF), .STA(InstructionSet1[15]), .STY(InstructionSet1[7]),
    .STX(InstructionSet1[3]), .LDA(InstructionSet1[6]), .LDY(InstructionSet1[14]), .LDX(InstructionSet1[2]),
    .TAX(InstructionSet3[6]), .TXA(InstructionSet3[1]), .TAY(InstructionSet3[5]), .TYA(InstructionSet3[2]),
    .TXS(InstructionSet3[3]), .TSX(InstructionSet3[8]), .out_18(InstructionOut),
    .TransferInstructionDone(TransferInstDone), .FlagFlag(TransferInstFlag));
  and and_3 (YWrite, or_4_out, Execute);
  and and_4 (XWrite, or_5_out, Execute);
  or or_5 (or_5_out, TransXWrite, IncrXWrite);
  and and_5 (AWrite, or_6_out, Execute);
  or or_6 (or_6_out, TransAWrite, or_7_out);
  or or_7 (or_7_out, StackAWrite, or_8_out);
  or or_8 (or_8_out, ArithAWrite, or_9_out);
  or or_9 (or_9_out, LogAWrite, RotAWrite);
  BranchInstructions branchinstructions_1 (
    .P({StatusIn, 1'b0}), .PC(PCin), .LowByte(LowByte), .PCWrite(BranchPCWrite), .BCC(InstructionSet3[4]),
    .BCS(InstructionSet3[9]), .BNE(InstructionSet3[13]), .BEQ(InstructionSet3[16]), .BPL(InstructionSet2[3]),
    .BMI(InstructionSet2[7]), .BVC(InstructionSet2[12]), .BVS(InstructionSet2[16]),
    .INSTPCOut(PCInstructionOut), .InstDone(BranchInstDone));
  IncrementInstructions incrementinstructions_1 (
    .X(RegisterIn[15:8]), .Y(RegisterIn[23:16]), .LowByte(LowByte), .XWrite(IncrXWrite), .YWrite(IncrYWrite),
    .MWrite(IncrMWrite), .PCOFF(IncrPCOFF), .DEX(InstructionSet3[11]), .DEY(InstructionSet3[0]),
    .DEC(InstructionSet1[1]), .INX(InstructionSet3[14]), .INY(InstructionSet3[10]), .INC(InstructionSet1[0]),
    .InstOut(InstructionOut), .InstDone(IncrementInstDone));
  StackInstructions stackinstructions_1 (
    .Execute(Execute), .Fetch(Fetch), .StackPointer(StackIn), .StatusRegister({StatusIn, 1'b0}),
    .Accumulator(RegisterIn[7:0]), .StackStack(StackStack), .Swrite(StackSWrite),
    .StackOveride(StackOveride), .MWrite(StackMWrite), .MRead(StackMRead), .AWrite(StackAWrite),
    .StatusWrite(StackPWrite), .PHA(InstructionSet2[9]), .PHP(InstructionSet2[1]), .PLA(InstructionSet2[14]),
    .PLP(InstructionSet2[5]), .InstDone(StackInstDone), .InstructionOut(InstructionOut),
    .FlagFlag(StackIntFlag));
  and and_6 (MWrite, or_10_out, Execute);
  or or_10 (or_10_out, TransMWrite, or_11_out);
  or or_11 (or_11_out, StackMWrite, or_12_out);
  or or_12 (or_12_out, IncrMWrite, or_13_out);
  or or_13 (or_13_out, RotMWrite, or_14_out);
  or or_14 (or_14_out, JumpMWrite, InteruptMWrite);
  and and_7 (PWrite, or_15_out, Execute);
  or or_15 (or_15_out, StackPWrite, InteruptPWrite);
  RotationInstruction rotationinstruction_1 (
    .AccumulatorTrigger(AMode), .A(RegisterIn[7:0]), .LowByte(LowByte), .Carry(StatusIn[0]),
    .AWrite(RotAWrite), .MWrite(RotMWrite), .PCOFF(RotPCOFF), .ASL(InstructionSet1[11]),
    .ROL(InstructionSet1[10]), .LSR(InstructionSet1[9]), .ROR(InstructionSet1[8]), .InstDone(RotInstDone),
    .InstructionOut(InstructionOut), .CarryFlag(RotIntCarry));
  and and_8 (Stack, or_16_out, Execute);
  or or_16 (or_16_out, StackStack, or_17_out);
  or or_17 (or_17_out, JumpStack, InteruptStack);
  JumpInstructions jumpinstructions_1 (
    .Execute(Execute), .Fetch(Fetch), .PCALT(PCin_2), .PC(PCin), .StackPointer(StackIn), .InstIn(InstIn),
    .StackStack(JumpStack), .SWrite(JumpSWrite), .MWrite(JumpMWrite), .StackOveride(JumpOveride),
    .MRead(JumpMRead), .PCWrite(JumpPCWrite), .JMP(InstructionSet2[11]), .JSR(InstructionSet2[4]),
    .RTS(InstructionSet2[13]), .InstDone(JumpInstDone), .PCinstOut(PCInstructionOut),
    .PCinstOut_2(InstructionOut));
  and and_9 (MRead, or_18_out, Execute);
  or or_18 (or_18_out, StackMRead, or_19_out);
  or or_19 (or_19_out, JumpMRead, InteruptMRead);
  InteruptInstructions interuptinstructions_1 (
    .Execute(Execute), .Fetch(Fetch), .PC(PCin), .P({StatusIn, 1'b0}), .StackPointer(StackIn),
    .InstIn(InstIn), .StackStack(InteruptStack), .SWrite(InteruptSWrite), .MWrite(InteruptMWrite),
    .StackOveride(InteruptOveride), .MRead(InteruptMRead), .PWrite(InteruptPWrite),
    .PCWrite(InteruptPCWrite), .Break(Break_t), .BRK(InstructionSet2[0]), .RTI(InstructionSet2[8]),
    .InstDone(InteruptInstDone), .InstOut(InstructionOut), .PCinstOut(PCInstructionOut));
  or or_20 (StackOverwrite, StackOveride, or_21_out);
  or or_21 (or_21_out, JumpOveride, InteruptOveride);
  or or_22 (KeepPCOFF, TransPCOFF, or_23_out);
  or or_23 (or_23_out, IncrPCOFF, or_24_out);
  buf or_24 (or_24_out, RotPCOFF);  // OR_Gate
  and and_10 (and_10_out, ArithInstDone, not_9_out);
  not not_9 (not_9_out, StatusIn[3]);
  and and_11 (and_11_out, TransferInstDone, TransferInstFlag);
  and and_12 (and_12_out, StackInstDone, StackIntFlag);
  or or_25 (CRead, and_10_out, RotInstDone);
  and and_13 (ORead, and_10_out, ArithIntFlag);
  or or_26 (CWrite, RotIntCarry, and_14_out);
  and and_14 (and_14_out, ArithInstDone, ArithIntCarry);
  not not_10 (not_10_out, StatusIn[3]);
  and and_15 (PCWrite, or_27_out, Execute);
  or or_27 (or_27_out, BranchPCWrite, or_28_out);
  or or_28 (or_28_out, JumpPCWrite, InteruptPCWrite);
  or or_29 (or_29_out, and_11_out, LogInstDone, and_12_out);
  or or_30 (or_30_out, IncrementInstDone, RotInstDone, and_10_out);
  and and_16 (Break, Break_t, not_10_out);
  or or_31 (ZNRead, or_29_out, or_30_out);
  or or_32 (InstructionDone, TransferInstDone, or_33_out);
  or or_33 (or_33_out, StackInstDone, or_34_out);
  or or_34 (or_34_out, IncrementInstDone, or_35_out);
  or or_35 (or_35_out, ArithInstDone, or_36_out);
  or or_36 (or_36_out, LogInstDone, or_37_out);
  or or_37 (or_37_out, RotInstDone, or_38_out);
  or or_38 (or_38_out, BranchInstDone, or_39_out);
  or or_39 (or_39_out, JumpInstDone, or_40_out);
  or or_40 (or_40_out, InteruptInstDone, FlagInstDone);

  assign NWrite = InstructionOut[7];

  // Other names for the same wires on the sheet: ArithIntOverflow = OWrite; BranchInstOut[15:0] = PCInstructionOut;
  //   InterupPCtInstOut[15:0] = PCInstructionOut; JumpPCInstOut[15:0] = PCInstructionOut; PAltCout[15:0] = PCin_2;
  //   PCout[15:0] = PCin; Pout[7:1] = StatusIn; RegOut[23:0] = RegisterIn; Sout[7:0] = StackIn;
  //   ArithInstOut[7:0] = InstructionOut; IncrementInstOut[7:0] = InstructionOut;
  //   InteruptInstOut[7:0] = InstructionOut; JumpInstOut[7:0] = InstructionOut; LogInstOut[7:0] = InstructionOut;
  //   RotInstOut[7:0] = InstructionOut; StackInstOut[7:0] = InstructionOut; TransferInstOut[7:0] = InstructionOut;
  //   Negative = InstructionOut[7]; Zero = ZWrite
endmodule

module InteruptInstructions (
  input  Execute,
  input  Fetch,
  input  [15:0] PC,
  input  [7:0] P,
  input  [7:0] StackPointer,
  input  [7:0] InstIn,
  input  BRK,
  input  RTI,
  output MWrite,
  output StackOveride,
  output MRead,
  output PWrite,
  output PCWrite,
  output Break,
  output StackStack,
  output SWrite,
  output InstDone,
  output [7:0] InstOut,
  output [15:0] PCinstOut
);

  wire and_1_out, and_2_out, and_3_out, and_4_out, and_5_out, and_7_out, and_8_out, and_9_out, and_10_out,
       and_11_out, and_12_out, and_13_out, and_14_out, and_15_out, and_16_out, and_17_out, and_18_out,
       d_ff_1_q, d_ff_2_q, d_ff_3_q, d_ff_4_q, d_ff_5_q, d_ff_6_q, d_ff_7_q, d_ff_8_q, d_ff_9_q, d_ff_10_q,
       d_ff_11_q, d_ff_12_q, d_ff_13_q, d_ff_14_q, d_ff_15_q, d_ff_16_q, not_1_out, not_2_out, not_3_out,
       not_4_out, not_5_out, not_6_out, not_7_out, not_8_out, not_9_out, not_10_out, not_11_out, not_12_out,
       not_13_out, not_14_out, not_15_out, not_16_out, not_17_out, not_18_out, or_5_out, or_6_out;
  wire [7:0] adder_1_out, register_1_q, register_2_q, subtractor_1_out;

  or or_1 (StackStack, and_1_out, and_7_out, and_13_out, or_6_out);
  not not_1 (not_1_out, d_ff_1_q);
  and and_1 (and_1_out, not_1_out, BRK);
  D_Flip_Flop #(.trigger("falling")) d_ff_1 (.D(BRK), .clk(Execute), .Q(d_ff_1_q), .reset(Fetch));  // open: Qn, preset
  assign InstOut = and_1_out ? StackPointer : 8'bz;  // Controlled_Buffer controlled_buffer_1
  Adder adder_1 (.a(StackPointer), .b(8'h1), .out(adder_1_out));  // open: cin, cout
  Subtractor subtractor_1 (.a(StackPointer), .b(8'h1), .out(subtractor_1_out));  // open: bin, bout
  not not_2 (not_2_out, d_ff_2_q);
  and and_2 (and_2_out, not_2_out, RTI);
  D_Flip_Flop #(.trigger("falling")) d_ff_2 (.D(RTI), .clk(Execute), .Q(d_ff_2_q), .reset(Fetch));  // open: Qn, preset
  assign InstOut = and_2_out ? subtractor_1_out : 8'bz;  // Controlled_Buffer controlled_buffer_2
  or or_2 (SWrite, and_3_out, and_9_out, and_15_out, or_5_out);
  not not_3 (not_3_out, d_ff_3_q);
  and and_3 (and_3_out, not_3_out, d_ff_1_q);
  D_Flip_Flop #(.trigger("falling")) d_ff_3 (
    .D(d_ff_1_q), .clk(Execute), .Q(d_ff_3_q), .reset(Fetch));  // open: Qn, preset
  assign InstOut = and_3_out ? adder_1_out : 8'bz;  // Controlled_Buffer controlled_buffer_3
  and and_4 (and_4_out, not_4_out, d_ff_2_q);
  and and_5 (and_5_out, not_5_out, d_ff_3_q);
  not not_4 (not_4_out, d_ff_4_q);
  D_Flip_Flop #(.trigger("falling")) d_ff_4 (
    .D(d_ff_2_q), .clk(Execute), .Q(d_ff_4_q), .reset(Fetch));  // open: Qn, preset
  assign InstOut = and_4_out ? StackPointer : 8'bz;  // Controlled_Buffer controlled_buffer_4
  or or_3 (MWrite, and_5_out, and_11_out, and_17_out);
  not not_5 (not_5_out, d_ff_5_q);
  D_Flip_Flop #(.trigger("falling")) d_ff_5 (
    .D(d_ff_3_q), .clk(Execute), .Q(d_ff_5_q), .reset(Fetch));  // open: Qn, preset
  assign InstOut = and_5_out ? PC[7:0] : 8'bz;  // Controlled_Buffer controlled_buffer_5
  and and_6 (PWrite, not_6_out, d_ff_4_q);
  or or_4 (StackOveride, MWrite, MRead);
  and and_7 (and_7_out, not_7_out, d_ff_5_q);
  assign InstOut = and_7_out ? StackPointer : 8'bz;  // Controlled_Buffer controlled_buffer_6
  not not_6 (not_6_out, d_ff_6_q);
  D_Flip_Flop #(.trigger("falling")) d_ff_6 (
    .D(d_ff_4_q), .clk(Execute), .Q(d_ff_6_q), .reset(Fetch));  // open: Qn, preset
  not not_7 (not_7_out, d_ff_7_q);
  D_Flip_Flop #(.trigger("falling")) d_ff_7 (
    .D(d_ff_5_q), .clk(Execute), .Q(d_ff_7_q), .reset(Fetch));  // open: Qn, preset
  and and_8 (and_8_out, not_9_out, d_ff_6_q);
  D_Flip_Flop #(.trigger("falling")) d_ff_8 (
    .D(d_ff_6_q), .clk(Execute), .Q(d_ff_8_q), .reset(Fetch));  // open: Qn, preset
  assign InstOut = and_8_out ? subtractor_1_out : 8'bz;  // Controlled_Buffer controlled_buffer_7
  not not_8 (not_8_out, d_ff_9_q);
  and and_9 (and_9_out, not_8_out, d_ff_7_q);
  D_Flip_Flop #(.trigger("falling")) d_ff_9 (
    .D(d_ff_7_q), .clk(Execute), .Q(d_ff_9_q), .reset(Fetch));  // open: Qn, preset
  assign InstOut = and_9_out ? adder_1_out : 8'bz;  // Controlled_Buffer controlled_buffer_8
  not not_9 (not_9_out, d_ff_8_q);
  not not_10 (not_10_out, d_ff_10_q);
  and and_10 (and_10_out, not_10_out, d_ff_8_q);
  D_Flip_Flop #(.trigger("falling")) d_ff_10 (
    .D(d_ff_8_q), .clk(Execute), .Q(d_ff_10_q), .reset(Fetch));  // open: Qn, preset
  assign InstOut = and_10_out ? StackPointer : 8'bz;  // Controlled_Buffer controlled_buffer_9
  not not_11 (not_11_out, d_ff_11_q);
  and and_11 (and_11_out, not_11_out, d_ff_9_q);
  D_Flip_Flop #(.trigger("falling")) d_ff_11 (
    .D(d_ff_9_q), .clk(Execute), .Q(d_ff_11_q), .reset(Fetch));  // open: Qn, preset
  assign InstOut = and_11_out ? PC[15:8] : 8'bz;  // Controlled_Buffer controlled_buffer_10
  and and_12 (and_12_out, not_12_out, d_ff_10_q);
  and and_13 (and_13_out, not_13_out, d_ff_11_q);
  not not_12 (not_12_out, d_ff_12_q);
  D_Flip_Flop #(.trigger("falling")) d_ff_12 (
    .D(d_ff_10_q), .clk(Execute), .Q(d_ff_12_q), .reset(Fetch));  // open: Qn, preset
  Register #(.trigger("falling")) register_1 (
    .D(InstIn), .en(and_12_out), .clk(Execute), .Q(register_1_q), .clr(Fetch));
  not not_13 (not_13_out, d_ff_13_q);
  D_Flip_Flop #(.trigger("falling")) d_ff_13 (
    .D(d_ff_11_q), .clk(Execute), .Q(d_ff_13_q), .reset(Fetch));  // open: Qn, preset
  assign InstOut = and_13_out ? StackPointer : 8'bz;  // Controlled_Buffer controlled_buffer_11
  or or_5 (or_5_out, and_8_out, and_2_out, and_14_out);
  and and_14 (and_14_out, not_14_out, d_ff_12_q);
  assign InstOut = and_14_out ? subtractor_1_out : 8'bz;  // Controlled_Buffer controlled_buffer_12
  and and_15 (and_15_out, not_15_out, d_ff_13_q);
  assign InstOut = and_15_out ? adder_1_out : 8'bz;  // Controlled_Buffer controlled_buffer_13
  not not_14 (not_14_out, d_ff_14_q);
  D_Flip_Flop #(.trigger("falling")) d_ff_14 (
    .D(d_ff_12_q), .clk(Execute), .Q(d_ff_14_q), .reset(Fetch));  // open: Qn, preset
  not not_15 (not_15_out, d_ff_15_q);
  D_Flip_Flop #(.trigger("falling")) d_ff_15 (
    .D(d_ff_13_q), .clk(Execute), .Q(d_ff_15_q), .reset(Fetch));  // open: Qn, preset
  or or_6 (or_6_out, and_10_out, and_4_out, and_16_out);
  and and_16 (and_16_out, not_16_out, d_ff_14_q);
  D_Flip_Flop #(.trigger("falling")) d_ff_16 (
    .D(d_ff_14_q), .clk(Execute), .Q(d_ff_16_q), .reset(Fetch));  // open: Qn, preset
  assign InstOut = and_16_out ? StackPointer : 8'bz;  // Controlled_Buffer controlled_buffer_14
  and and_17 (and_17_out, not_17_out, d_ff_15_q);
  D_Flip_Flop #(.trigger("falling")) d_ff_17 (
    .D(d_ff_15_q), .clk(Execute), .Q(Break), .reset(Fetch));  // open: Qn, preset
  assign InstOut = and_17_out ? P : 8'bz;  // Controlled_Buffer controlled_buffer_15
  not not_16 (not_16_out, d_ff_16_q);
  not not_17 (not_17_out, Break);
  or or_7 (MRead, and_12_out, PWrite, and_18_out);
  not not_18 (not_18_out, PCWrite);
  and and_18 (and_18_out, not_18_out, d_ff_16_q);
  D_Flip_Flop #(.trigger("falling")) d_ff_18 (
    .D(d_ff_16_q), .clk(Execute), .Q(PCWrite), .reset(Fetch));  // open: Qn, preset
  Register #(.trigger("falling")) register_2 (
    .D(InstIn), .en(and_18_out), .clk(Execute), .Q(register_2_q), .clr(Fetch));
  assign PCinstOut = PCWrite ? {register_1_q, register_2_q} : 16'bz;  // Controlled_Buffer controlled_buffer_16
  or or_8 (InstDone, Break, PCWrite);
endmodule

module JumpInstructions (
  input  Execute,
  input  Fetch,
  input  [15:0] PCALT,
  input  [15:0] PC,
  input  [7:0] StackPointer,
  input  [7:0] InstIn,
  input  JMP,
  input  JSR,
  input  RTS,
  output StackStack,
  output SWrite,
  output MWrite,
  output StackOveride,
  output MRead,
  output PCWrite,
  output InstDone,
  output [15:0] PCinstOut,
  output [7:0] PCinstOut_2
);

  wire and_1_out, and_2_out, and_3_out, and_4_out, and_5_out, and_6_out, and_7_out, and_8_out, and_9_out,
       and_10_out, and_11_out, and_12_out, d_ff_1_q, d_ff_2_q, d_ff_3_q, d_ff_4_q, d_ff_5_q, d_ff_6_q,
       d_ff_7_q, d_ff_8_q, d_ff_9_q, d_ff_10_q, d_ff_11_q, d_ff_12_q, not_1_out, not_2_out, not_3_out,
       not_4_out, not_5_out, not_6_out, not_7_out, not_8_out, not_9_out, not_10_out, not_11_out, not_12_out,
       or_1_out, or_2_out;
  wire [7:0] adder_1_out, register_2_q, register_3_q, subtractor_1_out;
  wire [15:0] register_1_q;

  Register #(.width(16)) register_1 (.D(PCALT), .en(and_1_out), .clk(Execute), .Q(register_1_q), .clr(Fetch));
  assign PCinstOut = JMP ? PCALT : 16'bz;  // Controlled_Buffer controlled_buffer_1
  Adder adder_1 (.a(8'h1), .b(StackPointer), .out(adder_1_out));  // open: cin, cout
  Subtractor subtractor_1 (.a(StackPointer), .b(8'h1), .out(subtractor_1_out));  // open: bin, bout
  or or_1 (or_1_out, and_10_out, and_4_out);
  or or_2 (or_2_out, and_8_out, and_2_out);
  and and_1 (and_1_out, not_1_out, JSR);
  and and_2 (and_2_out, not_2_out, RTS);
  assign PCinstOut_2 = and_2_out ? subtractor_1_out : 8'bz;  // Controlled_Buffer controlled_buffer_2
  or or_3 (StackStack, and_1_out, or_1_out, and_7_out);
  not not_1 (not_1_out, d_ff_1_q);
  D_Flip_Flop #(.trigger("falling")) d_ff_1 (.D(JSR), .clk(Execute), .Q(d_ff_1_q), .reset(Fetch));  // open: Qn, preset
  not not_2 (not_2_out, d_ff_2_q);
  D_Flip_Flop #(.trigger("falling")) d_ff_2 (.D(RTS), .clk(Execute), .Q(d_ff_2_q), .reset(Fetch));  // open: Qn, preset
  assign PCinstOut_2 = and_1_out ? StackPointer : 8'bz;  // Controlled_Buffer controlled_buffer_3
  or or_4 (SWrite, and_3_out, or_2_out, and_9_out);
  and and_3 (and_3_out, not_3_out, d_ff_1_q);
  and and_4 (and_4_out, not_4_out, d_ff_2_q);
  assign PCinstOut_2 = and_4_out ? StackPointer : 8'bz;  // Controlled_Buffer controlled_buffer_4
  not not_3 (not_3_out, d_ff_3_q);
  D_Flip_Flop #(.trigger("falling")) d_ff_3 (
    .D(d_ff_1_q), .clk(Execute), .Q(d_ff_3_q), .reset(Fetch));  // open: Qn, preset
  not not_4 (not_4_out, d_ff_4_q);
  D_Flip_Flop #(.trigger("falling")) d_ff_4 (
    .D(d_ff_2_q), .clk(Execute), .Q(d_ff_4_q), .reset(Fetch));  // open: Qn, preset
  assign PCinstOut_2 = and_3_out ? adder_1_out : 8'bz;  // Controlled_Buffer controlled_buffer_5
  or or_5 (MWrite, and_5_out, and_11_out);
  and and_5 (and_5_out, not_5_out, d_ff_3_q);
  and and_6 (and_6_out, not_6_out, d_ff_4_q);
  D_Flip_Flop #(.trigger("falling")) d_ff_5 (
    .D(d_ff_4_q), .clk(Execute), .Q(d_ff_5_q), .reset(Fetch));  // open: Qn, preset
  Register #(.trigger("falling")) register_2 (.D(InstIn), .en(and_6_out), .clk(Execute), .Q(register_2_q), .clr(Fetch));
  or or_6 (StackOveride, MWrite, MRead);
  not not_5 (not_5_out, d_ff_6_q);
  D_Flip_Flop #(.trigger("falling")) d_ff_6 (
    .D(d_ff_3_q), .clk(Execute), .Q(d_ff_6_q), .reset(Fetch));  // open: Qn, preset
  not not_6 (not_6_out, d_ff_5_q);
  assign PCinstOut_2 = and_5_out ? PC[7:0] : 8'bz;  // Controlled_Buffer controlled_buffer_6
  and and_7 (and_7_out, not_8_out, d_ff_6_q);
  D_Flip_Flop #(.trigger("falling")) d_ff_7 (
    .D(d_ff_6_q), .clk(Execute), .Q(d_ff_7_q), .reset(Fetch));  // open: Qn, preset
  not not_7 (not_7_out, d_ff_8_q);
  and and_8 (and_8_out, not_7_out, d_ff_5_q);
  D_Flip_Flop #(.trigger("falling")) d_ff_8 (
    .D(d_ff_5_q), .clk(Execute), .Q(d_ff_8_q), .reset(Fetch));  // open: Qn, preset
  assign PCinstOut_2 = and_8_out ? subtractor_1_out : 8'bz;  // Controlled_Buffer controlled_buffer_7
  not not_8 (not_8_out, d_ff_7_q);
  assign PCinstOut_2 = and_7_out ? StackPointer : 8'bz;  // Controlled_Buffer controlled_buffer_8
  and and_9 (and_9_out, not_10_out, d_ff_7_q);
  D_Flip_Flop #(.trigger("falling")) d_ff_9 (
    .D(d_ff_7_q), .clk(Execute), .Q(d_ff_9_q), .reset(Fetch));  // open: Qn, preset
  not not_9 (not_9_out, d_ff_10_q);
  and and_10 (and_10_out, not_9_out, d_ff_8_q);
  D_Flip_Flop #(.trigger("falling")) d_ff_10 (
    .D(d_ff_8_q), .clk(Execute), .Q(d_ff_10_q), .reset(Fetch));  // open: Qn, preset
  assign PCinstOut_2 = and_10_out ? StackPointer : 8'bz;  // Controlled_Buffer controlled_buffer_9
  not not_10 (not_10_out, d_ff_9_q);
  assign PCinstOut_2 = and_9_out ? adder_1_out : 8'bz;  // Controlled_Buffer controlled_buffer_10
  not not_11 (not_11_out, d_ff_11_q);
  and and_11 (and_11_out, not_11_out, d_ff_9_q);
  D_Flip_Flop #(.trigger("falling")) d_ff_11 (
    .D(d_ff_9_q), .clk(Execute), .Q(d_ff_11_q), .reset(Fetch));  // open: Qn, preset
  not not_12 (not_12_out, d_ff_12_q);
  and and_12 (and_12_out, not_12_out, d_ff_10_q);
  D_Flip_Flop #(.trigger("falling")) d_ff_12 (
    .D(d_ff_10_q), .clk(Execute), .Q(d_ff_12_q), .reset(Fetch));  // open: Qn, preset
  Register #(.trigger("falling")) register_3 (
    .D(InstIn), .en(and_12_out), .clk(Execute), .Q(register_3_q), .clr(Fetch));
  assign PCinstOut_2 = and_11_out ? PC[15:8] : 8'bz;  // Controlled_Buffer controlled_buffer_11
  assign PCinstOut = d_ff_12_q ? {register_2_q, register_3_q} : 16'bz;  // Controlled_Buffer controlled_buffer_12
  or or_7 (InstDone, JMP, d_ff_12_q, d_ff_11_q);
  or or_8 (MRead, and_12_out, and_6_out);
  assign PCinstOut = d_ff_11_q ? register_1_q : 16'bz;  // Controlled_Buffer controlled_buffer_13

  assign PCWrite = InstDone;
endmodule

module BranchInstructions (
  input  [7:0] P,
  input  [15:0] PC,
  input  [7:0] LowByte,
  input  BCC,
  input  BCS,
  input  BNE,
  input  BEQ,
  input  BPL,
  input  BMI,
  input  BVC,
  input  BVS,
  output PCWrite,
  output [15:0] INSTPCOut,
  output InstDone
);

  wire and_1_out, and_2_out, and_3_out, and_4_out, and_5_out, and_6_out, and_7_out, and_8_out, not_1_out,
       not_2_out, not_3_out, not_4_out, or_1_out, or_2_out, or_3_out, or_4_out, or_5_out, or_6_out, or_7_out,
       or_8_out, or_9_out, or_10_out, or_11_out, or_12_out;
  wire [15:0] controlled_buffer_1_out, controlled_buffer_9_out;

  not not_1 (not_1_out, P[7]);
  and and_1 (and_1_out, not_1_out, BCC);
  assign controlled_buffer_1_out = and_1_out ? PC : 16'bz;  // Controlled_Buffer controlled_buffer_1
  and and_2 (and_2_out, P[7], BCS);
  assign controlled_buffer_1_out = and_2_out ? PC : 16'bz;  // Controlled_Buffer controlled_buffer_2
  or or_1 (or_1_out, BCC, BCS);
  not not_2 (not_2_out, P[6]);
  and and_3 (and_3_out, not_2_out, BNE);
  or or_2 (or_2_out, and_2_out, and_1_out);
  assign controlled_buffer_1_out = and_3_out ? PC : 16'bz;  // Controlled_Buffer controlled_buffer_3
  or or_3 (or_3_out, or_1_out, BNE);
  and and_4 (and_4_out, P[6], BEQ);
  or or_4 (or_4_out, or_2_out, and_3_out);
  assign controlled_buffer_1_out = and_4_out ? PC : 16'bz;  // Controlled_Buffer controlled_buffer_4
  or or_5 (or_5_out, or_3_out, BEQ);
  not not_3 (not_3_out, P[1]);
  and and_5 (and_5_out, not_3_out, BPL);
  or or_6 (or_6_out, or_4_out, and_4_out);
  assign controlled_buffer_1_out = and_5_out ? PC : 16'bz;  // Controlled_Buffer controlled_buffer_5
  or or_7 (or_7_out, or_5_out, BPL);
  and and_6 (and_6_out, P[1], BMI);
  or or_8 (or_8_out, or_6_out, and_5_out);
  assign controlled_buffer_1_out = and_6_out ? PC : 16'bz;  // Controlled_Buffer controlled_buffer_6
  or or_9 (or_9_out, or_7_out, BMI);
  not not_4 (not_4_out, P[2]);
  and and_7 (and_7_out, not_4_out, BVC);
  or or_10 (or_10_out, or_8_out, and_6_out);
  assign controlled_buffer_1_out = and_7_out ? PC : 16'bz;  // Controlled_Buffer controlled_buffer_7
  or or_11 (or_11_out, or_9_out, BVC);
  and and_8 (and_8_out, P[2], BVS);
  or or_12 (or_12_out, or_10_out, and_7_out);
  assign controlled_buffer_1_out = and_8_out ? PC : 16'bz;  // Controlled_Buffer controlled_buffer_8
  or or_13 (InstDone, or_11_out, BVS);
  or or_14 (PCWrite, or_12_out, and_8_out);
  assign controlled_buffer_9_out = PCWrite ? {{8{1'b0}}, LowByte} : 16'bz;  // Controlled_Buffer controlled_buffer_9
  Adder #(.width(16)) adder_1 (
    .a(controlled_buffer_1_out), .b(controlled_buffer_9_out), .out(INSTPCOut));  // open: cin, cout
endmodule

module FlagInstructions (
  input  CLC,
  input  CLD,
  input  CLI,
  input  CLV,
  input  SEC,
  input  SED,
  input  SEI,
  output ClearCarry,
  output ClearDecimal,
  output ClearInterupt,
  output ClearOverflow,
  output SetCarry,
  output SetDecimal,
  output SetInterupt,
  output InstDone
);

  wire or_1_out, or_2_out, or_3_out, or_4_out, or_5_out;

  or or_1 (or_1_out, CLC, CLD);
  or or_2 (or_2_out, or_1_out, CLI);
  or or_3 (or_3_out, or_2_out, CLV);
  or or_4 (or_4_out, or_3_out, SEC);
  or or_5 (or_5_out, or_4_out, SED);
  or or_6 (InstDone, or_5_out, SEI);

  assign ClearCarry = CLC;
  assign ClearDecimal = CLD;
  assign ClearInterupt = CLI;
  assign ClearOverflow = CLV;
  assign SetCarry = SEC;
  assign SetDecimal = SED;
  assign SetInterupt = SEI;
endmodule

module RotationInstruction (
  input  AccumulatorTrigger,
  input  [7:0] A,
  input  [7:0] LowByte,
  input  Carry,
  input  ASL,
  input  ROL,
  input  LSR,
  input  ROR,
  output AWrite,
  output MWrite,
  output PCOFF,
  output InstDone,
  output [7:0] InstructionOut,
  output CarryFlag
);

  wire and_1_out, and_2_out, and_3_out, and_4_out, and_5_out, and_7_out, not_1_out, not_2_out, or_2_out,
       or_3_out, or_5_out, or_7_out;
  wire [0:0] or_1_out;
  wire [7:0] controlled_buffer_1_out;
  wire [7:7] or_4_out;

  assign controlled_buffer_1_out = AccumulatorTrigger ? A : 8'bz;  // Controlled_Buffer controlled_buffer_1
  not not_1 (not_1_out, AccumulatorTrigger);
  assign controlled_buffer_1_out = not_1_out ? LowByte : 8'bz;  // Controlled_Buffer controlled_buffer_2
  and and_1 (and_1_out, Carry, ROL);
  and and_2 (and_2_out, 1'b0, ASL);
  or or_1 (or_1_out[0], and_2_out, and_1_out);
  or or_2 (or_2_out, ROL, ASL);
  assign InstructionOut = or_3_out ? {controlled_buffer_1_out[6:0], or_1_out[0]} : 8'bz;  // Controlled_Buffer controlled_buffer_3
  and and_3 (and_3_out, controlled_buffer_1_out[7], or_3_out);
  or or_3 (or_3_out, ROL, ASL);
  and and_4 (and_4_out, 1'b0, LSR);
  and and_5 (and_5_out, Carry, ROR);
  or or_4 (or_4_out[7], and_4_out, and_5_out);
  or or_5 (or_5_out, or_2_out, LSR);
  or or_6 (InstDone, or_5_out, ROR);
  or or_7 (or_7_out, ROR, LSR);
  and and_6 (AWrite, AccumulatorTrigger, InstDone);
  assign InstructionOut = or_7_out ? {or_4_out[7], controlled_buffer_1_out[7:1]} : 8'bz;  // Controlled_Buffer controlled_buffer_4
  and and_7 (and_7_out, controlled_buffer_1_out[0], or_7_out);
  or or_8 (CarryFlag, and_3_out, and_7_out);
  and and_8 (MWrite, not_2_out, InstDone);
  not not_2 (not_2_out, AccumulatorTrigger);

  assign PCOFF = MWrite;
endmodule

module LogicalInstructions (
  input  [7:0] Lowbyte,
  input  [7:0] A,
  input  AND,
  input  ORA,
  input  EOR,
  output AWrite,
  output InstructionDone,
  output [7:0] InstructionOut
);

  wire or_2_out;
  wire [7:0] and_1_out, or_1_out, xor_1_out;

  assign and_1_out = Lowbyte & A;  // AND_Gate and_1, 8 bits wide
  assign InstructionOut = AND ? and_1_out : 8'bz;  // Controlled_Buffer controlled_buffer_1
  assign or_1_out = Lowbyte | A;  // OR_Gate or_1, 8 bits wide
  assign InstructionOut = ORA ? or_1_out : 8'bz;  // Controlled_Buffer controlled_buffer_2
  assign xor_1_out = Lowbyte ^ A;  // XOR_Gate xor_1, 8 bits wide
  assign InstructionOut = EOR ? xor_1_out : 8'bz;  // Controlled_Buffer controlled_buffer_3
  or or_2 (or_2_out, AND, ORA);
  or or_3 (AWrite, or_2_out, EOR);

  assign InstructionDone = AWrite;
endmodule

module ArithmeticInstructions (
  input  [7:0] Y,
  input  [7:0] X,
  input  [7:0] A,
  input  [7:0] LowByte,
  input  CarryFlag,
  input  DecimalFlag,
  input  ADC,
  input  CMP,
  input  CPX,
  input  CPY,
  input  SBC,
  output AWrite,
  output InstructionDone,
  output [7:0] InstructionOutput,
  output CarryFlag_2,
  output OverflowFlag,
  output FlagFlag
);

  wire adder_1_cout, adder_2_cout, adder_3_cout, and_1_out, and_2_out, and_3_out, and_4_out, not_1_out,
       not_2_out, not_3_out, not_4_out, not_5_out, not_6_out, not_7_out, not_8_out, not_9_out, not_10_out,
       not_11_out, not_12_out, not_13_out, or_1_out, or_2_out, or_3_out, or_4_out, or_5_out, or_6_out,
       or_8_out, subtractor_1_bout, subtractor_2_bout, subtractor_3_bout, subtractor_4_bout,
       subtractor_5_bout, subtractor_6_bout, subtractor_7_bout, subtractor_8_bout, subtractor_9_bout;
  wire [3:0] adder_2_out, adder_3_out, controlled_buffer_1_out, controlled_buffer_2_out,
       controlled_buffer_12_out, controlled_buffer_13_out, controlled_buffer_14_out,
       controlled_buffer_15_out, controlled_buffer_21_out, controlled_buffer_23_out, subtractor_1_out,
       subtractor_2_out, subtractor_4_out, subtractor_5_out, subtractor_6_out, subtractor_7_out,
       subtractor_8_out, subtractor_9_out, subtractor_10_out, subtractor_11_out;
  wire [7:0] adder_1_out, controlled_buffer_3_out, controlled_buffer_8_out, controlled_buffer_20_out,
       subtractor_3_out;

  and and_1 (and_1_out, ADC, CarryFlag);
  Adder adder_1 (.a(A), .b(LowByte), .out(adder_1_out), .cin(and_1_out), .cout(adder_1_cout));
  and and_2 (and_2_out, ADC, CarryFlag);
  Adder #(.width(4)) adder_2 (.a(A[3:0]), .b(LowByte[3:0]), .out(adder_2_out), .cin(and_2_out), .cout(adder_2_cout));
  not not_1 (not_1_out, subtractor_1_bout);
  or or_1 (or_1_out, adder_2_cout, not_1_out);
  Adder #(.width(4)) adder_3 (.a(A[7:4]), .b(LowByte[7:4]), .out(adder_3_out), .cin(or_1_out), .cout(adder_3_cout));
  or or_2 (or_2_out, adder_3_cout, adder_1_cout);
  not not_2 (not_2_out, CarryFlag);
  Subtractor #(.width(4)) subtractor_1 (
    .a(adder_2_out), .b(4'b1010), .out(subtractor_1_out), .bout(subtractor_1_bout));  // open: bin
  assign controlled_buffer_1_out = not_3_out ? subtractor_1_out : 4'bz;  // Controlled_Buffer controlled_buffer_1
  not not_3 (not_3_out, subtractor_1_bout);
  assign controlled_buffer_2_out = not_4_out ? subtractor_2_out : 4'bz;  // Controlled_Buffer controlled_buffer_2
  Subtractor #(.width(4)) subtractor_2 (
    .a(adder_3_out), .b(4'b1010), .out(subtractor_2_out), .bout(subtractor_2_bout));  // open: bin
  not not_4 (not_4_out, subtractor_2_bout);
  not not_5 (not_5_out, DecimalFlag);
  assign controlled_buffer_3_out = not_5_out ? adder_1_out : 8'bz;  // Controlled_Buffer controlled_buffer_3
  assign controlled_buffer_1_out = subtractor_1_bout ? adder_2_out : 4'bz;  // Controlled_Buffer controlled_buffer_4
  assign controlled_buffer_2_out = subtractor_2_bout ? adder_3_out : 4'bz;  // Controlled_Buffer controlled_buffer_5
  assign InstructionOutput = ADC ? controlled_buffer_3_out : 8'bz;  // Controlled_Buffer controlled_buffer_6
  assign controlled_buffer_3_out = DecimalFlag ? {controlled_buffer_2_out, controlled_buffer_1_out} : 8'bz;  // Controlled_Buffer controlled_buffer_7
  assign controlled_buffer_8_out = SBC ? A : 8'bz;  // Controlled_Buffer controlled_buffer_8
  assign controlled_buffer_8_out = CMP ? A : 8'bz;  // Controlled_Buffer controlled_buffer_9
  assign controlled_buffer_8_out = CPX ? X : 8'bz;  // Controlled_Buffer controlled_buffer_10
  or or_3 (or_3_out, CMP, CPX);
  assign controlled_buffer_8_out = CPY ? Y : 8'bz;  // Controlled_Buffer controlled_buffer_11
  or or_4 (or_4_out, or_3_out, CPY);
  and and_3 (and_3_out, SBC, not_2_out);
  Subtractor subtractor_3 (
    .a(controlled_buffer_8_out), .b(LowByte), .out(subtractor_3_out), .bin(and_3_out),
    .bout(subtractor_3_bout));
  or or_5 (or_5_out, subtractor_3_bout, or_2_out);
  and and_4 (and_4_out, SBC, not_2_out);
  Subtractor #(.width(4)) subtractor_4 (
    .a(A[3:0]), .b(LowByte[3:0]), .out(subtractor_4_out), .bin(and_4_out), .bout(subtractor_4_bout));
  or or_6 (or_6_out, subtractor_4_bout, subtractor_3_bout);
  not not_6 (not_6_out, subtractor_6_bout);
  or or_7 (AWrite, ADC, SBC);
  or or_8 (or_8_out, not_6_out, or_6_out);
  Subtractor #(.width(4)) subtractor_5 (
    .a(A[7:4]), .b(LowByte[7:4]), .out(subtractor_5_out), .bin(or_8_out), .bout(subtractor_5_bout));
  or or_9 (CarryFlag_2, subtractor_5_bout, or_5_out);
  or or_10 (InstructionDone, AWrite, or_4_out);
  assign controlled_buffer_12_out = not_7_out ? subtractor_6_out : 4'bz;  // Controlled_Buffer controlled_buffer_12
  Subtractor #(.width(4)) subtractor_6 (
    .a(subtractor_4_out), .b(4'b1010), .out(subtractor_6_out), .bout(subtractor_6_bout));  // open: bin
  not not_7 (not_7_out, subtractor_6_bout);
  assign controlled_buffer_13_out = not_8_out ? subtractor_7_out : 4'bz;  // Controlled_Buffer controlled_buffer_13
  Subtractor #(.width(4)) subtractor_7 (
    .a(subtractor_4_out), .b(4'b0110), .out(subtractor_7_out), .bout(subtractor_7_bout));  // open: bin
  not not_8 (not_8_out, subtractor_7_bout);
  Subtractor #(.width(4)) subtractor_8 (
    .a(subtractor_5_out), .b(4'b1010), .out(subtractor_8_out), .bout(subtractor_8_bout));  // open: bin
  assign controlled_buffer_14_out = not_9_out ? subtractor_8_out : 4'bz;  // Controlled_Buffer controlled_buffer_14
  not not_9 (not_9_out, subtractor_8_bout);
  Subtractor #(.width(4)) subtractor_9 (
    .a(subtractor_5_out), .b(4'b0110), .out(subtractor_9_out), .bout(subtractor_9_bout));  // open: bin
  assign controlled_buffer_15_out = not_10_out ? subtractor_9_out : 4'bz;  // Controlled_Buffer controlled_buffer_15
  not not_10 (not_10_out, subtractor_9_bout);
  assign controlled_buffer_12_out = subtractor_6_bout ? subtractor_4_out : 4'bz;  // Controlled_Buffer controlled_buffer_16
  assign controlled_buffer_13_out = subtractor_7_bout ? subtractor_10_out : 4'bz;  // Controlled_Buffer controlled_buffer_17
  Subtractor #(.width(4)) subtractor_10 (
    .a(subtractor_4_out), .b(4'b1010), .out(subtractor_10_out));  // open: bin, bout
  assign controlled_buffer_14_out = subtractor_8_bout ? subtractor_5_out : 4'bz;  // Controlled_Buffer controlled_buffer_18
  assign controlled_buffer_15_out = subtractor_9_bout ? subtractor_11_out : 4'bz;  // Controlled_Buffer controlled_buffer_19
  Subtractor #(.width(4)) subtractor_11 (
    .a(subtractor_5_out), .b(4'b1010), .out(subtractor_11_out));  // open: bin, bout
  not not_11 (not_11_out, DecimalFlag);
  assign controlled_buffer_20_out = not_11_out ? subtractor_3_out : 8'bz;  // Controlled_Buffer controlled_buffer_20
  assign controlled_buffer_21_out = not_12_out ? controlled_buffer_12_out : 4'bz;  // Controlled_Buffer controlled_buffer_21
  not not_12 (not_12_out, or_6_out);
  assign controlled_buffer_21_out = or_6_out ? controlled_buffer_13_out : 4'bz;  // Controlled_Buffer controlled_buffer_22
  assign controlled_buffer_23_out = not_13_out ? controlled_buffer_14_out : 4'bz;  // Controlled_Buffer controlled_buffer_23
  not not_13 (not_13_out, subtractor_5_bout);
  assign controlled_buffer_23_out = subtractor_5_bout ? controlled_buffer_15_out : 4'bz;  // Controlled_Buffer controlled_buffer_24
  assign InstructionOutput = SBC ? controlled_buffer_20_out : 8'bz;  // Controlled_Buffer controlled_buffer_25
  assign controlled_buffer_20_out = DecimalFlag ? {controlled_buffer_23_out, controlled_buffer_21_out} : 8'bz;  // Controlled_Buffer controlled_buffer_26
  or or_11 (FlagFlag, ADC, SBC);
  assign InstructionOutput = or_4_out ? controlled_buffer_20_out : 8'bz;  // Controlled_Buffer controlled_buffer_27
  xor xor_1 (OverflowFlag, LowByte[0], InstructionOutput[7]);
endmodule

module IncrementInstructions (
  input  [7:0] X,
  input  [7:0] Y,
  input  [7:0] LowByte,
  input  INX,
  input  INY,
  input  INC,
  input  DEX,
  input  DEY,
  input  DEC,
  output XWrite,
  output YWrite,
  output MWrite,
  output PCOFF,
  output [7:0] InstOut,
  output InstDone
);

  wire or_3_out, or_4_out, or_6_out, or_7_out, or_8_out, or_9_out, or_10_out, or_12_out;
  wire [7:0] adder_1_out, controlled_buffer_1_out, controlled_buffer_5_out, subtractor_1_out;

  or or_1 (XWrite, DEX, INX);
  assign controlled_buffer_1_out = DEX ? X : 8'bz;  // Controlled_Buffer controlled_buffer_1
  assign controlled_buffer_1_out = DEY ? Y : 8'bz;  // Controlled_Buffer controlled_buffer_2
  or or_2 (YWrite, DEY, INY);
  assign controlled_buffer_1_out = DEC ? LowByte : 8'bz;  // Controlled_Buffer controlled_buffer_3
  or or_3 (or_3_out, DEX, DEY);
  or or_4 (or_4_out, DEX, DEY);
  or or_5 (MWrite, DEC, INC);
  or or_6 (or_6_out, or_3_out, DEC);
  or or_7 (or_7_out, or_4_out, DEC);
  Subtractor subtractor_1 (.a(controlled_buffer_1_out), .b(8'h1), .out(subtractor_1_out));  // open: bin, bout
  assign InstOut = or_7_out ? subtractor_1_out : 8'bz;  // Controlled_Buffer controlled_buffer_4
  assign controlled_buffer_5_out = INX ? X : 8'bz;  // Controlled_Buffer controlled_buffer_5
  or or_8 (or_8_out, or_6_out, INX);
  assign controlled_buffer_5_out = INY ? Y : 8'bz;  // Controlled_Buffer controlled_buffer_6
  assign controlled_buffer_5_out = INC ? LowByte : 8'bz;  // Controlled_Buffer controlled_buffer_7
  or or_9 (or_9_out, or_8_out, INY);
  or or_10 (or_10_out, INX, INY);
  or or_11 (InstDone, or_9_out, INC);
  or or_12 (or_12_out, or_10_out, INC);
  Adder adder_1 (.a(controlled_buffer_5_out), .b(8'h1), .out(adder_1_out));  // open: cin, cout
  assign InstOut = or_12_out ? adder_1_out : 8'bz;  // Controlled_Buffer controlled_buffer_8

  assign PCOFF = MWrite;
endmodule

module StackInstructions (
  input  Execute,
  input  Fetch,
  input  [7:0] StackPointer,
  input  [7:0] StatusRegister,
  input  [7:0] Accumulator,
  input  PHA,
  input  PHP,
  input  PLA,
  input  PLP,
  output StackStack,
  output Swrite,
  output StackOveride,
  output MWrite,
  output MRead,
  output AWrite,
  output StatusWrite,
  output InstDone,
  output [7:0] InstructionOut,
  output FlagFlag
);

  wire and_1_out, and_2_out, and_3_out, and_4_out, and_5_out, and_6_out, and_7_out, and_8_out, and_9_out,
       and_10_out, and_11_out, and_12_out, and_13_out, and_14_out, and_16_out, and_17_out, d_ff_1_q,
       not_1_out, not_2_out, not_3_out, not_4_out, or_3_out, or_4_out, or_5_out, or_6_out, or_7_out;
  wire [7:0] adder_1_out, subtractor_1_out;

  and and_1 (and_1_out, and_2_out, not_1_out);
  and and_2 (and_2_out, or_3_out, or_4_out);
  D_Flip_Flop #(.trigger("falling")) d_ff_1 (
    .D(or_4_out), .clk(Execute), .Q(d_ff_1_q), .reset(Fetch));  // open: Qn, preset
  or or_1 (StackStack, and_1_out, and_11_out);
  and and_3 (and_3_out, and_4_out, not_1_out);
  and and_4 (and_4_out, or_6_out, or_4_out);
  not not_1 (not_1_out, d_ff_1_q);
  not not_2 (not_2_out, d_ff_1_q);
  Subtractor subtractor_1 (.a(StackPointer), .b(8'h1), .out(subtractor_1_out));  // open: bin, bout
  and and_5 (and_5_out, or_3_out, and_7_out);
  assign InstructionOut = and_5_out ? StackPointer : 8'bz;  // Controlled_Buffer controlled_buffer_1
  and and_6 (and_6_out, or_3_out, d_ff_1_q);
  and and_7 (and_7_out, not_2_out, not_4_out);
  and and_8 (and_8_out, and_7_out, or_6_out);
  assign InstructionOut = and_8_out ? subtractor_1_out : 8'bz;  // Controlled_Buffer controlled_buffer_2
  or or_2 (Swrite, and_9_out, and_3_out);
  and and_9 (and_9_out, and_6_out, not_3_out);
  and and_10 (and_10_out, or_6_out, d_ff_1_q);
  and and_11 (and_11_out, and_10_out, not_3_out);
  Adder adder_1 (.a(StackPointer), .b(8'h1), .out(adder_1_out));  // open: cin, cout
  not not_3 (not_3_out, InstDone);
  D_Flip_Flop #(.trigger("falling")) d_ff_2 (
    .D(d_ff_1_q), .clk(Execute), .Q(InstDone), .reset(Fetch));  // open: Qn, preset
  not not_4 (not_4_out, InstDone);
  and and_12 (and_12_out, d_ff_1_q, not_4_out);
  and and_13 (and_13_out, or_3_out, and_12_out);
  assign InstructionOut = and_13_out ? adder_1_out : 8'bz;  // Controlled_Buffer controlled_buffer_3
  and and_14 (and_14_out, and_12_out, or_6_out);
  assign InstructionOut = and_14_out ? StackPointer : 8'bz;  // Controlled_Buffer controlled_buffer_4
  and and_15 (MWrite, InstDone, or_3_out);
  or or_3 (or_3_out, PHP, PHA);
  or or_4 (or_4_out, or_5_out, PHA);
  assign InstructionOut = and_16_out ? Accumulator : 8'bz;  // Controlled_Buffer controlled_buffer_5
  and and_16 (and_16_out, PHA, InstDone);
  or or_5 (or_5_out, or_7_out, PHP);
  assign InstructionOut = and_17_out ? StatusRegister : 8'bz;  // Controlled_Buffer controlled_buffer_6
  and and_17 (and_17_out, PHP, InstDone);
  and and_18 (MRead, or_6_out, InstDone);
  or or_6 (or_6_out, PLP, PLA);
  or or_7 (or_7_out, PLP, PLA);
  and and_19 (AWrite, PLA, InstDone);
  and and_20 (StatusWrite, PLP, InstDone);

  assign FlagFlag = PLA;
  assign StackOveride = InstDone;
endmodule

module TransferInstructions (
  input  [7:0] x,
  input  [7:0] y,
  input  [7:0] a,
  input  [7:0] s,
  input  [7:0] M,
  input  STA,
  input  LDA,
  input  STY,
  input  LDY,
  input  TAX,
  input  TAY,
  input  TXS,
  input  STX,
  input  LDX,
  input  TXA,
  input  TYA,
  input  TSX,
  output [7:0] out_18,
  output MWrite,
  output PCOFF,
  output XWrite,
  output YWrite,
  output AWrite,
  output SWrite,
  output TransferInstructionDone,
  output FlagFlag
);

  wire or_1_out, or_2_out, or_3_out, or_4_out, or_5_out, or_6_out, or_7_out;

  assign out_18 = STA ? a : 8'bz;  // Controlled_Buffer controlled_buffer_1
  assign out_18 = STY ? y : 8'bz;  // Controlled_Buffer controlled_buffer_2
  assign out_18 = STX ? x : 8'bz;  // Controlled_Buffer controlled_buffer_3
  or or_1 (or_1_out, STA, STY, STX);
  assign out_18 = LDA ? M : 8'bz;  // Controlled_Buffer controlled_buffer_4
  assign out_18 = LDY ? M : 8'bz;  // Controlled_Buffer controlled_buffer_5
  assign out_18 = LDX ? M : 8'bz;  // Controlled_Buffer controlled_buffer_6
  assign out_18 = TAX ? a : 8'bz;  // Controlled_Buffer controlled_buffer_7
  or or_2 (or_2_out, LDA, LDY, or_1_out, LDX);
  or or_3 (or_3_out, LDA, LDY, LDX);
  assign out_18 = TAY ? a : 8'bz;  // Controlled_Buffer controlled_buffer_8
  assign out_18 = TXA ? x : 8'bz;  // Controlled_Buffer controlled_buffer_9
  or or_4 (or_4_out, TAX, or_2_out, TXA);
  or or_5 (or_5_out, TAX, or_3_out, TXA);
  assign out_18 = TYA ? y : 8'bz;  // Controlled_Buffer controlled_buffer_10
  or or_6 (or_6_out, TAY, or_4_out, TYA);
  or or_7 (or_7_out, TAY, or_5_out, TYA);
  assign out_18 = TXS ? x : 8'bz;  // Controlled_Buffer controlled_buffer_11
  assign out_18 = TSX ? s : 8'bz;  // Controlled_Buffer controlled_buffer_12
  or or_8 (XWrite, LDX, TAX, TSX);
  or or_9 (FlagFlag, TXS, or_7_out, TSX);
  or or_10 (TransferInstructionDone, TXS, or_6_out, TSX);
  or or_11 (YWrite, LDY, TAY);
  or or_12 (AWrite, LDA, TXA, TYA);
  or or_13 (MWrite, STA, STY, STX);

  assign PCOFF = MWrite;
  assign SWrite = TXS;
endmodule
