// Logisim project flag_instructions.circ as structural Verilog: 1 circuit, main circuit main
module main (
  input  CLC,
  input  CLD,
  input  CLI,
  input  CLV,
  input  SEC,
  input  SED,
  input  SEI,
  output ClearCarry,
  output ClearDecimal,
  output ClearInterupt,
  output ClearOverflow,
  output SetCarry,
  output SetDecimal,
  output SetInterupt,
  output InstDone
);

  wire or_1_out, or_2_out, or_3_out, or_4_out, or_5_out;

  or or_1 (or_1_out, CLC, CLD);
  or or_2 (or_2_out, or_1_out, CLI);
  or or_3 (or_3_out, or_2_out, CLV);
  or or_4 (or_4_out, or_3_out, SEC);
  or or_5 (or_5_out, or_4_out, SED);
  or or_6 (InstDone, or_5_out, SEI);

  assign ClearCarry = CLC;
  assign ClearDecimal = CLD;
  assign ClearInterupt = CLI;
  assign ClearOverflow = CLV;
  assign SetCarry = SEC;
  assign SetDecimal = SED;
  assign SetInterupt = SEI;
endmodule
