// Logisim project increment_instructions.circ as structural Verilog: 1 circuit, main circuit main
module main (
  input  [7:0] X,
  input  [7:0] Y,
  input  [7:0] LowByte,
  input  INX,
  input  INY,
  input  INC,
  input  DEX,
  input  DEY,
  input  DEC,
  output XWrite,
  output YWrite,
  output MWrite,
  output PCOFF,
  output [7:0] InstOut,
  output InstDone
);

  wire or_3_out, or_4_out, or_6_out, or_7_out, or_8_out, or_9_out, or_10_out, or_12_out;
  wire [7:0] adder_1_out, controlled_buffer_1_out, controlled_buffer_5_out, subtractor_1_out;

  or or_1 (XWrite, DEX, INX);
  assign controlled_buffer_1_out = DEX ? X : 8'bz;  // Controlled_Buffer controlled_buffer_1
  assign controlled_buffer_1_out = DEY ? Y : 8'bz;  // Controlled_Buffer controlled_buffer_2
  or or_2 (YWrite, DEY, INY);
  assign controlled_buffer_1_out = DEC ? LowByte : 8'bz;  // Controlled_Buffer controlled_buffer_3
  or or_3 (or_3_out, DEX, DEY);
  or or_4 (or_4_out, DEX, DEY);
  or or_5 (MWrite, DEC, INC);
  or or_6 (or_6_out, or_3_out, DEC);
  or or_7 (or_7_out, or_4_out, DEC);
  Subtractor subtractor_1 (.a(controlled_buffer_1_out), .b(8'h1), .out(subtractor_1_out));  // open: bin, bout
  assign InstOut = or_7_out ? subtractor_1_out : 8'bz;  // Controlled_Buffer controlled_buffer_4
  assign controlled_buffer_5_out = INX ? X : 8'bz;  // Controlled_Buffer controlled_buffer_5
  or or_8 (or_8_out, or_6_out, INX);
  assign controlled_buffer_5_out = INY ? Y : 8'bz;  // Controlled_Buffer controlled_buffer_6
  assign controlled_buffer_5_out = INC ? LowByte : 8'bz;  // Controlled_Buffer controlled_buffer_7
  or or_9 (or_9_out, or_8_out, INY);
  or or_10 (or_10_out, INX, INY);
  or or_11 (InstDone, or_9_out, INC);
  or or_12 (or_12_out, or_10_out, INC);
  Adder adder_1 (.a(controlled_buffer_5_out), .b(8'h1), .out(adder_1_out));  // open: cin, cout
  assign InstOut = or_12_out ? adder_1_out : 8'bz;  // Controlled_Buffer controlled_buffer_8

  assign PCOFF = MWrite;
endmodule
