// Logisim project interupt_instructions.circ as structural Verilog: 1 circuit, main circuit main
module main (
  input  Execute,
  input  Fetch,
  input  [15:0] PC,
  input  [7:0] P,
  input  [7:0] StackPointer,
  input  [7:0] InstIn,
  input  BRK,
  input  RTI,
  output MWrite,
  output StackOveride,
  output MRead,
  output PWrite,
  output PCWrite,
  output Break,
  output StackStack,
  output SWrite,
  output InstDone,
  output [7:0] InstOut,
  output [15:0] PCinstOut
);

  wire and_1_out, and_2_out, and_3_out, and_4_out, and_5_out, and_7_out, and_8_out, and_9_out, and_10_out,
       and_11_out, and_12_out, and_13_out, and_14_out, and_15_out, and_16_out, and_17_out, and_18_out,
       d_ff_1_q, d_ff_2_q, d_ff_3_q, d_ff_4_q, d_ff_5_q, d_ff_6_q, d_ff_7_q, d_ff_8_q, d_ff_9_q, d_ff_10_q,
       d_ff_11_q, d_ff_12_q, d_ff_13_q, d_ff_14_q, d_ff_15_q, d_ff_16_q, not_1_out, not_2_out, not_3_out,
       not_4_out, not_5_out, not_6_out, not_7_out, not_8_out, not_9_out, not_10_out, not_11_out, not_12_out,
       not_13_out, not_14_out, not_15_out, not_16_out, not_17_out, not_18_out, or_5_out, or_6_out;
  wire [7:0] adder_1_out, register_1_q, register_2_q, subtractor_1_out;

  or or_1 (StackStack, and_1_out, and_7_out, and_13_out, or_6_out);
  not not_1 (not_1_out, d_ff_1_q);
  and and_1 (and_1_out, not_1_out, BRK);
  D_Flip_Flop #(.trigger("falling")) d_ff_1 (.D(BRK), .clk(Execute), .Q(d_ff_1_q), .reset(Fetch));  // open: Qn, preset
  assign InstOut = and_1_out ? StackPointer : 8'bz;  // Controlled_Buffer controlled_buffer_1
  Adder adder_1 (.a(StackPointer), .b(8'h1), .out(adder_1_out));  // open: cin, cout
  Subtractor subtractor_1 (.a(StackPointer), .b(8'h1), .out(subtractor_1_out));  // open: bin, bout
  not not_2 (not_2_out, d_ff_2_q);
  and and_2 (and_2_out, not_2_out, RTI);
  D_Flip_Flop #(.trigger("falling")) d_ff_2 (.D(RTI), .clk(Execute), .Q(d_ff_2_q), .reset(Fetch));  // open: Qn, preset
  assign InstOut = and_2_out ? subtractor_1_out : 8'bz;  // Controlled_Buffer controlled_buffer_2
  or or_2 (SWrite, and_3_out, and_9_out, and_15_out, or_5_out);
  not not_3 (not_3_out, d_ff_3_q);
  and and_3 (and_3_out, not_3_out, d_ff_1_q);
  D_Flip_Flop #(.trigger("falling")) d_ff_3 (
    .D(d_ff_1_q), .clk(Execute), .Q(d_ff_3_q), .reset(Fetch));  // open: Qn, preset
  assign InstOut = and_3_out ? adder_1_out : 8'bz;  // Controlled_Buffer controlled_buffer_3
  and and_4 (and_4_out, not_4_out, d_ff_2_q);
  and and_5 (and_5_out, not_5_out, d_ff_3_q);
  not not_4 (not_4_out, d_ff_4_q);
  D_Flip_Flop #(.trigger("falling")) d_ff_4 (
    .D(d_ff_2_q), .clk(Execute), .Q(d_ff_4_q), .reset(Fetch));  // open: Qn, preset
  assign InstOut = and_4_out ? StackPointer : 8'bz;  // Controlled_Buffer controlled_buffer_4
  or or_3 (MWrite, and_5_out, and_11_out, and_17_out);
  not not_5 (not_5_out, d_ff_5_q);
  D_Flip_Flop #(.trigger("falling")) d_ff_5 (
    .D(d_ff_3_q), .clk(Execute), .Q(d_ff_5_q), .reset(Fetch));  // open: Qn, preset
  assign InstOut = and_5_out ? PC[7:0] : 8'bz;  // Controlled_Buffer controlled_buffer_5
  and and_6 (PWrite, not_6_out, d_ff_4_q);
  or or_4 (StackOveride, MWrite, MRead);
  and and_7 (and_7_out, not_7_out, d_ff_5_q);
  assign InstOut = and_7_out ? StackPointer : 8'bz;  // Controlled_Buffer controlled_buffer_6
  not not_6 (not_6_out, d_ff_6_q);
  D_Flip_Flop #(.trigger("falling")) d_ff_6 (
    .D(d_ff_4_q), .clk(Execute), .Q(d_ff_6_q), .reset(Fetch));  // open: Qn, preset
  not not_7 (not_7_out, d_ff_7_q);
  D_Flip_Flop #(.trigger("falling")) d_ff_7 (
    .D(d_ff_5_q), .clk(Execute), .Q(d_ff_7_q), .reset(Fetch));  // open: Qn, preset
  and and_8 (and_8_out, not_9_out, d_ff_6_q);
  D_Flip_Flop #(.trigger("falling")) d_ff_8 (
    .D(d_ff_6_q), .clk(Execute), .Q(d_ff_8_q), .reset(Fetch));  // open: Qn, preset
  assign InstOut = and_8_out ? subtractor_1_out : 8'bz;  // Controlled_Buffer controlled_buffer_7
  not not_8 (not_8_out, d_ff_9_q);
  and and_9 (and_9_out, not_8_out, d_ff_7_q);
  D_Flip_Flop #(.trigger("falling")) d_ff_9 (
    .D(d_ff_7_q), .clk(Execute), .Q(d_ff_9_q), .reset(Fetch));  // open: Qn, preset
  assign InstOut = and_9_out ? adder_1_out : 8'bz;  // Controlled_Buffer controlled_buffer_8
  not not_9 (not_9_out, d_ff_8_q);
  not not_10 (not_10_out, d_ff_10_q);
  and and_10 (and_10_out, not_10_out, d_ff_8_q);
  D_Flip_Flop #(.trigger("falling")) d_ff_10 (
    .D(d_ff_8_q), .clk(Execute), .Q(d_ff_10_q), .reset(Fetch));  // open: Qn, preset
  assign InstOut = and_10_out ? StackPointer : 8'bz;  // Controlled_Buffer controlled_buffer_9
  not not_11 (not_11_out, d_ff_11_q);
  and and_11 (and_11_out, not_11_out, d_ff_9_q);
  D_Flip_Flop #(.trigger("falling")) d_ff_11 (
    .D(d_ff_9_q), .clk(Execute), .Q(d_ff_11_q), .reset(Fetch));  // open: Qn, preset
  assign InstOut = and_11_out ? PC[15:8] : 8'bz;  // Controlled_Buffer controlled_buffer_10
  and and_12 (and_12_out, not_12_out, d_ff_10_q);
  and and_13 (and_13_out, not_13_out, d_ff_11_q);
  not not_12 (not_12_out, d_ff_12_q);
  D_Flip_Flop #(.trigger("falling")) d_ff_12 (
    .D(d_ff_10_q), .clk(Execute), .Q(d_ff_12_q), .reset(Fetch));  // open: Qn, preset
  Register #(.trigger("falling")) register_1 (
    .D(InstIn), .en(and_12_out), .clk(Execute), .Q(register_1_q), .clr(Fetch));
  not not_13 (not_13_out, d_ff_13_q);
  D_Flip_Flop #(.trigger("falling")) d_ff_13 (
    .D(d_ff_11_q), .clk(Execute), .Q(d_ff_13_q), .reset(Fetch));  // open: Qn, preset
  assign InstOut = and_13_out ? StackPointer : 8'bz;  // Controlled_Buffer controlled_buffer_11
  or or_5 (or_5_out, and_8_out, and_2_out, and_14_out);
  and and_14 (and_14_out, not_14_out, d_ff_12_q);
  assign InstOut = and_14_out ? subtractor_1_out : 8'bz;  // Controlled_Buffer controlled_buffer_12
  and and_15 (and_15_out, not_15_out, d_ff_13_q);
  assign InstOut = and_15_out ? adder_1_out : 8'bz;  // Controlled_Buffer controlled_buffer_13
  not not_14 (not_14_out, d_ff_14_q);
  D_Flip_Flop #(.trigger("falling")) d_ff_14 (
    .D(d_ff_12_q), .clk(Execute), .Q(d_ff_14_q), .reset(Fetch));  // open: Qn, preset
  not not_15 (not_15_out, d_ff_15_q);
  D_Flip_Flop #(.trigger("falling")) d_ff_15 (
    .D(d_ff_13_q), .clk(Execute), .Q(d_ff_15_q), .reset(Fetch));  // open: Qn, preset
  or or_6 (or_6_out, and_10_out, and_4_out, and_16_out);
  and and_16 (and_16_out, not_16_out, d_ff_14_q);
  D_Flip_Flop #(.trigger("falling")) d_ff_16 (
    .D(d_ff_14_q), .clk(Execute), .Q(d_ff_16_q), .reset(Fetch));  // open: Qn, preset
  assign InstOut = and_16_out ? StackPointer : 8'bz;  // Controlled_Buffer controlled_buffer_14
  and and_17 (and_17_out, not_17_out, d_ff_15_q);
  D_Flip_Flop #(.trigger("falling")) d_ff_17 (
    .D(d_ff_15_q), .clk(Execute), .Q(Break), .reset(Fetch));  // open: Qn, preset
  assign InstOut = and_17_out ? P : 8'bz;  // Controlled_Buffer controlled_buffer_15
  not not_16 (not_16_out, d_ff_16_q);
  not not_17 (not_17_out, Break);
  or or_7 (MRead, and_12_out, PWrite, and_18_out);
  not not_18 (not_18_out, PCWrite);
  and and_18 (and_18_out, not_18_out, d_ff_16_q);
  D_Flip_Flop #(.trigger("falling")) d_ff_18 (
    .D(d_ff_16_q), .clk(Execute), .Q(PCWrite), .reset(Fetch));  // open: Qn, preset
  Register #(.trigger("falling")) register_2 (
    .D(InstIn), .en(and_18_out), .clk(Execute), .Q(register_2_q), .clr(Fetch));
  assign PCinstOut = PCWrite ? {register_1_q, register_2_q} : 16'bz;  // Controlled_Buffer controlled_buffer_16
  or or_8 (InstDone, Break, PCWrite);
endmodule
