// Logisim project jump_instructions.circ as structural Verilog: 1 circuit, main circuit main
module main (
  input  Execute,
  input  Fetch,
  input  [15:0] PCALT,
  input  [15:0] PC,
  input  [7:0] StackPointer,
  input  [7:0] InstIn,
  input  JMP,
  input  JSR,
  input  RTS,
  output StackStack,
  output SWrite,
  output MWrite,
  output StackOveride,
  output MRead,
  output PCWrite,
  output InstDone,
  output [15:0] PCinstOut,
  output [7:0] PCinstOut_2
);

  wire and_1_out, and_2_out, and_3_out, and_4_out, and_5_out, and_6_out, and_7_out, and_8_out, and_9_out,
       and_10_out, and_11_out, and_12_out, d_ff_1_q, d_ff_2_q, d_ff_3_q, d_ff_4_q, d_ff_5_q, d_ff_6_q,
       d_ff_7_q, d_ff_8_q, d_ff_9_q, d_ff_10_q, d_ff_11_q, d_ff_12_q, not_1_out, not_2_out, not_3_out,
       not_4_out, not_5_out, not_6_out, not_7_out, not_8_out, not_9_out, not_10_out, not_11_out, not_12_out,
       or_1_out, or_2_out;
  wire [7:0] adder_1_out, register_2_q, register_3_q, subtractor_1_out;
  wire [15:0] register_1_q;

  Register #(.width(16)) register_1 (.D(PCALT), .en(and_1_out), .clk(Execute), .Q(register_1_q), .clr(Fetch));
  assign PCinstOut = JMP ? PCALT : 16'bz;  // Controlled_Buffer controlled_buffer_1
  Adder adder_1 (.a(8'h1), .b(StackPointer), .out(adder_1_out));  // open: cin, cout
  Subtractor subtractor_1 (.a(StackPointer), .b(8'h1), .out(subtractor_1_out));  // open: bin, bout
  or or_1 (or_1_out, and_10_out, and_4_out);
  or or_2 (or_2_out, and_8_out, and_2_out);
  and and_1 (and_1_out, not_1_out, JSR);
  and and_2 (and_2_out, not_2_out, RTS);
  assign PCinstOut_2 = and_2_out ? subtractor_1_out : 8'bz;  // Controlled_Buffer controlled_buffer_2
  or or_3 (StackStack, and_1_out, or_1_out, and_7_out);
  not not_1 (not_1_out, d_ff_1_q);
  D_Flip_Flop #(.trigger("falling")) d_ff_1 (.D(JSR), .clk(Execute), .Q(d_ff_1_q), .reset(Fetch));  // open: Qn, preset
  not not_2 (not_2_out, d_ff_2_q);
  D_Flip_Flop #(.trigger("falling")) d_ff_2 (.D(RTS), .clk(Execute), .Q(d_ff_2_q), .reset(Fetch));  // open: Qn, preset
  assign PCinstOut_2 = and_1_out ? StackPointer : 8'bz;  // Controlled_Buffer controlled_buffer_3
  or or_4 (SWrite, and_3_out, or_2_out, and_9_out);
  and and_3 (and_3_out, not_3_out, d_ff_1_q);
  and and_4 (and_4_out, not_4_out, d_ff_2_q);
  assign PCinstOut_2 = and_4_out ? StackPointer : 8'bz;  // Controlled_Buffer controlled_buffer_4
  not not_3 (not_3_out, d_ff_3_q);
  D_Flip_Flop #(.trigger("falling")) d_ff_3 (
    .D(d_ff_1_q), .clk(Execute), .Q(d_ff_3_q), .reset(Fetch));  // open: Qn, preset
  not not_4 (not_4_out, d_ff_4_q);
  D_Flip_Flop #(.trigger("falling")) d_ff_4 (
    .D(d_ff_2_q), .clk(Execute), .Q(d_ff_4_q), .reset(Fetch));  // open: Qn, preset
  assign PCinstOut_2 = and_3_out ? adder_1_out : 8'bz;  // Controlled_Buffer controlled_buffer_5
  or or_5 (MWrite, and_5_out, and_11_out);
  and and_5 (and_5_out, not_5_out, d_ff_3_q);
  and and_6 (and_6_out, not_6_out, d_ff_4_q);
  D_Flip_Flop #(.trigger("falling")) d_ff_5 (
    .D(d_ff_4_q), .clk(Execute), .Q(d_ff_5_q), .reset(Fetch));  // open: Qn, preset
  Register #(.trigger("falling")) register_2 (.D(InstIn), .en(and_6_out), .clk(Execute), .Q(register_2_q), .clr(Fetch));
  or or_6 (StackOveride, MWrite, MRead);
  not not_5 (not_5_out, d_ff_6_q);
  D_Flip_Flop #(.trigger("falling")) d_ff_6 (
    .D(d_ff_3_q), .clk(Execute), .Q(d_ff_6_q), .reset(Fetch));  // open: Qn, preset
  not not_6 (not_6_out, d_ff_5_q);
  assign PCinstOut_2 = and_5_out ? PC[7:0] : 8'bz;  // Controlled_Buffer controlled_buffer_6
  and and_7 (and_7_out, not_8_out, d_ff_6_q);
  D_Flip_Flop #(.trigger("falling")) d_ff_7 (
    .D(d_ff_6_q), .clk(Execute), .Q(d_ff_7_q), .reset(Fetch));  // open: Qn, preset
  not not_7 (not_7_out, d_ff_8_q);
  and and_8 (and_8_out, not_7_out, d_ff_5_q);
  D_Flip_Flop #(.trigger("falling")) d_ff_8 (
    .D(d_ff_5_q), .clk(Execute), .Q(d_ff_8_q), .reset(Fetch));  // open: Qn, preset
  assign PCinstOut_2 = and_8_out ? subtractor_1_out : 8'bz;  // Controlled_Buffer controlled_buffer_7
  not not_8 (not_8_out, d_ff_7_q);
  assign PCinstOut_2 = and_7_out ? StackPointer : 8'bz;  // Controlled_Buffer controlled_buffer_8
  and and_9 (and_9_out, not_10_out, d_ff_7_q);
  D_Flip_Flop #(.trigger("falling")) d_ff_9 (
    .D(d_ff_7_q), .clk(Execute), .Q(d_ff_9_q), .reset(Fetch));  // open: Qn, preset
  not not_9 (not_9_out, d_ff_10_q);
  and and_10 (and_10_out, not_9_out, d_ff_8_q);
  D_Flip_Flop #(.trigger("falling")) d_ff_10 (
    .D(d_ff_8_q), .clk(Execute), .Q(d_ff_10_q), .reset(Fetch));  // open: Qn, preset
  assign PCinstOut_2 = and_10_out ? StackPointer : 8'bz;  // Controlled_Buffer controlled_buffer_9
  not not_10 (not_10_out, d_ff_9_q);
  assign PCinstOut_2 = and_9_out ? adder_1_out : 8'bz;  // Controlled_Buffer controlled_buffer_10
  not not_11 (not_11_out, d_ff_11_q);
  and and_11 (and_11_out, not_11_out, d_ff_9_q);
  D_Flip_Flop #(.trigger("falling")) d_ff_11 (
    .D(d_ff_9_q), .clk(Execute), .Q(d_ff_11_q), .reset(Fetch));  // open: Qn, preset
  not not_12 (not_12_out, d_ff_12_q);
  and and_12 (and_12_out, not_12_out, d_ff_10_q);
  D_Flip_Flop #(.trigger("falling")) d_ff_12 (
    .D(d_ff_10_q), .clk(Execute), .Q(d_ff_12_q), .reset(Fetch));  // open: Qn, preset
  Register #(.trigger("falling")) register_3 (
    .D(InstIn), .en(and_12_out), .clk(Execute), .Q(register_3_q), .clr(Fetch));
  assign PCinstOut_2 = and_11_out ? PC[15:8] : 8'bz;  // Controlled_Buffer controlled_buffer_11
  assign PCinstOut = d_ff_12_q ? {register_2_q, register_3_q} : 16'bz;  // Controlled_Buffer controlled_buffer_12
  or or_7 (InstDone, JMP, d_ff_12_q, d_ff_11_q);
  or or_8 (MRead, and_12_out, and_6_out);
  assign PCinstOut = d_ff_11_q ? register_1_q : 16'bz;  // Controlled_Buffer controlled_buffer_13

  assign PCWrite = InstDone;
endmodule
