// Logisim project logical_instructions.circ as structural Verilog: 1 circuit, main circuit main
module main (
  input  [7:0] Lowbyte,
  input  [7:0] A,
  input  AND,
  input  ORA,
  input  EOR,
  output AWrite,
  output InstructionDone,
  output [7:0] InstructionOut
);

  wire or_2_out;
  wire [7:0] and_1_out, or_1_out, xor_1_out;

  assign and_1_out = Lowbyte & A;  // AND_Gate and_1, 8 bits wide
  assign InstructionOut = AND ? and_1_out : 8'bz;  // Controlled_Buffer controlled_buffer_1
  assign or_1_out = Lowbyte | A;  // OR_Gate or_1, 8 bits wide
  assign InstructionOut = ORA ? or_1_out : 8'bz;  // Controlled_Buffer controlled_buffer_2
  assign xor_1_out = Lowbyte ^ A;  // XOR_Gate xor_1, 8 bits wide
  assign InstructionOut = EOR ? xor_1_out : 8'bz;  // Controlled_Buffer controlled_buffer_3
  or or_2 (or_2_out, AND, ORA);
  or or_3 (AWrite, or_2_out, EOR);

  assign InstructionDone = AWrite;
endmodule
