// Logisim project processor_status_register.circ as structural Verilog: 1 circuit, main circuit main
module main (
  input  [6:0] Pin,
  input  RegsiterInput,
  input  Execute,
  input  Clear,
  input  BreakOff,
  input  ClearOverflow,
  input  Overflow,
  input  Negative,
  input  OverflowRead,
  input  NegativeRead,
  input  Zero,
  input  InteruptOn,
  input  InteruptOff,
  input  DecimalOn,
  input  DecimalOff,
  input  CarryOff,
  input  BreakOn,
  input  Carry,
  input  CarryOn,
  input  ZeroRead,
  input  CarryRead,
  output Carry_2,
  output Zero_2,
  output Interupt,
  output Decimal,
  output Break,
  output Overflow_2,
  output Negative_2
);

  wire and_1_out, and_2_out, and_3_out, and_4_out, and_5_out, and_6_out, and_7_out, and_8_out, and_9_out,
       and_10_out, and_11_out, and_12_out, and_13_out, and_14_out, and_15_out, and_16_out, and_17_out,
       and_18_out, and_19_out, and_20_out, and_21_out, and_22_out, and_23_out, and_24_out, and_25_out,
       and_26_out, and_27_out, and_28_out, and_29_out, and_30_out, and_31_out, and_32_out, and_33_out,
       and_34_out, and_35_out, and_36_out, and_37_out, and_38_out, and_39_out, and_40_out, and_41_out,
       and_42_out, and_43_out, not_1_out, not_2_out, not_3_out, not_4_out, not_5_out, not_6_out, not_7_out,
       not_8_out, not_9_out, not_10_out, not_11_out, not_12_out, not_13_out, not_14_out, not_15_out,
       not_16_out, not_17_out, not_18_out, or_1_out, or_2_out, or_3_out, or_4_out, or_5_out, or_6_out,
       or_7_out, or_8_out, or_9_out, or_10_out, or_11_out, or_12_out, or_13_out, or_14_out, or_15_out,
       or_16_out, or_17_out, or_18_out, or_19_out, or_20_out;

  not not_1 (not_1_out, RegsiterInput);
  or or_1 (or_1_out, CarryOn, Carry);
  not not_2 (not_2_out, RegsiterInput);
  or or_2 (or_2_out, CarryOn, CarryRead);
  and and_1 (and_1_out, RegsiterInput, Pin[6]);
  or or_3 (or_3_out, and_1_out, and_2_out);
  and and_2 (and_2_out, not_1_out, or_1_out);
  and and_3 (and_3_out, RegsiterInput, Pin[6]);
  and and_4 (and_4_out, not_2_out, or_2_out);
  D_Flip_Flop #(.trigger("falling")) d_ff_1 (
    .D(or_3_out), .clk(and_5_out), .Q(Carry_2), .reset(or_4_out));  // open: Qn, preset
  and and_5 (and_5_out, or_5_out, Execute);
  or or_4 (or_4_out, and_6_out, Clear);
  and and_6 (and_6_out, Execute, and_7_out);
  or or_5 (or_5_out, and_3_out, and_4_out);
  and and_7 (and_7_out, not_3_out, CarryOff);
  not not_3 (not_3_out, RegsiterInput);
  not not_4 (not_4_out, RegsiterInput);
  not not_5 (not_5_out, RegsiterInput);
  and and_8 (and_8_out, RegsiterInput, Pin[5]);
  and and_9 (and_9_out, not_4_out, Zero);
  and and_10 (and_10_out, RegsiterInput, Pin[5]);
  and and_11 (and_11_out, not_5_out, ZeroRead);
  or or_6 (or_6_out, and_8_out, and_9_out);
  D_Flip_Flop #(.trigger("falling")) d_ff_2 (
    .D(or_6_out), .clk(and_12_out), .Q(Zero_2), .reset(Clear));  // open: Qn, preset
  and and_12 (and_12_out, or_7_out, Execute);
  or or_7 (or_7_out, and_10_out, and_11_out);
  not not_6 (not_6_out, RegsiterInput);
  not not_7 (not_7_out, RegsiterInput);
  and and_13 (and_13_out, RegsiterInput, Pin[4]);
  and and_14 (and_14_out, not_6_out, InteruptOn);
  and and_15 (and_15_out, RegsiterInput, Pin[4]);
  and and_16 (and_16_out, not_7_out, InteruptOn);
  or or_8 (or_8_out, and_13_out, and_14_out);
  D_Flip_Flop #(.trigger("falling")) d_ff_3 (
    .D(or_8_out), .clk(and_17_out), .Q(Interupt), .reset(or_9_out));  // open: Qn, preset
  and and_17 (and_17_out, or_10_out, Execute);
  or or_9 (or_9_out, and_18_out, Clear);
  and and_18 (and_18_out, Execute, and_19_out);
  or or_10 (or_10_out, and_15_out, and_16_out);
  and and_19 (and_19_out, not_8_out, InteruptOff);
  not not_8 (not_8_out, RegsiterInput);
  not not_9 (not_9_out, RegsiterInput);
  not not_10 (not_10_out, RegsiterInput);
  and and_20 (and_20_out, RegsiterInput, Pin[3]);
  and and_21 (and_21_out, not_9_out, DecimalOn);
  and and_22 (and_22_out, RegsiterInput, Pin[3]);
  and and_23 (and_23_out, not_10_out, DecimalOn);
  or or_11 (or_11_out, and_20_out, and_21_out);
  D_Flip_Flop #(.trigger("falling")) d_ff_4 (
    .D(or_11_out), .clk(and_24_out), .Q(Decimal), .reset(or_12_out));  // open: Qn, preset
  and and_24 (and_24_out, or_13_out, Execute);
  or or_12 (or_12_out, and_25_out, Clear);
  and and_25 (and_25_out, Execute, and_26_out);
  or or_13 (or_13_out, and_22_out, and_23_out);
  and and_26 (and_26_out, not_11_out, DecimalOff);
  not not_11 (not_11_out, RegsiterInput);
  not not_12 (not_12_out, RegsiterInput);
  not not_13 (not_13_out, RegsiterInput);
  and and_27 (and_27_out, RegsiterInput, Pin[2]);
  or or_14 (or_14_out, and_27_out, and_28_out);
  and and_28 (and_28_out, not_12_out, BreakOn);
  and and_29 (and_29_out, RegsiterInput, Pin[2]);
  or or_15 (or_15_out, and_29_out, and_30_out);
  and and_30 (and_30_out, not_13_out, BreakOn);
  D_Flip_Flop #(.trigger("falling")) d_ff_5 (
    .D(or_14_out), .clk(and_31_out), .Q(Break), .reset(BreakOff));  // open: Qn, preset
  and and_31 (and_31_out, or_15_out, Execute);
  not not_14 (not_14_out, RegsiterInput);
  not not_15 (not_15_out, RegsiterInput);
  and and_32 (and_32_out, RegsiterInput, Pin[1]);
  or or_16 (or_16_out, and_32_out, and_33_out);
  and and_33 (and_33_out, not_14_out, Overflow);
  and and_34 (and_34_out, or_17_out, Execute);
  and and_35 (and_35_out, RegsiterInput, Pin[1]);
  or or_17 (or_17_out, and_35_out, and_36_out);
  and and_36 (and_36_out, not_15_out, OverflowRead);
  D_Flip_Flop #(.trigger("falling")) d_ff_6 (
    .D(or_16_out), .clk(and_34_out), .Q(Overflow_2), .reset(or_18_out));  // open: Qn, preset
  or or_18 (or_18_out, and_37_out, Clear);
  and and_37 (and_37_out, Execute, and_38_out);
  and and_38 (and_38_out, not_16_out, ClearOverflow);
  not not_16 (not_16_out, RegsiterInput);
  not not_17 (not_17_out, RegsiterInput);
  not not_18 (not_18_out, RegsiterInput);
  and and_39 (and_39_out, RegsiterInput, Pin[0]);
  or or_19 (or_19_out, and_39_out, and_40_out);
  and and_40 (and_40_out, not_17_out, Negative);
  and and_41 (and_41_out, or_20_out, Execute);
  and and_42 (and_42_out, RegsiterInput, Pin[0]);
  or or_20 (or_20_out, and_42_out, and_43_out);
  and and_43 (and_43_out, not_18_out, NegativeRead);
  D_Flip_Flop #(.trigger("falling")) d_ff_7 (
    .D(or_19_out), .clk(and_41_out), .Q(Negative_2), .reset(Clear));  // open: Qn, preset
endmodule
