// Logisim project program_counter.circ as structural Verilog: 1 circuit, main circuit main
module main (
  input  [15:0] Input,
  input  ClockIn,
  input  OverwriteIn,
  input  Reset,
  input  ItterateIn,
  output [15:0] Output
);

  wire or_1_out;
  wire [15:0] adder_1_out, controlled_buffer_1_out;

  Adder #(.width(16)) adder_1 (.a(Output), .b(16'h1), .out(adder_1_out));  // open: cin, cout
  assign controlled_buffer_1_out = ItterateIn ? adder_1_out : 16'bz;  // Controlled_Buffer controlled_buffer_1
  assign controlled_buffer_1_out = OverwriteIn ? Input : 16'bz;  // Controlled_Buffer controlled_buffer_2
  Register #(.width(16), .trigger("falling")) register_1 (
    .D(controlled_buffer_1_out), .en(or_1_out), .clk(ClockIn), .Q(Output), .clr(Reset));
  or or_1 (or_1_out, OverwriteIn, ItterateIn);
endmodule
