// Logisim project retreiver.circ as structural Verilog: 1 circuit, main circuit main
module main (
  input  Reset,
  input  Clock,
  input  [7:0] LowByte,
  input  DecodeHigh,
  input  [7:0] X,
  input  [7:0] Y,
  input  [7:0] HighByte,
  input  [11:0] AddressInput,
  output ExecuteFlag,
  output DecodeFlag,
  output HighByteFlag,
  output PCOFFflag,
  output [15:0] NextAddress
);

  wire and_1_out, and_2_out, and_4_out, and_5_out, d_ff_1_q, d_ff_3_q, d_ff_4_q, Itter1, not_1_out,
       not_3_out, not_4_out, not_5_out, not_6_out, not_7_out, not_8_out, not_9_out, or_1_out, or_3_out,
       or_4_out, or_5_out, or_6_out, or_7_out, or_8_out, or_9_out, or_10_out, or_11_out, or_12_out,
       or_13_out, or_14_out, or_15_out, or_16_out, or_17_out, or_18_out, or_19_out, or_20_out, or_21_out,
       or_22_out;
  wire [7:0] adder_1_out, adder_2_out, adder_3_out, adder_4_out, adder_5_out, adder_6_out,
       controlled_buffer_14_out, controlled_buffer_16_out, controlled_buffer_21_out, controlled_buffer_23_out;

  not not_1 (not_1_out, or_1_out);
  or or_1 (or_1_out, AddressInput[11], AddressInput[10], AddressInput[9], AddressInput[8], AddressInput[7], AddressInput[6], AddressInput[5], AddressInput[4], AddressInput[2], AddressInput[1], AddressInput[0]);
  not not_2 (DecodeFlag, ExecuteFlag);
  or or_2 (ExecuteFlag, not_1_out, d_ff_1_q);
  or or_3 (or_3_out, AddressInput[11], AddressInput[10]);
  or or_4 (or_4_out, or_3_out, Itter1);
  assign NextAddress[7:0] = AddressInput[7] ? LowByte : 8'bz;  // Controlled_Buffer controlled_buffer_1
  Adder adder_1 (.a(LowByte), .b(X), .out(adder_1_out));  // open: cin, cout
  assign NextAddress[15:8] = AddressInput[7] ? {8{1'b0}} : 8'bz;  // Controlled_Buffer controlled_buffer_2
  D_Flip_Flop #(.trigger("falling")) d_ff_1 (
    .D(or_4_out), .clk(Clock), .Q(d_ff_1_q), .reset(Reset));  // open: Qn, preset
  assign NextAddress[7:0] = AddressInput[6] ? adder_1_out : 8'bz;  // Controlled_Buffer controlled_buffer_3
  assign NextAddress[15:8] = AddressInput[6] ? {8{1'b0}} : 8'bz;  // Controlled_Buffer controlled_buffer_4
  or or_5 (or_5_out, AddressInput[7], AddressInput[6]);
  assign NextAddress[7:0] = AddressInput[5] ? adder_2_out : 8'bz;  // Controlled_Buffer controlled_buffer_5
  Adder adder_2 (.a(LowByte), .b(Y), .out(adder_2_out));  // open: cin, cout
  assign NextAddress[15:8] = AddressInput[5] ? {8{1'b0}} : 8'bz;  // Controlled_Buffer controlled_buffer_6
  or or_6 (or_6_out, or_5_out, AddressInput[5]);
  assign NextAddress[7:0] = AddressInput[1] ? LowByte : 8'bz;  // Controlled_Buffer controlled_buffer_7
  assign NextAddress[15:8] = AddressInput[1] ? HighByte : 8'bz;  // Controlled_Buffer controlled_buffer_8
  assign NextAddress[7:0] = AddressInput[0] ? adder_3_out : 8'bz;  // Controlled_Buffer controlled_buffer_9
  Adder adder_3 (.a(LowByte), .b(X), .out(adder_3_out));  // open: cin, cout
  assign NextAddress[15:8] = AddressInput[0] ? HighByte : 8'bz;  // Controlled_Buffer controlled_buffer_10
  or or_7 (or_7_out, or_6_out, AddressInput[1]);
  assign NextAddress[7:0] = AddressInput[4] ? adder_4_out : 8'bz;  // Controlled_Buffer controlled_buffer_11
  Adder adder_4 (.a(LowByte), .b(Y), .out(adder_4_out));  // open: cin, cout
  assign NextAddress[15:8] = AddressInput[4] ? HighByte : 8'bz;  // Controlled_Buffer controlled_buffer_12
  or or_8 (or_8_out, AddressInput[1], AddressInput[0]);
  or or_9 (or_9_out, AddressInput[1], AddressInput[0]);
  or or_10 (or_10_out, or_7_out, AddressInput[0]);
  or or_11 (or_11_out, or_8_out, AddressInput[4]);
  or or_12 (or_12_out, or_9_out, AddressInput[4]);
  or or_13 (or_13_out, or_10_out, AddressInput[4]);
  D_Flip_Flop #(.trigger("falling")) d_ff_2 (
    .D(or_14_out), .clk(Clock), .Q(Itter1), .reset(Reset));  // open: Qn, preset
  or or_14 (or_14_out, or_13_out, d_ff_3_q);
  assign NextAddress[7:0] = AddressInput[2] ? LowByte : 8'bz;  // Controlled_Buffer controlled_buffer_13
  not not_3 (not_3_out, Itter1);
  not not_4 (not_4_out, not_3_out);
  not not_5 (not_5_out, Itter1);
  assign controlled_buffer_14_out = not_5_out ? {8{1'b0}} : 8'bz;  // Controlled_Buffer controlled_buffer_14
  assign NextAddress[15:8] = AddressInput[2] ? HighByte : 8'bz;  // Controlled_Buffer controlled_buffer_15
  or or_15 (or_15_out, or_11_out, AddressInput[2]);
  or or_16 (or_16_out, or_12_out, AddressInput[2]);
  assign controlled_buffer_16_out = not_3_out ? X : 8'bz;  // Controlled_Buffer controlled_buffer_16
  assign controlled_buffer_16_out = not_4_out ? {8{1'b0}} : 8'bz;  // Controlled_Buffer controlled_buffer_17
  and and_1 (and_1_out, AddressInput[9], Itter1);
  assign controlled_buffer_14_out = Itter1 ? HighByte : 8'bz;  // Controlled_Buffer controlled_buffer_18
  Adder adder_5 (.a(LowByte), .b(controlled_buffer_16_out), .out(adder_5_out));  // open: cin, cout
  or or_17 (or_17_out, and_1_out, or_16_out);
  assign NextAddress[7:0] = AddressInput[9] ? adder_5_out : 8'bz;  // Controlled_Buffer controlled_buffer_19
  assign NextAddress[15:8] = AddressInput[9] ? controlled_buffer_14_out : 8'bz;  // Controlled_Buffer controlled_buffer_20
  or or_18 (or_18_out, AddressInput[2], AddressInput[9]);
  assign controlled_buffer_21_out = Itter1 ? Y : 8'bz;  // Controlled_Buffer controlled_buffer_21
  not not_6 (not_6_out, Itter1);
  assign controlled_buffer_21_out = not_6_out ? {8{1'b0}} : 8'bz;  // Controlled_Buffer controlled_buffer_22
  assign controlled_buffer_23_out = Itter1 ? HighByte : 8'bz;  // Controlled_Buffer controlled_buffer_23
  not not_7 (not_7_out, Itter1);
  assign controlled_buffer_23_out = not_7_out ? {8{1'b0}} : 8'bz;  // Controlled_Buffer controlled_buffer_24
  Adder adder_6 (.a(LowByte), .b(controlled_buffer_21_out), .out(adder_6_out));  // open: cin, cout
  and and_2 (and_2_out, AddressInput[8], Itter1);
  or or_19 (or_19_out, and_2_out, or_17_out);
  and and_3 (HighByteFlag, DecodeFlag, or_19_out);
  assign NextAddress[7:0] = AddressInput[8] ? adder_6_out : 8'bz;  // Controlled_Buffer controlled_buffer_25
  assign NextAddress[15:8] = AddressInput[8] ? controlled_buffer_23_out : 8'bz;  // Controlled_Buffer controlled_buffer_26
  or or_20 (or_20_out, or_18_out, AddressInput[8]);
  D_Flip_Flop #(.trigger("falling")) d_ff_3 (
    .D(or_20_out), .clk(Clock), .Q(d_ff_3_q), .reset(Reset));  // open: Qn, preset
  or or_21 (or_21_out, Itter1, d_ff_3_q);
  not not_8 (not_8_out, ExecuteFlag);
  and and_4 (and_4_out, or_21_out, not_9_out);
  and and_5 (and_5_out, d_ff_4_q, or_15_out);
  not not_9 (not_9_out, or_15_out);
  D_Flip_Flop #(.trigger("falling")) d_ff_4 (
    .D(or_15_out), .clk(DecodeHigh), .Q(d_ff_4_q), .reset(Reset));  // open: Qn, preset
  and and_6 (PCOFFflag, not_8_out, or_22_out);
  or or_22 (or_22_out, and_4_out, and_5_out);

  // Notes on the sheet:
  //   impl
  //   rel
  //   Hash
  //   A
  //   zpg
  //   zpgX
  //   zpgY
  //   abs
  //   absX
  //   absY
  //   ind
  //   indX
  //   indY
endmodule
