// Logisim project rotation_instructions.circ as structural Verilog: 1 circuit, main circuit main
module main (
  input  AccumulatorTrigger,
  input  [7:0] A,
  input  [7:0] LowByte,
  input  Carry,
  input  ASL,
  input  ROL,
  input  LSR,
  input  ROR,
  output AWrite,
  output MWrite,
  output PCOFF,
  output InstDone,
  output [7:0] InstructionOut,
  output CarryFlag
);

  wire and_1_out, and_2_out, and_3_out, and_4_out, and_5_out, and_7_out, not_1_out, not_2_out, or_2_out,
       or_3_out, or_5_out, or_7_out;
  wire [0:0] or_1_out;
  wire [7:0] controlled_buffer_1_out;
  wire [7:7] or_4_out;

  assign controlled_buffer_1_out = AccumulatorTrigger ? A : 8'bz;  // Controlled_Buffer controlled_buffer_1
  not not_1 (not_1_out, AccumulatorTrigger);
  assign controlled_buffer_1_out = not_1_out ? LowByte : 8'bz;  // Controlled_Buffer controlled_buffer_2
  and and_1 (and_1_out, Carry, ROL);
  and and_2 (and_2_out, 1'b0, ASL);
  or or_1 (or_1_out[0], and_2_out, and_1_out);
  or or_2 (or_2_out, ROL, ASL);
  assign InstructionOut = or_3_out ? {controlled_buffer_1_out[6:0], or_1_out[0]} : 8'bz;  // Controlled_Buffer controlled_buffer_3
  and and_3 (and_3_out, controlled_buffer_1_out[7], or_3_out);
  or or_3 (or_3_out, ROL, ASL);
  and and_4 (and_4_out, Carry, ROR);
  and and_5 (and_5_out, 1'b0, LSR);
  or or_4 (or_4_out[7], and_5_out, and_4_out);
  or or_5 (or_5_out, or_2_out, LSR);
  or or_6 (InstDone, or_5_out, ROR);
  or or_7 (or_7_out, ROR, LSR);
  and and_6 (AWrite, AccumulatorTrigger, InstDone);
  assign InstructionOut = or_7_out ? {or_4_out[7], controlled_buffer_1_out[7:1]} : 8'bz;  // Controlled_Buffer controlled_buffer_4
  and and_7 (and_7_out, controlled_buffer_1_out[0], or_7_out);
  or or_8 (CarryFlag, and_3_out, and_7_out);
  and and_8 (MWrite, not_2_out, InstDone);
  not not_2 (not_2_out, AccumulatorTrigger);

  assign PCOFF = MWrite;
endmodule
