// Logisim project stack_instructions.circ as structural Verilog: 1 circuit, main circuit main
module main (
  input  Execute,
  input  Fetch,
  input  [7:0] StackPointer,
  input  [7:0] StatusRegister,
  input  [7:0] Accumulator,
  input  PHA,
  input  PHP,
  input  PLA,
  input  PLP,
  output StackStack,
  output Swrite,
  output StackOveride,
  output MWrite,
  output MRead,
  output AWrite,
  output StatusWrite,
  output InstDone,
  output [7:0] InstructionOut,
  output FlagFlag
);

  wire and_1_out, and_2_out, and_3_out, and_4_out, and_5_out, and_6_out, and_7_out, and_8_out, and_9_out,
       and_10_out, and_11_out, and_12_out, and_13_out, and_14_out, and_16_out, and_17_out, d_ff_1_q,
       not_1_out, not_2_out, not_3_out, not_4_out, or_3_out, or_4_out, or_5_out, or_6_out, or_7_out;
  wire [7:0] adder_1_out, subtractor_1_out;

  and and_1 (and_1_out, and_2_out, not_1_out);
  and and_2 (and_2_out, or_3_out, or_4_out);
  D_Flip_Flop #(.trigger("falling")) d_ff_1 (
    .D(or_4_out), .clk(Execute), .Q(d_ff_1_q), .reset(Fetch));  // open: Qn, preset
  or or_1 (StackStack, and_1_out, and_11_out);
  and and_3 (and_3_out, and_4_out, not_1_out);
  and and_4 (and_4_out, or_6_out, or_4_out);
  not not_1 (not_1_out, d_ff_1_q);
  not not_2 (not_2_out, d_ff_1_q);
  Subtractor subtractor_1 (.a(StackPointer), .b(8'h1), .out(subtractor_1_out));  // open: bin, bout
  and and_5 (and_5_out, or_3_out, and_7_out);
  assign InstructionOut = and_5_out ? StackPointer : 8'bz;  // Controlled_Buffer controlled_buffer_1
  and and_6 (and_6_out, or_3_out, d_ff_1_q);
  and and_7 (and_7_out, not_2_out, not_4_out);
  and and_8 (and_8_out, and_7_out, or_6_out);
  assign InstructionOut = and_8_out ? subtractor_1_out : 8'bz;  // Controlled_Buffer controlled_buffer_2
  or or_2 (Swrite, and_9_out, and_3_out);
  and and_9 (and_9_out, and_6_out, not_3_out);
  and and_10 (and_10_out, or_6_out, d_ff_1_q);
  and and_11 (and_11_out, and_10_out, not_3_out);
  Adder adder_1 (.a(StackPointer), .b(8'h1), .out(adder_1_out));  // open: cin, cout
  not not_3 (not_3_out, InstDone);
  D_Flip_Flop #(.trigger("falling")) d_ff_2 (
    .D(d_ff_1_q), .clk(Execute), .Q(InstDone), .reset(Fetch));  // open: Qn, preset
  not not_4 (not_4_out, InstDone);
  and and_12 (and_12_out, d_ff_1_q, not_4_out);
  and and_13 (and_13_out, or_3_out, and_12_out);
  assign InstructionOut = and_13_out ? adder_1_out : 8'bz;  // Controlled_Buffer controlled_buffer_3
  and and_14 (and_14_out, and_12_out, or_6_out);
  assign InstructionOut = and_14_out ? StackPointer : 8'bz;  // Controlled_Buffer controlled_buffer_4
  and and_15 (MWrite, InstDone, or_3_out);
  or or_3 (or_3_out, PHP, PHA);
  or or_4 (or_4_out, or_5_out, PHA);
  assign InstructionOut = and_16_out ? Accumulator : 8'bz;  // Controlled_Buffer controlled_buffer_5
  and and_16 (and_16_out, PHA, InstDone);
  or or_5 (or_5_out, or_7_out, PHP);
  assign InstructionOut = and_17_out ? StatusRegister : 8'bz;  // Controlled_Buffer controlled_buffer_6
  and and_17 (and_17_out, PHP, InstDone);
  and and_18 (MRead, or_6_out, InstDone);
  or or_6 (or_6_out, PLP, PLA);
  or or_7 (or_7_out, PLP, PLA);
  and and_19 (StatusWrite, PLP, InstDone);
  and and_20 (AWrite, PLA, InstDone);

  assign FlagFlag = PLA;
  assign StackOveride = InstDone;
endmodule
