// Logisim project transfer_instructions.circ as structural Verilog: 1 circuit, main circuit main
module main (
  input  [7:0] x,
  input  [7:0] y,
  input  [7:0] a,
  input  [7:0] s,
  input  [7:0] M,
  input  STA,
  input  LDA,
  input  STY,
  input  LDY,
  input  TAX,
  input  TAY,
  input  TXS,
  input  STX,
  input  LDX,
  input  TXA,
  input  TYA,
  input  TSX,
  output [7:0] out_18,
  output MWrite,
  output PCOFF,
  output XWrite,
  output YWrite,
  output AWrite,
  output SWrite,
  output TransferInstructionDone,
  output FlagFlag
);

  wire or_1_out, or_2_out, or_3_out, or_4_out, or_5_out, or_6_out, or_7_out;

  assign out_18 = STA ? a : 8'bz;  // Controlled_Buffer controlled_buffer_1
  assign out_18 = STY ? y : 8'bz;  // Controlled_Buffer controlled_buffer_2
  assign out_18 = STX ? x : 8'bz;  // Controlled_Buffer controlled_buffer_3
  or or_1 (or_1_out, STA, STY, STX);
  assign out_18 = LDA ? M : 8'bz;  // Controlled_Buffer controlled_buffer_4
  assign out_18 = LDY ? M : 8'bz;  // Controlled_Buffer controlled_buffer_5
  assign out_18 = LDX ? M : 8'bz;  // Controlled_Buffer controlled_buffer_6
  assign out_18 = TAX ? a : 8'bz;  // Controlled_Buffer controlled_buffer_7
  or or_2 (or_2_out, LDA, LDY, or_1_out, LDX);
  or or_3 (or_3_out, LDA, LDY, LDX);
  assign out_18 = TAY ? a : 8'bz;  // Controlled_Buffer controlled_buffer_8
  assign out_18 = TXA ? x : 8'bz;  // Controlled_Buffer controlled_buffer_9
  or or_4 (or_4_out, TAX, or_2_out, TXA);
  or or_5 (or_5_out, TAX, or_3_out, TXA);
  assign out_18 = TYA ? y : 8'bz;  // Controlled_Buffer controlled_buffer_10
  or or_6 (or_6_out, TAY, or_4_out, TYA);
  or or_7 (or_7_out, TAY, or_5_out, TYA);
  assign out_18 = TXS ? x : 8'bz;  // Controlled_Buffer controlled_buffer_11
  assign out_18 = TSX ? s : 8'bz;  // Controlled_Buffer controlled_buffer_12
  or or_8 (XWrite, LDX, TAX, TSX);
  or or_9 (FlagFlag, TXS, or_7_out, TSX);
  or or_10 (TransferInstructionDone, TXS, or_6_out, TSX);
  or or_11 (YWrite, LDY, TAY);
  or or_12 (AWrite, LDA, TXA, TYA);
  or or_13 (MWrite, STA, STY, STX);

  assign PCOFF = MWrite;
  assign SWrite = TXS;
endmodule
